// Logisim project cpu21-riscv-单周期(CCAB)-动态分支预测.circ as structural Verilog: 26 circuits, main circuit ◇单周期RISC-V
// 单周期硬布线控制器
module \单周期硬布线控制器  (
  input  [4:0] OP,
  input  [4:0] Funct,
  output [3:0] ALU_OP,
  output MemToReg,
  output MemWrite,
  output ALU_SRC,
  output RegWrite,
  output ecall,
  output S_type,
  output Beq,
  output Bne,
  output Jalr,
  output JAL,
  output U_type,
  output BGEU,
  output LHU,
  output URET,
  output CSRRSI,
  output CSRRCI
);

  \运算控制器自动生成  \u_运算控制器自动生成_1  (
    .OP2(OP[0]), .OP3(OP[1]), .OP4(OP[2]), .OP5(OP[3]), .OP6(OP[4]), .F12(Funct[0]), .F13(Funct[1]),
    .F14(Funct[2]), .F25(Funct[3]), .F30(Funct[4]), .S0(ALU_OP[0]), .S1(ALU_OP[1]), .S2(ALU_OP[2]),
    .S3(ALU_OP[3]));
  \控制信号自动生成  \u_控制信号自动生成_1  (
    .OP2(OP[0]), .OP3(OP[1]), .OP4(OP[2]), .OP5(OP[3]), .OP6(OP[4]), .MemToReg(MemToReg), .F12(Funct[0]),
    .F13(Funct[1]), .F14(Funct[2]), .F25(Funct[3]), .F30(Funct[4]), .MemWrite(MemWrite), .ALU_SRC(ALU_SRC),
    .RegWrite(RegWrite), .ecall(ecall), .S_Type(S_type), .BEQ(Beq), .BNE(Bne), .JALR(Jalr), .JAL(JAL),
    .U_Type(U_type), .BGEU(BGEU), .LHU(LHU), .URET(URET), .CSRRSI(CSRRSI), .CSRRCI(CSRRCI));

  // Other names for the same wires on the sheet: OP_CODE[4:0] = OP

  // Notes on the sheet:
  //   运算器控制器，根据指令生成运算器功能选择信号
  //   控制信号生成，产生数据通路需要的其他控制信号
endmodule

module \单周期RISC_V  (
  input  IR1,
  input  IR2,
  input  IR3,
  output RegWrite,
  output MemWrite,
  output [31:0] PC,
  output [31:0] IR,
  output [31:0] RDin,
  output [31:0] MDin,
  output [31:0] LedData
);

  wire AluSrcB, and_1_out, and_2_out, and_3_out, and_4_out, and_5_out, beq, bgeu, bne, Branch, CLK,
       clock_2_out, comparator_1_eq, comparator_2_eq, comparator_2_lt, controlled_buffer_1_out, d_ff_1_q,
       ecall, equal, Go, halt, IR1_t, IR2_t, IR3_t, IRA, IRB, IRC, jal, jalr, lhu, MemToReg, MoreAndEqu,
       nand_1_out, not_1_out, not_2_out, not_3_out, not_4_out, not_5_out, or_3_out, PCToReg, RST, S_type,
       U_type, W1, W2, W3;
  wire [3:0] AluOP;
  wire [4:0] multiplexer_5_out, multiplexer_6_out;
  wire [11:0] imm12_B;
  wire [12:0] CNT_num;
  wire [15:0] multiplexer_11_out, \分支成功数 , \总周期数 ;
  wire [19:0] imm20_J;
  wire [31:0] adder_1_out, adder_2_out, adder_3_out, and_6_out, bit_extender_1_out, bit_extender_2_out,
       bit_extender_3_out, bit_extender_4_out, bit_extender_5_out, MDout, multiplexer_1_out,
       multiplexer_2_out, multiplexer_3_out, multiplexer_7_out, multiplexer_9_out, multiplexer_10_out, PC_4,
       R1, ram_1_data, Result, RPCin;

  Clock #(.highDuration(1), .lowDuration(1)) clock_1 (.out(CLK));
  Button _1 (.out(IRA));
  Button _2 (.out(IRB));
  Button _3 (.out(IRC));
  Button \u_继续运行  (.out(Go));
  LED #(.active("true")) led_1 (.in(W1));
  LED #(.active("true")) led_2 (.in(W2));
  LED #(.active("true")) led_3 (.in(W3));
  // Probe on \分支成功数 
  Hex_Digit_Display hex_digit_display_1 (.value(LedData[31:28]));  // open: dp
  assign bit_extender_1_out = {{12{imm20_J[19]}}, imm20_J};  // Bit_Extender bit_extender_1
  Hex_Digit_Display hex_digit_display_2 (.value(LedData[23:20]));  // open: dp
  Hex_Digit_Display hex_digit_display_3 (.value(LedData[27:24]));  // open: dp
  not not_1 (not_1_out, equal);
  Comparator #(.width(32), .mode("twosComplement")) comparator_1 (
    .a(R1), .b(32'ha), .eq(comparator_1_eq));  // open: gt, lt
  Adder #(.width(32)) adder_1 (.a(bit_extender_1_out), .b(PC), .out(adder_1_out));  // open: cin, cout
  assign bit_extender_2_out = {{20{imm12_B[11]}}, imm12_B};  // Bit_Extender bit_extender_2
  Hex_Digit_Display hex_digit_display_4 (.value(LedData[19:16]));  // open: dp
  Hex_Digit_Display hex_digit_display_5 (.value(LedData[15:12]));  // open: dp
  and and_1 (and_1_out, beq, equal);
  or or_1 (Branch, and_1_out, and_2_out, and_3_out);
  and and_2 (and_2_out, not_1_out, bne);
  and and_3 (and_3_out, MoreAndEqu, bgeu);
  and and_4 (and_4_out, ecall, not_2_out);
  not not_2 (not_2_out, comparator_1_eq);
  and and_5 (and_5_out, comparator_1_eq, ecall);
  not not_3 (not_3_out, Go);
  Multiplexer #(.select(1), .width(32), .disabled("Z"), .enable("false")) multiplexer_1 (
    .in0(PC_4), .in1(adder_1_out), .out(multiplexer_1_out), .sel(jal));
  Multiplexer #(.select(1), .width(32), .disabled("Z"), .enable("false")) multiplexer_2 (
    .in0(multiplexer_1_out), .in1(and_6_out), .out(multiplexer_2_out), .sel(jalr));
  assign and_6_out = Result & 32'hfffffffe;  // AND_Gate and_6, 32 bits wide
  Adder #(.width(32)) adder_2 (.a(bit_extender_2_out), .b(PC), .out(adder_2_out));  // open: cin, cout
  Hex_Digit_Display hex_digit_display_6 (.value(LedData[11:8]));  // open: dp
  Hex_Digit_Display hex_digit_display_7 (.value(LedData[7:4]));  // open: dp
  // Probe on \总周期数 
  Counter #(.width(16), .max('hffff), .ongoal("wrap"), .trigger("rising"), .behavior("new")) counter_1 (
    .count(Branch), .Q(\分支成功数 ), .clk(CLK), .clr(RST));  // open: load, D, carry, preset, down
  Register #(.width(32), .trigger("rising"), .Select("low")) register_1 (
    .D(MDin), .en(and_4_out), .Q(LedData), .clk(CLK), .clr(RST));
  and and_7 (halt, and_5_out, not_3_out);
  Multiplexer #(.select(1), .width(32), .disabled("Z"), .enable("false")) multiplexer_3 (
    .in0(multiplexer_2_out), .in1(adder_2_out), .out(multiplexer_3_out), .sel(Branch));
  not not_4 (not_4_out, halt);
  Hex_Digit_Display hex_digit_display_8 (.value(LedData[3:0]));  // open: dp
  Register #(.width(32), .trigger("rising"), .Select("low")) u_PC (
    .D(multiplexer_3_out), .en(not_4_out), .Q(PC), .clk(CLK), .clr(RST));
  not not_5 (not_5_out, halt);
  or or_2 (IR1_t, IR1, IRA);
  Counter #(.width(16), .max('hffff), .ongoal("wrap"), .trigger("rising"), .behavior("new")) counter_2 (
    .count(not_5_out), .Q(\总周期数 ), .clk(CLK), .clr(RST));  // open: load, D, carry, preset, down
  or or_3 (or_3_out, jal, jalr);
  or or_4 (PCToReg, or_3_out, U_type);
  Multiplexer #(.select(1), .width(32), .disabled("Z"), .enable("false")) multiplexer_4 (
    .in0(PC_4), .in1(adder_3_out), .out(RPCin), .sel(U_type));
  Adder #(.width(32)) adder_3 (.a({IR[31:12], {12{1'b0}}}), .b(PC), .out(adder_3_out));  // open: cin, cout
  // RiscV_Probe riscv_probe_1: pin names not known; wires that end beside it: IR
  Adder #(.width(32)) adder_4 (.a(PC), .b(32'h4), .out(PC_4));  // open: cin, cout
  or or_5 (IR2_t, IR2, IRB);
  ROM #(.addrWidth(10), .dataWidth(32), .Select("high")) rom_1 (.addr(PC[11:2]), .data(IR));
  or or_6 (IR3_t, IR3, IRC);
  \单周期硬布线控制器  \u_单周期硬布线控制器_1  (
    .Funct({IR[30], IR[25], IR[14:12]}), .OP(IR[6:2]), .ALU_OP(AluOP), .MemToReg(MemToReg),
    .MemWrite(MemWrite), .ALU_SRC(AluSrcB), .RegWrite(RegWrite), .ecall(ecall), .S_type(S_type), .Jalr(jalr),
    .Beq(beq), .JAL(jal), .Bne(bne), .U_type(U_type), .BGEU(bgeu), .LHU(lhu));  // open: URET, CSRRSI, CSRRCI
  Multiplexer #(.select(1), .width(5), .disabled("Z"), .enable("false")) multiplexer_5 (
    .in0(IR[19:15]), .in1(5'b10001), .out(multiplexer_5_out), .sel(ecall));
  Multiplexer #(.select(1), .width(5), .disabled("Z"), .enable("false")) multiplexer_6 (
    .in0(IR[24:20]), .in1(5'b01010), .out(multiplexer_6_out), .sel(ecall));
  Multiplexer #(.select(1), .width(32), .disabled("Z"), .enable("false")) multiplexer_7 (
    .in0(Result), .in1(MDout), .out(multiplexer_7_out), .sel(MemToReg));
  Shifter #(.width(12), .shift("ll")) shifter_1 (
    .in({IR[31], IR[7], IR[30:25], IR[11:8]}), .\dist (4'b0001), .out(imm12_B));
  Shifter #(.width(20), .shift("ll")) shifter_2 (
    .in({IR[31], IR[19:12], IR[20], IR[30:21]}), .\dist (5'b00001), .out(imm20_J));
  Multiplexer #(.select(1), .width(32), .disabled("Z"), .enable("false")) multiplexer_8 (
    .in0(multiplexer_7_out), .in1(RPCin), .out(RDin), .sel(PCToReg));
  Regifile regifile_1 (
    .Din(RDin), .Clk(CLK), .R1(R1), .R2(MDin), .WE(RegWrite), .W_num(IR[11:7]), .R1_num(multiplexer_5_out),
    .R2_num(multiplexer_6_out));
  assign bit_extender_3_out = {{20{IR[31]}}, IR[31:20]};  // Bit_Extender bit_extender_3
  assign bit_extender_4_out = {{20{IR[31]}}, {IR[31:25], IR[11:7]}};  // Bit_Extender bit_extender_4
  Multiplexer #(.select(1), .width(32), .disabled("Z"), .enable("false")) multiplexer_9 (
    .in0(bit_extender_3_out), .in1(bit_extender_4_out), .out(multiplexer_9_out), .sel(S_type));
  Multiplexer #(.select(1), .width(32), .disabled("Z"), .enable("false")) multiplexer_10 (
    .in0(MDin), .in1(multiplexer_9_out), .out(multiplexer_10_out), .sel(AluSrcB));
  ALU alu_1 (
    .X(R1), .Y(multiplexer_10_out), .AluOP(AluOP), .Equal(equal), .Result(Result), .out_4(MoreAndEqu));  // open: Result_2, out_6
  D_Flip_Flop #(.trigger("high"), .Pre_Clr_Positions("LEGACY"), .NegatePresetClear("false"), .enable("true"), .NewFFLayout("false")) d_ff_1 (.Q(d_ff_1_q));  // open: clk, D, Qn, preset, en, reset
  // Probe on 13'hc
  Comparator #(.width(13), .mode("twosComplement")) comparator_2 (
    .a(CNT_num), .b(13'hc), .eq(comparator_2_eq), .lt(comparator_2_lt));  // open: gt
  Clock #(.highDuration(1), .lowDuration(1)) clock_2 (.out(clock_2_out));
  Counter #(.width(13), .max('h1fff), .ongoal("stay"), .trigger("rising"), .behavior("old")) counter_3 (
    .count(comparator_2_lt), .Q(CNT_num), .clk(clock_2_out));  // open: load, D, carry, clr, preset
  nand nand_1 (nand_1_out, d_ff_1_q, comparator_2_eq);
  assign controlled_buffer_1_out = nand_1_out ? clock_2_out : 1'bz;  // Controlled_Buffer controlled_buffer_1
  Pull_Resistor #(.pull(1)) pull_resistor_1 (.node(controlled_buffer_1_out));
  RAM #(.addrWidth(10), .dataWidth(32), .bus("separate"), .Select("high")) ram_1 (
    .addr(Result[11:2]), .din(MDin), .data(ram_1_data), .str(MemWrite), .clk(CLK), .ld(MemToReg), .clr(RST));  // open: sel
  assign bit_extender_5_out = {{16{1'b0}}, multiplexer_11_out};  // Bit_Extender bit_extender_5
  Multiplexer #(.select(1), .width(16), .disabled("Z"), .enable("false")) multiplexer_11 (
    .in0(ram_1_data[15:0]), .in1(ram_1_data[31:16]), .out(multiplexer_11_out), .sel(Result[1]));
  Multiplexer #(.select(1), .width(32), .disabled("Z"), .enable("false")) multiplexer_12 (
    .in0(ram_1_data), .in1(bit_extender_5_out), .out(MDout), .sel(lhu));

  // Other names for the same wires on the sheet: imm12_S[11:0] = {IR[31:25], IR[11:7]}; imm32_U[31:12] = IR[31:12];
  //   imm12_I[11:0] = IR[31:20]; R2[31:0] = MDin; X = Result[1]

  // Notes on the sheet:
  //   中断源
  //   中断等待指示
  //   总复位信号应将除ROM以外所有存储组件全部清零
  //   数码管输出
  //   数码管输出应该用寄存器锁存，否则显示数据只能一闪而过
  //   指令存储器
  //   指令字
  //   contents of rom_1 (hex, n*v repeats v):
  //   100493 100006f 100493 200913 300993 100006f 100493 200913 300993 100006f 100493 200913 300993
  //   100006f 100493 200913 300993 424000ef 100413 100493 1f49493 900533 2200893 73 24d493 48463 fedff06f
  //   900533 2200893 73 100493 249493 900533 2200893 73 48463 fedff06f 100493 1f49493 900533 2200893 73
  //   4034d493 900533 2200893 73 4044d493 900533 2200893 73 4044d493 900533 2200893 73 4044d493 900533
  //   2200893 73 4044d493 900533 2200893 73 4044d493 900533 2200893 73 4044d493 900533 2200893 73 4044d493
  //   900533 2200893 73 100413 1f41993 41f9d993 433 c00913 300b13 140413 f47413 800293 100313 499993
  //   89e9b3 1300533 2200893 73 406282b3 fe0294e3 140413 f00f93 1f47433 1c41413 800293 100313 49d993
  //   89e9b3 1300533 2200893 73 406282b3 fe0294e3 1c45413 406b0b33 b0463 f95ff06f 2b3 fff2c293 829293
  //   ff2e293 500533 2200893 73 fff00413 493 84a023 140413 448493 84a023 140413 448493 84a023 140413
  //   448493 84a023 140413 448493 84a023 140413 448493 84a023 140413 448493 84a023 140413 448493 84a023
  //   140413 448493 84a023 140413 448493 84a023 140413 448493 84a023 140413 448493 84a023 140413 448493
  //   84a023 140413 448493 84a023 140413 448493 84a023 140413 448493 84a023 140413 448493 140413 433
  //   3c00493 42983 4aa03 149a2b3 28663 134a023 1442023 ffc48493 fe9412e3 800533 2200893 73 440413 3c00493
  //   fc9416e3 a00893 73 100293 300313 800493 849493 7648493 1449493 900533 2200893 73 800e13 54d4b3
  //   64d4b3 900533 2200893 73 fffe0e13 fe0e14e3 a00893 73 13 430497 900533 2200893 73 430497 900533
  //   2200893 73 430497 900533 2200893 73 430497 900533 2200893 73 430497 900533 2200893 73 430497 900533
  //   2200893 73 430497 900533 2200893 73 430497 900533 2200893 73 a00893 73 313 1000e13 8400493 849493
  //   8348493 400913 891913 490913 849493 8248493 849493 8148493 891913 490913 891913 490913 932023
  //   12484b3 430313 fffe0e13 fe0e18e3 2000e13 313 35483 900533 2200893 73 230313 fffe0e13 fe0e14e3 a00893
  //   73 f00493 100913 409909b3 900533 2200893 73 fff48493 ff29f6e3 a00893 73 a00893 73 413 140413 800533
  //   2200893 73 240413 800533 2200893 73 340413 800533 2200893 73 440413 800533 2200893 73 540413 800533
  //   2200893 73 640413 800533 2200893 73 740413 800533 2200893 73 840413 800533 2200893 2200893 73 8067
  //   rs1
  //   rs2
  //   rd
  //   Beq
  //   Bgeu
  //   Bne
  //   MemToReg
  //   MemWrite
  //   AluOP
  //   AluSrcB
  //   RegWrite
  //   为方便自动评测，需要输出PC，IR，寄存器堆写如数据RDin
  //   RAM写使能MemWrite、RAM写入数据MDin等信号
  //   控制位
  //   暂停节拍，不能为0
  //   戳工具置1进入计数暂停模式，ctrl+k时钟自动运行到对应节拍暂停
  //   ctrl+k关闭时钟连续运行，将控制位置零，进入单步调试模式调试
  //   用这个时钟源需要去掉电路中的其他时钟源
  //   数据存储器
  //   可计数暂停的时钟源
endmodule

// 运算器控制器
module \运算控制器自动生成  (
  input  OP2,
  input  OP3,
  input  OP4,
  input  OP5,
  input  OP6,
  input  F12,
  input  F13,
  input  F14,
  input  F25,
  input  F30,
  output S0,
  output S1,
  output S2,
  output S3
);

  wire and_1_out, and_2_out, and_3_out, and_4_out, and_5_out, and_6_out, and_7_out, and_8_out, and_9_out,
       and_10_out, and_11_out, and_12_out, and_13_out, and_14_out, and_15_out, and_16_out, and_17_out,
       and_18_out, and_19_out, and_20_out, and_21_out, and_22_out, and_23_out, and_24_out, and_25_out,
       and_26_out, and_27_out, and_28_out, and_29_out, and_30_out, and_31_out, and_32_out, and_33_out,
       and_34_out, and_35_out, and_36_out, and_37_out, and_38_out, and_39_out, and_40_out, and_41_out,
       and_42_out, and_43_out, not_1_out, not_2_out, not_3_out, not_4_out, not_5_out, not_6_out, not_7_out,
       not_8_out, not_9_out, not_10_out, not_11_out, not_12_out, not_13_out, not_14_out, not_15_out,
       not_16_out, not_17_out, not_18_out, not_19_out, not_20_out, not_21_out, not_22_out, not_23_out,
       not_24_out, not_25_out, not_26_out, not_27_out, not_28_out, not_29_out, not_30_out, not_31_out,
       not_32_out, not_33_out, not_34_out, not_35_out, not_36_out, not_37_out, not_38_out, not_39_out,
       not_40_out, not_41_out, not_42_out, not_43_out, not_44_out, not_45_out, not_46_out, not_47_out,
       not_48_out, not_49_out, not_50_out, not_51_out, not_52_out, not_53_out, not_54_out, not_55_out,
       not_56_out, not_57_out, not_58_out, not_59_out, not_60_out, not_61_out, not_62_out, not_63_out,
       not_64_out, not_65_out, not_66_out, not_67_out, not_68_out, not_69_out, not_70_out, not_71_out,
       not_72_out, not_73_out, not_74_out, not_75_out, not_76_out, not_77_out, not_78_out, not_79_out,
       not_80_out, not_81_out, not_82_out, not_83_out, not_84_out, not_85_out, not_86_out, not_87_out,
       not_88_out, not_89_out, not_90_out, not_91_out, not_92_out, not_93_out, not_94_out, not_95_out,
       not_96_out, not_97_out, not_98_out, not_99_out, not_100_out, not_101_out, not_102_out, not_103_out,
       not_104_out, not_105_out, not_106_out, not_107_out, not_108_out, not_109_out, not_110_out,
       not_111_out, not_112_out, not_113_out, not_114_out, not_115_out, not_116_out, not_117_out,
       not_118_out, not_119_out, not_120_out, not_121_out, not_122_out, not_123_out, not_124_out,
       not_125_out, not_126_out, not_127_out, not_128_out, not_129_out, not_130_out, not_131_out,
       not_132_out, not_133_out, not_134_out, not_135_out, not_136_out, not_137_out, not_138_out,
       not_139_out, not_140_out, not_141_out, not_142_out, not_143_out, not_144_out, not_145_out,
       not_146_out, not_147_out, not_148_out, not_149_out, not_150_out, not_151_out, not_152_out,
       not_153_out, not_154_out, not_155_out, not_156_out, not_157_out, not_158_out, not_159_out,
       not_160_out, not_161_out, not_162_out, not_163_out, not_164_out, not_165_out, not_166_out,
       not_167_out, not_168_out, not_169_out, not_170_out, not_171_out, not_172_out, not_173_out,
       not_174_out, not_175_out, not_176_out, not_177_out, not_178_out, not_179_out, not_180_out,
       not_181_out, not_182_out, not_183_out, not_184_out, not_185_out, not_186_out, not_187_out,
       not_188_out, not_189_out, not_190_out, not_191_out, not_192_out, not_193_out, not_194_out,
       not_195_out, not_196_out, not_197_out, not_198_out, not_199_out, not_200_out, not_201_out,
       not_202_out, not_203_out, not_204_out, not_205_out, not_206_out, not_207_out, not_208_out,
       not_209_out, not_210_out, not_211_out, not_212_out, not_213_out, not_214_out, not_215_out,
       not_216_out, not_217_out, not_218_out, not_219_out, not_220_out, not_221_out, not_222_out,
       not_223_out, not_224_out, not_225_out, not_226_out, not_227_out, not_228_out, not_229_out,
       not_230_out, not_231_out, not_232_out, not_233_out, not_234_out, not_235_out, not_236_out,
       not_237_out, not_238_out, not_239_out, not_240_out, not_241_out, not_242_out;

  not not_1 (not_1_out, F30);
  not not_2 (not_2_out, F25);
  not not_3 (not_3_out, F14);
  not not_4 (not_4_out, F13);
  not not_5 (not_5_out, F12);
  not not_6 (not_6_out, OP6);
  not not_7 (not_7_out, OP3);
  not not_8 (not_8_out, OP2);
  not not_9 (not_9_out, F30);
  not not_10 (not_10_out, F25);
  not not_11 (not_11_out, OP6);
  not not_12 (not_12_out, OP3);
  not not_13 (not_13_out, OP2);
  not not_14 (not_14_out, F30);
  not not_15 (not_15_out, F25);
  not not_16 (not_16_out, F14);
  not not_17 (not_17_out, F12);
  not not_18 (not_18_out, OP6);
  not not_19 (not_19_out, OP3);
  not not_20 (not_20_out, OP2);
  not not_21 (not_21_out, F14);
  not not_22 (not_22_out, F13);
  not not_23 (not_23_out, F12);
  not not_24 (not_24_out, OP6);
  not not_25 (not_25_out, OP5);
  not not_26 (not_26_out, OP3);
  not not_27 (not_27_out, OP2);
  not not_28 (not_28_out, OP6);
  not not_29 (not_29_out, OP5);
  not not_30 (not_30_out, OP3);
  not not_31 (not_31_out, OP2);
  not not_32 (not_32_out, F13);
  not not_33 (not_33_out, F12);
  not not_34 (not_34_out, OP6);
  not not_35 (not_35_out, OP5);
  not not_36 (not_36_out, OP3);
  not not_37 (not_37_out, OP2);
  not not_38 (not_38_out, F14);
  not not_39 (not_39_out, F12);
  not not_40 (not_40_out, OP6);
  not not_41 (not_41_out, OP5);
  not not_42 (not_42_out, OP3);
  not not_43 (not_43_out, OP2);
  not not_44 (not_44_out, F25);
  not not_45 (not_45_out, F13);
  not not_46 (not_46_out, OP6);
  not not_47 (not_47_out, OP5);
  not not_48 (not_48_out, OP3);
  not not_49 (not_49_out, OP2);
  not not_50 (not_50_out, F14);
  not not_51 (not_51_out, F12);
  not not_52 (not_52_out, OP6);
  not not_53 (not_53_out, OP5);
  not not_54 (not_54_out, OP4);
  not not_55 (not_55_out, OP3);
  not not_56 (not_56_out, OP2);
  not not_57 (not_57_out, F14);
  not not_58 (not_58_out, F12);
  not not_59 (not_59_out, OP6);
  not not_60 (not_60_out, OP4);
  not not_61 (not_61_out, OP3);
  not not_62 (not_62_out, OP2);
  not not_63 (not_63_out, F14);
  not not_64 (not_64_out, F13);
  not not_65 (not_65_out, F12);
  not not_66 (not_66_out, OP4);
  not not_67 (not_67_out, OP3);
  not not_68 (not_68_out, OP2);
  not not_69 (not_69_out, F14);
  not not_70 (not_70_out, F13);
  not not_71 (not_71_out, OP4);
  not not_72 (not_72_out, OP3);
  not not_73 (not_73_out, OP2);
  not not_74 (not_74_out, OP4);
  not not_75 (not_75_out, F14);
  not not_76 (not_76_out, F13);
  not not_77 (not_77_out, F12);
  not not_78 (not_78_out, OP4);
  not not_79 (not_79_out, OP3);
  not not_80 (not_80_out, F13);
  not not_81 (not_81_out, OP6);
  not not_82 (not_82_out, OP5);
  not not_83 (not_83_out, OP4);
  not not_84 (not_84_out, OP3);
  not not_85 (not_85_out, OP2);
  not not_86 (not_86_out, F25);
  not not_87 (not_87_out, F14);
  not not_88 (not_88_out, F13);
  not not_89 (not_89_out, F12);
  not not_90 (not_90_out, OP6);
  not not_91 (not_91_out, OP3);
  not not_92 (not_92_out, OP2);
  not not_93 (not_93_out, F30);
  not not_94 (not_94_out, F25);
  not not_95 (not_95_out, OP6);
  not not_96 (not_96_out, OP3);
  not not_97 (not_97_out, OP2);
  not not_98 (not_98_out, F30);
  not not_99 (not_99_out, F25);
  not not_100 (not_100_out, F14);
  not not_101 (not_101_out, F12);
  not not_102 (not_102_out, OP6);
  not not_103 (not_103_out, OP3);
  not not_104 (not_104_out, OP2);
  not not_105 (not_105_out, OP6);
  not not_106 (not_106_out, OP5);
  not not_107 (not_107_out, OP3);
  not not_108 (not_108_out, OP2);
  not not_109 (not_109_out, F14);
  not not_110 (not_110_out, F12);
  not not_111 (not_111_out, OP6);
  not not_112 (not_112_out, OP5);
  not not_113 (not_113_out, OP3);
  not not_114 (not_114_out, OP2);
  not not_115 (not_115_out, F30);
  not not_116 (not_116_out, F25);
  not not_117 (not_117_out, F13);
  not not_118 (not_118_out, OP6);
  not not_119 (not_119_out, OP5);
  not not_120 (not_120_out, OP3);
  not not_121 (not_121_out, OP2);
  not not_122 (not_122_out, F30);
  not not_123 (not_123_out, F25);
  not not_124 (not_124_out, F13);
  not not_125 (not_125_out, OP6);
  not not_126 (not_126_out, OP3);
  not not_127 (not_127_out, OP2);
  not not_128 (not_128_out, F30);
  not not_129 (not_129_out, F25);
  not not_130 (not_130_out, F14);
  not not_131 (not_131_out, F13);
  not not_132 (not_132_out, F12);
  not not_133 (not_133_out, OP6);
  not not_134 (not_134_out, OP3);
  not not_135 (not_135_out, OP2);
  not not_136 (not_136_out, F25);
  not not_137 (not_137_out, F14);
  not not_138 (not_138_out, F13);
  not not_139 (not_139_out, F12);
  not not_140 (not_140_out, OP6);
  not not_141 (not_141_out, OP3);
  not not_142 (not_142_out, OP2);
  not not_143 (not_143_out, F30);
  not not_144 (not_144_out, F25);
  not not_145 (not_145_out, OP6);
  not not_146 (not_146_out, OP3);
  not not_147 (not_147_out, OP2);
  not not_148 (not_148_out, F30);
  not not_149 (not_149_out, F25);
  not not_150 (not_150_out, F14);
  not not_151 (not_151_out, OP6);
  not not_152 (not_152_out, OP3);
  not not_153 (not_153_out, OP2);
  not not_154 (not_154_out, F14);
  not not_155 (not_155_out, F13);
  not not_156 (not_156_out, F12);
  not not_157 (not_157_out, OP6);
  not not_158 (not_158_out, OP5);
  not not_159 (not_159_out, OP3);
  not not_160 (not_160_out, OP2);
  not not_161 (not_161_out, OP6);
  not not_162 (not_162_out, OP5);
  not not_163 (not_163_out, OP3);
  not not_164 (not_164_out, OP2);
  not not_165 (not_165_out, F14);
  not not_166 (not_166_out, F12);
  not not_167 (not_167_out, OP6);
  not not_168 (not_168_out, OP5);
  not not_169 (not_169_out, OP4);
  not not_170 (not_170_out, OP3);
  not not_171 (not_171_out, OP2);
  not not_172 (not_172_out, F14);
  not not_173 (not_173_out, F12);
  not not_174 (not_174_out, OP6);
  not not_175 (not_175_out, OP4);
  not not_176 (not_176_out, OP3);
  not not_177 (not_177_out, OP2);
  not not_178 (not_178_out, F14);
  not not_179 (not_179_out, F13);
  not not_180 (not_180_out, F12);
  not not_181 (not_181_out, OP4);
  not not_182 (not_182_out, OP3);
  not not_183 (not_183_out, OP2);
  not not_184 (not_184_out, F14);
  not not_185 (not_185_out, F13);
  not not_186 (not_186_out, OP4);
  not not_187 (not_187_out, OP3);
  not not_188 (not_188_out, OP2);
  not not_189 (not_189_out, OP4);
  not not_190 (not_190_out, F14);
  not not_191 (not_191_out, F13);
  not not_192 (not_192_out, F12);
  not not_193 (not_193_out, OP4);
  not not_194 (not_194_out, OP3);
  not not_195 (not_195_out, F13);
  not not_196 (not_196_out, OP6);
  not not_197 (not_197_out, OP5);
  not not_198 (not_198_out, OP4);
  not not_199 (not_199_out, OP3);
  not not_200 (not_200_out, OP2);
  not not_201 (not_201_out, OP4);
  not not_202 (not_202_out, OP3);
  not not_203 (not_203_out, OP2);
  not not_204 (not_204_out, F30);
  not not_205 (not_205_out, F25);
  not not_206 (not_206_out, F12);
  not not_207 (not_207_out, OP6);
  not not_208 (not_208_out, OP3);
  not not_209 (not_209_out, OP2);
  not not_210 (not_210_out, F30);
  not not_211 (not_211_out, F25);
  not not_212 (not_212_out, F14);
  not not_213 (not_213_out, F12);
  not not_214 (not_214_out, OP6);
  not not_215 (not_215_out, OP3);
  not not_216 (not_216_out, OP2);
  not not_217 (not_217_out, F30);
  not not_218 (not_218_out, F25);
  not not_219 (not_219_out, F14);
  not not_220 (not_220_out, OP6);
  not not_221 (not_221_out, OP3);
  not not_222 (not_222_out, OP2);
  not not_223 (not_223_out, F12);
  not not_224 (not_224_out, OP6);
  not not_225 (not_225_out, OP5);
  not not_226 (not_226_out, OP3);
  not not_227 (not_227_out, OP2);
  not not_228 (not_228_out, F13);
  not not_229 (not_229_out, F12);
  not not_230 (not_230_out, OP6);
  not not_231 (not_231_out, OP5);
  not not_232 (not_232_out, OP3);
  not not_233 (not_233_out, OP2);
  not not_234 (not_234_out, F14);
  not not_235 (not_235_out, F12);
  not not_236 (not_236_out, OP6);
  not not_237 (not_237_out, OP5);
  not not_238 (not_238_out, OP3);
  not not_239 (not_239_out, OP2);
  not not_240 (not_240_out, OP4);
  not not_241 (not_241_out, OP3);
  not not_242 (not_242_out, OP2);
  and and_1 (and_1_out, not_1_out, not_2_out, not_3_out, not_4_out, not_5_out, not_6_out, OP5, OP4, not_7_out, not_8_out);
  and and_2 (and_2_out, not_9_out, not_10_out, F14, F13, F12, not_11_out, OP5, OP4, not_12_out, not_13_out);
  and and_3 (and_3_out, not_14_out, not_15_out, not_16_out, F13, not_17_out, not_18_out, OP5, OP4, not_19_out, not_20_out);
  and and_4 (and_4_out, not_21_out, not_22_out, not_23_out, not_24_out, not_25_out, OP4, not_26_out, not_27_out);
  and and_5 (and_5_out, F14, F13, F12, not_28_out, not_29_out, OP4, not_30_out, not_31_out);
  and and_6 (and_6_out, F14, not_32_out, not_33_out, not_34_out, not_35_out, OP4, not_36_out, not_37_out);
  and and_7 (and_7_out, not_38_out, F13, not_39_out, not_40_out, not_41_out, OP4, not_42_out, not_43_out);
  and and_8 (and_8_out, F30, not_44_out, F14, not_45_out, F12, not_46_out, not_47_out, OP4, not_48_out, not_49_out);
  and and_9 (and_9_out, not_50_out, F13, not_51_out, not_52_out, not_53_out, not_54_out, not_55_out, not_56_out);
  and and_10 (and_10_out, not_57_out, F13, not_58_out, not_59_out, OP5, not_60_out, not_61_out, not_62_out);
  and and_11 (and_11_out, not_63_out, not_64_out, not_65_out, OP6, OP5, not_66_out, not_67_out, not_68_out);
  and and_12 (and_12_out, not_69_out, not_70_out, F12, OP6, OP5, not_71_out, not_72_out, not_73_out);
  and and_13 (and_13_out, OP6, OP5, not_74_out, OP3, OP2);
  and and_14 (and_14_out, not_75_out, not_76_out, not_77_out, OP6, OP5, not_78_out, not_79_out, OP2);
  and and_15 (and_15_out, F14, not_80_out, F12, not_81_out, not_82_out, not_83_out, not_84_out, not_85_out);
  and and_16 (and_16_out, F30, not_86_out, not_87_out, not_88_out, not_89_out, not_90_out, OP5, OP4, not_91_out, not_92_out);
  and and_17 (and_17_out, not_93_out, not_94_out, F14, F13, F12, not_95_out, OP5, OP4, not_96_out, not_97_out);
  and and_18 (and_18_out, not_98_out, not_99_out, not_100_out, F13, not_101_out, not_102_out, OP5, OP4, not_103_out, not_104_out);
  and and_19 (and_19_out, F14, F13, F12, not_105_out, not_106_out, OP4, not_107_out, not_108_out);
  and and_20 (and_20_out, not_109_out, F13, not_110_out, not_111_out, not_112_out, OP4, not_113_out, not_114_out);
  and and_21 (and_21_out, not_115_out, not_116_out, F14, not_117_out, F12, not_118_out, not_119_out, OP4, not_120_out, not_121_out);
  and and_22 (and_22_out, not_122_out, not_123_out, F14, not_124_out, F12, not_125_out, OP5, OP4, not_126_out, not_127_out);
  and and_23 (and_23_out, not_128_out, not_129_out, not_130_out, not_131_out, not_132_out, not_133_out, OP5, OP4, not_134_out, not_135_out);
  and and_24 (and_24_out, F30, not_136_out, not_137_out, not_138_out, not_139_out, not_140_out, OP5, OP4, not_141_out, not_142_out);
  and and_25 (and_25_out, not_143_out, not_144_out, F14, F13, F12, not_145_out, OP5, OP4, not_146_out, not_147_out);
  and and_26 (and_26_out, not_148_out, not_149_out, not_150_out, F13, F12, not_151_out, OP5, OP4, not_152_out, not_153_out);
  and and_27 (and_27_out, not_154_out, not_155_out, not_156_out, not_157_out, not_158_out, OP4, not_159_out, not_160_out);
  and and_28 (and_28_out, F14, F13, F12, not_161_out, not_162_out, OP4, not_163_out, not_164_out);
  and and_29 (and_29_out, not_165_out, F13, not_166_out, not_167_out, not_168_out, not_169_out, not_170_out, not_171_out);
  and and_30 (and_30_out, not_172_out, F13, not_173_out, not_174_out, OP5, not_175_out, not_176_out, not_177_out);
  and and_31 (and_31_out, not_178_out, not_179_out, not_180_out, OP6, OP5, not_181_out, not_182_out, not_183_out);
  and and_32 (and_32_out, not_184_out, not_185_out, F12, OP6, OP5, not_186_out, not_187_out, not_188_out);
  and and_33 (and_33_out, OP6, OP5, not_189_out, OP3, OP2);
  and and_34 (and_34_out, not_190_out, not_191_out, not_192_out, OP6, OP5, not_193_out, not_194_out, OP2);
  and and_35 (and_35_out, F14, not_195_out, F12, not_196_out, not_197_out, not_198_out, not_199_out, not_200_out);
  and and_36 (and_36_out, F14, F13, F12, OP6, OP5, not_201_out, not_202_out, not_203_out);
  and and_37 (and_37_out, not_204_out, not_205_out, F14, F13, not_206_out, not_207_out, OP5, OP4, not_208_out, not_209_out);
  and and_38 (and_38_out, not_210_out, not_211_out, not_212_out, F13, not_213_out, not_214_out, OP5, OP4, not_215_out, not_216_out);
  and and_39 (and_39_out, not_217_out, not_218_out, not_219_out, F13, F12, not_220_out, OP5, OP4, not_221_out, not_222_out);
  and and_40 (and_40_out, F14, F13, not_223_out, not_224_out, not_225_out, OP4, not_226_out, not_227_out);
  and and_41 (and_41_out, F14, not_228_out, not_229_out, not_230_out, not_231_out, OP4, not_232_out, not_233_out);
  and and_42 (and_42_out, not_234_out, F13, not_235_out, not_236_out, not_237_out, OP4, not_238_out, not_239_out);
  and and_43 (and_43_out, F14, F13, F12, OP6, OP5, not_240_out, not_241_out, not_242_out);
  or or_1 (S0, and_1_out, and_2_out, and_3_out, and_4_out, and_5_out, and_6_out, and_7_out, and_8_out, and_9_out, and_10_out, and_11_out, and_12_out, and_13_out, and_14_out, and_15_out);
  or or_2 (S1, and_16_out, and_17_out, and_18_out, and_19_out, and_20_out, and_21_out, and_22_out);
  or or_3 (S2, and_23_out, and_24_out, and_25_out, and_26_out, and_27_out, and_28_out, and_29_out, and_30_out, and_31_out, and_32_out, and_33_out, and_34_out, and_35_out, and_36_out);
  or or_4 (S3, and_37_out, and_38_out, and_39_out, and_40_out, and_41_out, and_42_out, and_43_out);
endmodule

// 控制信号生成
module \控制信号自动生成  (
  input  OP2,
  input  OP3,
  input  OP4,
  input  OP5,
  input  OP6,
  input  F12,
  input  F13,
  input  F14,
  input  F25,
  input  F30,
  output MemToReg,
  output MemWrite,
  output ALU_SRC,
  output RegWrite,
  output ecall,
  output S_Type,
  output BEQ,
  output BNE,
  output JALR,
  output JAL,
  output U_Type,
  output BGEU,
  output LHU,
  output URET,
  output CSRRSI,
  output CSRRCI
);

  wire and_1_out, and_2_out, and_4_out, and_5_out, and_6_out, and_7_out, and_8_out, and_9_out, and_10_out,
       and_11_out, and_12_out, and_13_out, and_14_out, and_15_out, and_16_out, and_17_out, and_18_out,
       and_19_out, and_20_out, and_21_out, and_22_out, not_1_out, not_2_out, not_3_out, not_4_out, not_5_out,
       not_6_out, not_7_out, not_8_out, not_9_out, not_10_out, not_11_out, not_12_out, not_13_out,
       not_14_out, not_15_out, not_16_out, not_17_out, not_18_out, not_19_out, not_20_out, not_21_out,
       not_22_out, not_23_out, not_24_out, not_25_out, not_26_out, not_27_out, not_28_out, not_29_out,
       not_30_out, not_31_out, not_32_out, not_33_out, not_34_out, not_35_out, not_36_out, not_37_out,
       not_38_out, not_39_out, not_40_out, not_41_out, not_42_out, not_43_out, not_44_out, not_45_out,
       not_46_out, not_47_out, not_48_out, not_49_out, not_50_out, not_51_out, not_52_out, not_53_out,
       not_54_out, not_55_out, not_56_out, not_57_out, not_58_out, not_59_out, not_60_out, not_61_out,
       not_62_out, not_63_out, not_64_out, not_65_out, not_66_out, not_67_out, not_68_out, not_69_out,
       not_70_out, not_71_out, not_72_out, not_73_out, not_74_out, not_75_out, not_76_out, not_77_out,
       not_78_out, not_79_out, not_80_out, not_81_out, not_82_out, not_83_out, not_84_out, not_85_out,
       not_86_out, not_87_out, not_88_out, not_89_out, not_90_out, not_91_out, not_92_out, not_93_out,
       not_94_out, not_95_out, not_96_out, not_97_out, not_98_out, not_99_out, not_100_out, not_101_out,
       not_102_out, not_103_out, not_104_out, not_105_out, not_106_out, not_107_out, not_108_out,
       not_109_out, not_110_out, not_111_out, not_112_out, not_113_out, not_114_out, not_115_out,
       not_116_out, not_117_out, not_118_out, not_119_out, not_120_out, not_121_out, not_122_out,
       not_123_out, not_124_out, not_125_out, not_126_out, not_127_out, not_128_out, not_129_out,
       not_130_out, not_131_out, not_132_out, not_133_out, not_134_out, not_135_out, not_136_out,
       not_137_out, not_138_out, not_139_out, not_140_out, not_141_out, not_142_out, not_143_out,
       not_144_out, not_145_out, not_146_out, not_147_out, not_148_out, not_149_out, not_150_out,
       not_151_out, not_152_out, not_153_out, not_154_out, not_155_out, not_156_out, not_157_out,
       not_158_out, not_159_out, not_160_out, not_161_out, not_162_out, not_163_out, not_164_out, not_165_out;

  not not_1 (not_1_out, OP2);
  not not_2 (not_2_out, OP3);
  not not_3 (not_3_out, OP4);
  not not_4 (not_4_out, OP5);
  not not_5 (not_5_out, OP6);
  not not_6 (not_6_out, F12);
  not not_7 (not_7_out, F14);
  not not_8 (not_8_out, OP2);
  not not_9 (not_9_out, OP3);
  not not_10 (not_10_out, OP4);
  not not_11 (not_11_out, OP5);
  not not_12 (not_12_out, OP6);
  not not_13 (not_13_out, F13);
  not not_14 (not_14_out, OP2);
  not not_15 (not_15_out, OP3);
  not not_16 (not_16_out, OP4);
  not not_17 (not_17_out, OP6);
  not not_18 (not_18_out, F12);
  not not_19 (not_19_out, F14);
  not not_20 (not_20_out, OP2);
  not not_21 (not_21_out, OP3);
  not not_22 (not_22_out, OP4);
  not not_23 (not_23_out, OP6);
  not not_24 (not_24_out, F12);
  not not_25 (not_25_out, F14);
  not not_26 (not_26_out, OP2);
  not not_27 (not_27_out, OP3);
  not not_28 (not_28_out, OP4);
  not not_29 (not_29_out, OP5);
  not not_30 (not_30_out, OP6);
  not not_31 (not_31_out, F13);
  not not_32 (not_32_out, OP2);
  not not_33 (not_33_out, OP3);
  not not_34 (not_34_out, OP5);
  not not_35 (not_35_out, OP6);
  not not_36 (not_36_out, F12);
  not not_37 (not_37_out, OP2);
  not not_38 (not_38_out, OP3);
  not not_39 (not_39_out, OP5);
  not not_40 (not_40_out, OP6);
  not not_41 (not_41_out, F13);
  not not_42 (not_42_out, F25);
  not not_43 (not_43_out, F30);
  not not_44 (not_44_out, OP2);
  not not_45 (not_45_out, OP3);
  not not_46 (not_46_out, OP5);
  not not_47 (not_47_out, OP6);
  not not_48 (not_48_out, F25);
  not not_49 (not_49_out, OP2);
  not not_50 (not_50_out, OP3);
  not not_51 (not_51_out, OP5);
  not not_52 (not_52_out, OP6);
  not not_53 (not_53_out, OP3);
  not not_54 (not_54_out, OP4);
  not not_55 (not_55_out, F12);
  not not_56 (not_56_out, F13);
  not not_57 (not_57_out, F14);
  not not_58 (not_58_out, OP2);
  not not_59 (not_59_out, OP3);
  not not_60 (not_60_out, OP5);
  not not_61 (not_61_out, OP6);
  not not_62 (not_62_out, F12);
  not not_63 (not_63_out, F14);
  not not_64 (not_64_out, OP2);
  not not_65 (not_65_out, OP3);
  not not_66 (not_66_out, OP4);
  not not_67 (not_67_out, OP5);
  not not_68 (not_68_out, OP6);
  not not_69 (not_69_out, F13);
  not not_70 (not_70_out, OP2);
  not not_71 (not_71_out, OP3);
  not not_72 (not_72_out, OP6);
  not not_73 (not_73_out, F12);
  not not_74 (not_74_out, F13);
  not not_75 (not_75_out, F14);
  not not_76 (not_76_out, F25);
  not not_77 (not_77_out, OP3);
  not not_78 (not_78_out, OP5);
  not not_79 (not_79_out, OP6);
  not not_80 (not_80_out, F12);
  not not_81 (not_81_out, OP3);
  not not_82 (not_82_out, OP5);
  not not_83 (not_83_out, OP6);
  not not_84 (not_84_out, F13);
  not not_85 (not_85_out, F25);
  not not_86 (not_86_out, F30);
  not not_87 (not_87_out, OP3);
  not not_88 (not_88_out, OP5);
  not not_89 (not_89_out, OP6);
  not not_90 (not_90_out, F25);
  not not_91 (not_91_out, OP3);
  not not_92 (not_92_out, OP5);
  not not_93 (not_93_out, OP6);
  not not_94 (not_94_out, OP2);
  not not_95 (not_95_out, OP3);
  not not_96 (not_96_out, OP6);
  not not_97 (not_97_out, F25);
  not not_98 (not_98_out, F30);
  not not_99 (not_99_out, OP2);
  not not_100 (not_100_out, OP3);
  not not_101 (not_101_out, OP6);
  not not_102 (not_102_out, F25);
  not not_103 (not_103_out, F30);
  not not_104 (not_104_out, OP4);
  not not_105 (not_105_out, F12);
  not not_106 (not_106_out, F13);
  not not_107 (not_107_out, F14);
  not not_108 (not_108_out, OP3);
  not not_109 (not_109_out, OP5);
  not not_110 (not_110_out, OP6);
  not not_111 (not_111_out, OP4);
  not not_112 (not_112_out, OP2);
  not not_113 (not_113_out, OP3);
  not not_114 (not_114_out, F12);
  not not_115 (not_115_out, F13);
  not not_116 (not_116_out, F14);
  not not_117 (not_117_out, F25);
  not not_118 (not_118_out, F30);
  not not_119 (not_119_out, OP2);
  not not_120 (not_120_out, OP3);
  not not_121 (not_121_out, OP4);
  not not_122 (not_122_out, OP6);
  not not_123 (not_123_out, F12);
  not not_124 (not_124_out, F14);
  not not_125 (not_125_out, OP2);
  not not_126 (not_126_out, OP3);
  not not_127 (not_127_out, OP4);
  not not_128 (not_128_out, F12);
  not not_129 (not_129_out, F13);
  not not_130 (not_130_out, F14);
  not not_131 (not_131_out, OP2);
  not not_132 (not_132_out, OP3);
  not not_133 (not_133_out, OP4);
  not not_134 (not_134_out, F13);
  not not_135 (not_135_out, F14);
  not not_136 (not_136_out, OP3);
  not not_137 (not_137_out, OP4);
  not not_138 (not_138_out, F12);
  not not_139 (not_139_out, F13);
  not not_140 (not_140_out, F14);
  not not_141 (not_141_out, OP4);
  not not_142 (not_142_out, OP3);
  not not_143 (not_143_out, OP5);
  not not_144 (not_144_out, OP6);
  not not_145 (not_145_out, OP2);
  not not_146 (not_146_out, OP3);
  not not_147 (not_147_out, OP4);
  not not_148 (not_148_out, OP2);
  not not_149 (not_149_out, OP3);
  not not_150 (not_150_out, OP4);
  not not_151 (not_151_out, OP5);
  not not_152 (not_152_out, OP6);
  not not_153 (not_153_out, F13);
  not not_154 (not_154_out, OP2);
  not not_155 (not_155_out, OP3);
  not not_156 (not_156_out, F12);
  not not_157 (not_157_out, F13);
  not not_158 (not_158_out, F14);
  not not_159 (not_159_out, F25);
  not not_160 (not_160_out, F30);
  not not_161 (not_161_out, F12);
  not not_162 (not_162_out, OP3);
  not not_163 (not_163_out, OP2);
  not not_164 (not_164_out, OP3);
  not not_165 (not_165_out, OP2);
  and and_1 (and_1_out, not_1_out, not_2_out, not_3_out, not_4_out, not_5_out, not_6_out, F13, not_7_out);
  and and_2 (and_2_out, not_8_out, not_9_out, not_10_out, not_11_out, not_12_out, F12, not_13_out, F14);
  and and_3 (MemWrite, not_14_out, not_15_out, not_16_out, OP5, not_17_out, not_18_out, F13, not_19_out);
  and and_4 (and_4_out, not_20_out, not_21_out, not_22_out, not_23_out, not_24_out, F13, not_25_out);
  and and_5 (and_5_out, not_26_out, not_27_out, not_28_out, not_29_out, not_30_out, F12, not_31_out, F14);
  and and_6 (and_6_out, not_32_out, not_33_out, OP4, not_34_out, not_35_out, not_36_out);
  and and_7 (and_7_out, not_37_out, not_38_out, OP4, not_39_out, not_40_out, not_41_out, not_42_out, not_43_out);
  and and_8 (and_8_out, not_44_out, not_45_out, OP4, not_46_out, not_47_out, F14, not_48_out);
  and and_9 (and_9_out, not_49_out, not_50_out, OP4, not_51_out, not_52_out, F13, F14);
  and and_10 (and_10_out, OP2, not_53_out, not_54_out, OP5, OP6, not_55_out, not_56_out, not_57_out);
  and and_11 (and_11_out, not_58_out, not_59_out, not_60_out, not_61_out, not_62_out, F13, not_63_out);
  and and_12 (and_12_out, not_64_out, not_65_out, not_66_out, not_67_out, not_68_out, F12, not_69_out, F14);
  and and_13 (and_13_out, not_70_out, not_71_out, OP4, not_72_out, not_73_out, not_74_out, not_75_out, not_76_out);
  and and_14 (and_14_out, not_77_out, OP4, not_78_out, not_79_out, not_80_out);
  and and_15 (and_15_out, not_81_out, OP4, not_82_out, not_83_out, not_84_out, not_85_out, not_86_out);
  and and_16 (and_16_out, not_87_out, OP4, not_88_out, not_89_out, F14, not_90_out);
  and and_17 (and_17_out, not_91_out, OP4, not_92_out, not_93_out, F13, F14);
  and and_18 (and_18_out, not_94_out, not_95_out, OP4, not_96_out, F12, F14, not_97_out, not_98_out);
  and and_19 (and_19_out, not_99_out, not_100_out, OP4, OP5, not_101_out, F13, not_102_out, not_103_out);
  and and_20 (and_20_out, OP2, not_104_out, OP5, OP6, not_105_out, not_106_out, not_107_out);
  and and_21 (and_21_out, OP2, not_108_out, OP4, not_109_out, not_110_out);
  and and_22 (and_22_out, OP2, OP3, not_111_out, OP5, OP6);
  and and_23 (ecall, not_112_out, not_113_out, OP4, OP5, OP6, not_114_out, not_115_out, not_116_out, not_117_out, not_118_out);
  and and_24 (S_Type, not_119_out, not_120_out, not_121_out, OP5, not_122_out, not_123_out, F13, not_124_out);
  and and_25 (BEQ, not_125_out, not_126_out, not_127_out, OP5, OP6, not_128_out, not_129_out, not_130_out);
  and and_26 (BNE, not_131_out, not_132_out, not_133_out, OP5, OP6, F12, not_134_out, not_135_out);
  and and_27 (JALR, OP2, not_136_out, not_137_out, OP5, OP6, not_138_out, not_139_out, not_140_out);
  and and_28 (JAL, OP2, OP3, not_141_out, OP5, OP6);
  and and_29 (U_Type, OP2, not_142_out, OP4, not_143_out, not_144_out);
  and and_30 (BGEU, not_145_out, not_146_out, not_147_out, OP5, OP6, F12, F13, F14);
  and and_31 (LHU, not_148_out, not_149_out, not_150_out, not_151_out, not_152_out, F12, not_153_out, F14);
  and and_32 (URET, not_154_out, not_155_out, OP4, OP5, OP6, not_156_out, not_157_out, not_158_out, not_159_out, not_160_out);
  and and_33 (CSRRSI, F14, F13, not_161_out, OP6, OP5, OP4, not_162_out, not_163_out);
  and and_34 (CSRRCI, F14, F13, F12, OP6, OP5, OP4, not_164_out, not_165_out);
  or or_1 (MemToReg, and_1_out, and_2_out);
  or or_2 (ALU_SRC, and_4_out, and_5_out, and_6_out, and_7_out, and_8_out, and_9_out, and_10_out);
  or or_3 (RegWrite, and_11_out, and_12_out, and_13_out, and_14_out, and_15_out, and_16_out, and_17_out, and_18_out, and_19_out, and_20_out, and_21_out, and_22_out);
endmodule

// ALU
module ALU (
  input  [31:0] X,
  input  [31:0] Y,
  input  [3:0] AluOP,
  output out_4,
  output Equal,
  output out_6,
  output [31:0] Result,
  output [31:0] Result_2
);

  wire [0:0] comparator_1_lt, comparator_2_lt;
  wire [31:0] adder_1_out, AND_out, divider_1_out, divider_1_rem, multiplier_1_cout, multiplier_1_out,
       NOR_out, OR_out, shifter_1_out, shifter_2_out, shifter_3_out, subtractor_1_out, XOR_out;

  assign AND_out = X & Y;  // AND_Gate AND, 32 bits wide
  assign OR_out = X | Y;  // OR_Gate OR, 32 bits wide
  Shifter #(.width(32), .shift("ll")) shifter_1 (.in(X), .\dist (Y[4:0]), .out(shifter_1_out));
  Shifter #(.width(32), .shift("ar")) shifter_2 (.in(X), .\dist (Y[4:0]), .out(shifter_2_out));
  Shifter #(.width(32), .shift("lr")) shifter_3 (.in(X), .\dist (Y[4:0]), .out(shifter_3_out));
  Multiplier #(.width(32)) multiplier_1 (.a(X), .b(Y), .out(multiplier_1_out), .cout(multiplier_1_cout));  // open: cin
  Divider #(.width(32)) divider_1 (.a(X), .b(Y), .out(divider_1_out), .rem(divider_1_rem));  // open: upper
  Adder #(.width(32)) adder_1 (.a(X), .b(Y), .out(adder_1_out));  // open: cin, cout
  Subtractor #(.width(32)) subtractor_1 (.a(X), .b(Y), .out(subtractor_1_out));  // open: bin, bout
  assign XOR_out = X ^ Y;  // XOR_Gate XOR, 32 bits wide
  assign NOR_out = ~(X | Y);  // NOR_Gate NOR, 32 bits wide
  Comparator #(.width(32), .mode("twosComplement")) comparator_1 (
    .a(X), .b(Y), .eq(Equal), .lt(comparator_1_lt[0]));  // open: gt
  Comparator #(.width(32), .mode("unsigned")) comparator_2 (.a(X), .b(Y), .lt(comparator_2_lt[0]));  // open: gt, eq
  Multiplexer #(.select(4), .width(32), .disabled("Z"), .enable("false")) multiplexer_1 (
    .in0(shifter_1_out), .in1(shifter_2_out), .in2(shifter_3_out), .in3(multiplier_1_out),
    .in4(divider_1_out), .in5(adder_1_out), .in6(subtractor_1_out), .in7(AND_out), .in8(OR_out),
    .in9(XOR_out), .in10(NOR_out), .in11({{31{1'b0}}, comparator_1_lt[0]}),
    .in12({{31{1'b0}}, comparator_2_lt[0]}), .in13({32{1'b0}}), .in14({32{1'b0}}), .in15({32{1'b0}}),
    .out(Result), .sel(AluOP));
  Multiplexer #(.select(4), .width(32), .disabled("Z"), .enable("false")) multiplexer_2 (
    .in0({32{1'b0}}), .in1({32{1'b0}}), .in2({32{1'b0}}), .in3(multiplier_1_cout), .in4(divider_1_rem),
    .in5({32{1'b0}}), .in6({32{1'b0}}), .in7({32{1'b0}}), .in8({32{1'b0}}), .in9({32{1'b0}}),
    .in10({32{1'b0}}), .in11({32{1'b0}}), .in12({32{1'b0}}), .in13({32{1'b0}}), .in14({32{1'b0}}),
    .in15({32{1'b0}}), .out(Result_2), .sel(AluOP));
  Multiplexer #(.select(4), .width(1), .disabled("Z"), .enable("false")) multiplexer_3 (
    .in0(1'b0), .in1(1'b0), .in2(1'b0), .in3(1'b0), .in4(1'b0), .in5(1'b0), .in6(1'b0), .in7(1'b0),
    .in8(1'b0), .in9(1'b0), .in10(1'b0), .in11(comparator_1_lt[0]), .in12(comparator_2_lt[0]), .in13(1'b0),
    .in14(1'b0), .in15(1'b0), .out(out_6), .sel(AluOP));
  not not_1 (out_4, out_6);

  // Other names for the same wires on the sheet: Result2[31:0] = Result_2; S[3:0] = AluOP; tunnel = out_6;
  //   tunnel_t = out_4

  // Notes on the sheet:
  //   不要改变此引脚区域内容，也不要改变ALU封装形式
  //   输入引脚
  //   输出引脚
endmodule

module Regifile (
  input  [31:0] Din,
  input  Clk,
  input  WE,
  input  [4:0] R1_num,
  input  [4:0] W_num,
  input  [4:0] R2_num,
  output [31:0] R1,
  output [31:0] R2
);

  // RegisterFile registerfile_1: pin names not known; wires that end beside it: Din, Clk, WE, W_num, R1_num, R2_num, R1, R2
endmodule

module \理想流水线  (
  output RegWrite,
  output MemWrite,
  output [31:0] IF_PC,
  output [31:0] ID_PC,
  output [31:0] EX_PC,
  output [31:0] M_PC,
  output [31:0] WB_PC,
  output [31:0] RDin,
  output [31:0] MDin,
  output [31:0] LedData
);

  wire CLK, clock_1_out, clock_2_out, comparator_1_eq, comparator_1_lt, d_ff_1_q, Go, IR1, IR2, IR3,
       nand_1_out, RST, W1, W2, W3;
  wire [12:0] CNT_num;
  wire [15:0] \LoadUse次数 , \总周期数 , \插入气泡数 , \无条件分支数 , \条件分支成功数 ;
  wire [31:0] EX_IR, ID_IR, IF_IR, MEM_IR, WB_IR;

  Button \u_总复位  (.out(RST));
  Button _1 (.out(IR1));
  Button _2 (.out(IR2));
  Button _3 (.out(IR3));
  // Probe on \总周期数 
  // Probe on \总周期数 
  Button \u_继续运行  (.out(Go));
  LED #(.active("true")) led_1 (.in(W1));
  LED #(.active("true")) led_2 (.in(W2));
  LED #(.active("true")) led_3 (.in(W3));
  Hex_Digit_Display hex_digit_display_1 (.value(LedData[31:28]));  // open: dp
  // Probe on IF_PC[19:0]
  // RiscV_Probe riscv_probe_1: pin names not known; wires that end beside it: IF_IR
  Hex_Digit_Display hex_digit_display_2 (.value(LedData[23:20]));  // open: dp
  Hex_Digit_Display hex_digit_display_3 (.value(LedData[27:24]));  // open: dp
  // Probe on ID_PC[19:0]
  // RiscV_Probe riscv_probe_2: pin names not known; wires that end beside it: ID_IR
  Hex_Digit_Display hex_digit_display_4 (.value(LedData[15:12]));  // open: dp
  Hex_Digit_Display hex_digit_display_5 (.value(LedData[19:16]));  // open: dp
  Hex_Digit_Display hex_digit_display_6 (.value(LedData[11:8]));  // open: dp
  Hex_Digit_Display hex_digit_display_7 (.value(LedData[7:4]));  // open: dp
  Clock #(.highDuration(1), .lowDuration(1)) clock_1 (.out(clock_1_out));
  // Probe on EX_PC[19:0]
  // RiscV_Probe riscv_probe_3: pin names not known; wires that end beside it: clock_1_out, EX_IR, CLK
  Hex_Digit_Display hex_digit_display_8 (.value(LedData[3:0]));  // open: dp
  // Probe on \总周期数 
  // Probe on M_PC[19:0]
  // RiscV_Probe riscv_probe_4: pin names not known; wires that end beside it: MEM_IR
  // Probe on \总周期数 
  // Probe on \无条件分支数 
  // Probe on \条件分支成功数 
  // Probe on \插入气泡数 
  // Probe on \LoadUse次数 
  // Probe on IF_PC[11:0]
  // Probe on WB_PC[19:0]
  // RiscV_Probe riscv_probe_5: pin names not known; wires that end beside it: WB_IR
  // Probe on EX_PC[11:0]
  // Probe on ID_PC[11:0]
  // Probe on M_PC[11:0]
  D_Flip_Flop #(.trigger("high"), .Pre_Clr_Positions("LEGACY"), .NegatePresetClear("false"), .enable("true"), .NewFFLayout("false")) d_ff_1 (.Q(d_ff_1_q));  // open: clk, D, Qn, preset, en, reset
  // Probe on 13'hc
  // Probe on WB_PC[11:0]
  Comparator #(.width(13), .mode("twosComplement")) comparator_1 (
    .a(CNT_num), .b(13'hc), .eq(comparator_1_eq), .lt(comparator_1_lt));  // open: gt
  Clock #(.highDuration(1), .lowDuration(1)) clock_2 (.out(clock_2_out));
  nand nand_1 (nand_1_out, d_ff_1_q, comparator_1_eq);
  Counter #(.width(13), .max('h1fff), .ongoal("stay"), .trigger("rising"), .behavior("old")) counter_1 (
    .count(comparator_1_lt), .Q(CNT_num), .clk(clock_2_out));  // open: load, D, carry, clr, preset
  assign CLK = nand_1_out ? clock_2_out : 1'bz;  // Controlled_Buffer controlled_buffer_1
  Pull_Resistor #(.pull(1)) pull_resistor_1 (.node(CLK));

  // Other names for the same wires on the sheet: MEM_PC[31:0] = M_PC

  // Notes on the sheet:
  //   中断源
  //   时空图监测，可删除
  //   中断等待指示
  //   数码管输出
  //   控制位
  //   流水调试日志用
  //   暂停节拍，不能为0
  //   戳工具置1进入计数暂停模式，ctrl+k时钟自动运行到对应节拍暂停
  //   ctrl+k关闭时钟连续运行，将控制位置零，进入单步调试模式调试
  //   用这个时钟源需要去掉电路中的其他时钟源
  //   可计数暂停的时钟源
  //   为方便自动评测，需要输出流水线各段保存的PC值，注意是PC不是PC+4，另外ID段寄存器写入信息，Mem段内存写入信息也要输出
endmodule

module \流水线_EX段分支  (
  output RegWrite,
  output MemWrite,
  output [31:0] IF_PC,
  output [31:0] ID_PC,
  output [31:0] EX_PC,
  output [31:0] M_PC,
  output [31:0] WB_PC,
  output [31:0] RDin,
  output [31:0] MDin,
  output [31:0] LedData
);

  wire and_2_out, and_3_out, and_4_out, and_5_out, and_6_out, Branch, CLK, clock_2_out, comparator_1_eq,
       comparator_1_lt, comparator_2_eq, controlled_buffer_1_out, d_ff_1_q, ecall, en, equal,
       ex_mem_1_haltout, ex_mem_1_jalout, ex_mem_1_jalrout, ex_mem_1_lhuout, ex_mem_1_regwriteout,
       ex_mem_1_u_tpyeout, Go, halt, id_ex_1_alusrcbout, id_ex_1_beqout, id_ex_1_bgeuout, id_ex_1_bneout,
       id_ex_1_ecallout, id_ex_1_lhuout, id_ex_1_memtoregout, id_ex_1_memwriteout, id_ex_1_regwriteout,
       id_ex_1_s_tpyeout, id_ex_1_u_tpyeout, IR1, IR2, IR3, Jal, Jalr, mem_wb_1_haltout, mem_wb_1_jalout,
       mem_wb_1_jalrout, mem_wb_1_lhuout, mem_wb_1_memtoregout, mem_wb_1_u_tpyeout, mem_wb_1_xout, MemToReg,
       MoreAndEqu, nand_1_out, not_1_out, not_2_out, not_3_out, not_4_out, or_1_out, or_2_out, or_3_out,
       or_5_out, RST, W1, W2, W3, \单周期硬布线控制器_1_alu_src , \单周期硬布线控制器_1_beq , \单周期硬布线控制器_1_bgeu ,
       \单周期硬布线控制器_1_bne , \单周期硬布线控制器_1_jal , \单周期硬布线控制器_1_jalr , \单周期硬布线控制器_1_lhu , \单周期硬布线控制器_1_memtoreg ,
       \单周期硬布线控制器_1_memwrite , \单周期硬布线控制器_1_regwrite , \单周期硬布线控制器_1_s_type , \单周期硬布线控制器_1_u_type ;
  wire [3:0] id_ex_1_aluopout, \单周期硬布线控制器_1_alu_op ;
  wire [4:0] ex_mem_1_w_out, id_ex_1_w_out, ID_Funct, multiplexer_4_out, multiplexer_5_out, W_num;
  wire [11:0] shifter_1_out;
  wire [12:0] CNT_num;
  wire [15:0] adder_4_out, \LoadUse次数 , multiplexer_8_out, \总周期数 , \插入气泡数 , \无条件分支数 , \条件分支成功数 ;
  wire [19:0] shifter_2_out;
  wire [31:0] adder_1_out, adder_2_out, adder_3_out, adder_5_out, and_1_out, bit_extender_1_out,
       bit_extender_2_out, bit_extender_3_out, bit_extender_4_out, bit_extender_5_out, EX_IR,
       ex_mem_1_imm_u_out, ex_mem_1_resultout, id_ex_1_imm_i_out, id_ex_1_imm_s_out, id_ex_1_imm_u_out,
       id_ex_1_r1out, id_ex_1_r2out, ID_IR, IF_IR, imm_B, imm_J, Jalr_Addr, MEM_IR, mem_wb_1_aluresultout,
       mem_wb_1_imm_u_out, mem_wb_1_rmdataout, multiplexer_1_out, multiplexer_2_out, multiplexer_3_out,
       multiplexer_6_out, multiplexer_7_out, multiplexer_9_out, multiplexer_10_out, multiplexer_11_out, R1,
       R2, ram_1_data, WB_IR, WB_PC_4;

  Button \u_总复位  (.out(RST));
  Button _1 (.out(IR1));
  Button _2 (.out(IR2));
  Button _3 (.out(IR3));
  // Probe on \总周期数 
  // Probe on \总周期数 
  Button \u_继续运行  (.out(Go));
  LED #(.active("true")) led_1 (.in(W1));
  LED #(.active("true")) led_2 (.in(W2));
  LED #(.active("true")) led_3 (.in(W3));
  Hex_Digit_Display hex_digit_display_1 (.value(LedData[31:28]));  // open: dp
  // Probe on IF_PC[19:0]
  // RiscV_Probe riscv_probe_1: pin names not known; wires that end beside it: IF_IR
  Hex_Digit_Display hex_digit_display_2 (.value(LedData[27:24]));  // open: dp
  Hex_Digit_Display hex_digit_display_3 (.value(LedData[23:20]));  // open: dp
  // Probe on ID_PC[19:0]
  // RiscV_Probe riscv_probe_2: pin names not known; wires that end beside it: {ID_IR[31], ID_Funct[4], ID_IR[29:26], ID_Funct[3], ID_IR[24:15], ID_Funct[2:0], ID_IR[11:0]}
  Adder #(.width(32)) adder_1 (.a(imm_J), .b(EX_PC), .out(adder_1_out));  // open: cin, cout
  assign and_1_out = Jalr_Addr & 32'hfffffffe;  // AND_Gate and_1, 32 bits wide
  Hex_Digit_Display hex_digit_display_4 (.value(LedData[15:12]));  // open: dp
  Hex_Digit_Display hex_digit_display_5 (.value(LedData[19:16]));  // open: dp
  Multiplexer #(.select(1), .width(32), .disabled("Z"), .enable("false")) multiplexer_1 (
    .in0(adder_3_out), .in1(adder_1_out), .out(multiplexer_1_out), .sel(Jal));
  Multiplexer #(.select(1), .width(32), .disabled("Z"), .enable("false")) multiplexer_2 (
    .in0(multiplexer_1_out), .in1(and_1_out), .out(multiplexer_2_out), .sel(Jalr));
  Adder #(.width(32)) adder_2 (.a(imm_B), .b(EX_PC), .out(adder_2_out));  // open: cin, cout
  Hex_Digit_Display hex_digit_display_6 (.value(LedData[7:4]));  // open: dp
  Hex_Digit_Display hex_digit_display_7 (.value(LedData[11:8]));  // open: dp
  Clock #(.highDuration(1), .lowDuration(1)) clock_1 (.out(CLK));
  // Probe on EX_PC[19:0]
  // RiscV_Probe riscv_probe_3: pin names not known; wires that end beside it: EX_IR
  Multiplexer #(.select(1), .width(32), .disabled("Z"), .enable("false")) multiplexer_3 (
    .in0(multiplexer_2_out), .in1(adder_2_out), .out(multiplexer_3_out), .sel(Branch));
  not not_1 (not_1_out, halt);
  Hex_Digit_Display hex_digit_display_8 (.value(LedData[3:0]));  // open: dp
  Register #(.width(32), .trigger("rising"), .Select("low")) PC (
    .D(multiplexer_3_out), .en(not_1_out), .Q(IF_PC), .clk(CLK), .clr(RST));
  // Probe on \总周期数 
  // Probe on M_PC[19:0]
  // RiscV_Probe riscv_probe_4: pin names not known; wires that end beside it: MEM_IR
  // Probe on \总周期数 
  // Probe on \无条件分支数 
  // Probe on \条件分支成功数 
  // Probe on \插入气泡数 
  // Probe on \LoadUse次数 
  Adder #(.width(32)) adder_3 (.a(IF_PC), .b(32'h4), .out(adder_3_out));  // open: cin, cout
  // Probe on IF_PC[11:0]
  // Probe on WB_PC[19:0]
  // RiscV_Probe riscv_probe_5: pin names not known; wires that end beside it: WB_IR
  ROM #(.addrWidth(10), .dataWidth(32), .Select("high")) rom_1 (.addr(IF_PC[11:2]), .data(IF_IR));
  // Probe on EX_PC[11:0]
  // Probe on ID_PC[11:0]
  IF_ID if_id_1 (
    .PCin(IF_PC), .IRin(IF_IR), .PCout(ID_PC),
    .IRout({ID_IR[31], ID_Funct[4], ID_IR[29:26], ID_Funct[3], ID_IR[24:15], ID_Funct[2:0], ID_IR[11:0]}),
    .RST(or_2_out), .EN_H(en), .CLK(CLK));  // open: PredictJumpin, PredictJumpout
  // Probe on M_PC[11:0]
  D_Flip_Flop #(.trigger("high"), .Pre_Clr_Positions("LEGACY"), .NegatePresetClear("false"), .enable("true"), .NewFFLayout("false")) d_ff_1 (.Q(d_ff_1_q));  // open: clk, D, Qn, preset, en, reset
  // Probe on 13'hc
  // Probe on WB_PC[11:0]
  Comparator #(.width(13), .mode("twosComplement")) comparator_1 (
    .a(CNT_num), .b(13'hc), .eq(comparator_1_eq), .lt(comparator_1_lt));  // open: gt
  Clock #(.highDuration(1), .lowDuration(1)) clock_2 (.out(clock_2_out));
  assign bit_extender_1_out = {{20{ID_IR[31]}}, {ID_IR[31], ID_Funct[4], ID_IR[29:26], ID_Funct[3], ID_IR[24:20]}};  // Bit_Extender bit_extender_1
  assign bit_extender_2_out = {{20{ID_IR[31]}}, {ID_IR[31], ID_Funct[4], ID_IR[29:26], ID_Funct[3], ID_IR[11:7]}};  // Bit_Extender bit_extender_2
  nand nand_1 (nand_1_out, d_ff_1_q, comparator_1_eq);
  Counter #(.width(13), .max('h1fff), .ongoal("stay"), .trigger("rising"), .behavior("old")) counter_1 (
    .count(comparator_1_lt), .Q(CNT_num), .clk(clock_2_out));  // open: load, D, carry, clr, preset
  \单周期硬布线控制器  \u_单周期硬布线控制器_1  (
    .Funct(ID_Funct), .OP(ID_IR[6:2]), .ALU_OP(\单周期硬布线控制器_1_alu_op ), .MemToReg(\单周期硬布线控制器_1_memtoreg ),
    .MemWrite(\单周期硬布线控制器_1_memwrite ), .ALU_SRC(\单周期硬布线控制器_1_alu_src ), .RegWrite(\单周期硬布线控制器_1_regwrite ),
    .ecall(ecall), .S_type(\单周期硬布线控制器_1_s_type ), .Jalr(\单周期硬布线控制器_1_jalr ), .Beq(\单周期硬布线控制器_1_beq ),
    .JAL(\单周期硬布线控制器_1_jal ), .Bne(\单周期硬布线控制器_1_bne ), .U_type(\单周期硬布线控制器_1_u_type ),
    .BGEU(\单周期硬布线控制器_1_bgeu ), .LHU(\单周期硬布线控制器_1_lhu ));  // open: URET, CSRRSI, CSRRCI
  Multiplexer #(.select(1), .width(5), .disabled("Z"), .enable("false")) multiplexer_4 (
    .in0(ID_IR[19:15]), .in1(5'b10001), .out(multiplexer_4_out), .sel(ecall));
  Multiplexer #(.select(1), .width(5), .disabled("Z"), .enable("false")) multiplexer_5 (
    .in0(ID_IR[24:20]), .in1(5'b01010), .out(multiplexer_5_out), .sel(ecall));
  Shifter #(.width(12), .shift("ll")) shifter_1 (
    .in({ID_IR[31], ID_IR[7], ID_Funct[4], ID_IR[29:26], ID_Funct[3], ID_IR[11:8]}), .\dist (4'b0001),
    .out(shifter_1_out));
  Shifter #(.width(20), .shift("ll")) shifter_2 (
    .in({ID_IR[31], ID_IR[19:15], ID_Funct[2:0], ID_IR[20], ID_Funct[4], ID_IR[29:26], ID_Funct[3], ID_IR[24:21]}),
    .\dist (5'b00001), .out(shifter_2_out));
  assign controlled_buffer_1_out = nand_1_out ? clock_2_out : 1'bz;  // Controlled_Buffer controlled_buffer_1
  assign bit_extender_3_out = {{20{shifter_1_out[11]}}, shifter_1_out};  // Bit_Extender bit_extender_3
  assign bit_extender_4_out = {{12{shifter_2_out[19]}}, shifter_2_out};  // Bit_Extender bit_extender_4
  Pull_Resistor #(.pull(1)) pull_resistor_1 (.node(controlled_buffer_1_out));
  Regifile regifile_1 (
    .Din(RDin), .Clk(CLK), .R1(R1), .R2(R2), .WE(RegWrite), .W_num(W_num), .R1_num(multiplexer_4_out),
    .R2_num(multiplexer_5_out));
  not not_2 (not_2_out, halt);
  Counter #(.width(16), .max('hffff), .ongoal("wrap"), .trigger("rising"), .behavior("new")) counter_2 (
    .count(not_2_out), .Q(\总周期数 ), .clk(CLK), .clr(RST));  // open: load, D, carry, preset, down
  Comparator #(.width(32), .mode("twosComplement")) comparator_2 (
    .a(R1), .b(32'ha), .eq(comparator_2_eq));  // open: gt, lt
  not not_3 (not_3_out, comparator_2_eq);
  or or_1 (or_1_out, Branch, Jal, Jalr);
  and and_2 (and_2_out, ecall, not_3_out);
  and and_3 (and_3_out, comparator_2_eq, ecall);
  Register #(.width(32), .trigger("rising"), .Select("low")) register_1 (
    .D(R2), .en(and_2_out), .Q(LedData), .clk(CLK), .clr(RST));
  Counter #(.width(16), .max('hffff), .ongoal("wrap"), .trigger("rising"), .behavior("new")) counter_3 (
    .count(Branch), .Q(\条件分支成功数 ), .clk(CLK), .clr(RST));  // open: load, D, carry, preset, down
  or or_2 (or_2_out, RST, or_1_out);
  ID_EX id_ex_1 (
    .PCin(ID_PC), .PCout(EX_PC),
    .IRin({ID_IR[31], ID_Funct[4], ID_IR[29:26], ID_Funct[3], ID_IR[24:15], ID_Funct[2:0], ID_IR[11:0]}),
    .IRout(EX_IR), .RST(or_2_out), .EN_H(en), .CLK(CLK), .Imm_I_in(bit_extender_1_out),
    .Imm_I_out(id_ex_1_imm_i_out), .Imm_S_in(bit_extender_2_out), .Imm_S_out(id_ex_1_imm_s_out),
    .Imm_B_in(bit_extender_3_out), .Imm_B_out(imm_B), .Imm_J_in(bit_extender_4_out), .Imm_J_out(imm_J),
    .Imm_U_in({ID_IR[31], ID_Funct[4], ID_IR[29:26], ID_Funct[3], ID_IR[24:15], ID_Funct[2:0], {12{1'b0}}}),
    .Imm_U_out(id_ex_1_imm_u_out), .R1in(R1), .R1out(id_ex_1_r1out), .R2in(R2), .R2out(id_ex_1_r2out),
    .Lhuin(\单周期硬布线控制器_1_lhu ), .Lhuout(id_ex_1_lhuout), .Jalrin(\单周期硬布线控制器_1_jalr ), .Jalrout(Jalr),
    .Jalout(Jal), .Jalin(\单周期硬布线控制器_1_jal ), .Beqin(\单周期硬布线控制器_1_beq ), .Beqout(id_ex_1_beqout),
    .Bgeuin(\单周期硬布线控制器_1_bgeu ), .Bgeuout(id_ex_1_bgeuout), .Bnein(\单周期硬布线控制器_1_bne ),
    .Bneout(id_ex_1_bneout), .MemToRegin(\单周期硬布线控制器_1_memtoreg ), .MemToRegout(id_ex_1_memtoregout),
    .MemWritein(\单周期硬布线控制器_1_memwrite ), .MemWriteout(id_ex_1_memwriteout),
    .AluSrcBin(\单周期硬布线控制器_1_alu_src ), .AluSrcBout(id_ex_1_alusrcbout), .RegWritein(\单周期硬布线控制器_1_regwrite ),
    .RegWriteout(id_ex_1_regwriteout), .U_Typein(\单周期硬布线控制器_1_u_type ), .U_Tpyeout(id_ex_1_u_tpyeout),
    .AluOpin(\单周期硬布线控制器_1_alu_op ), .AluOpout(id_ex_1_aluopout), .S_Typein(\单周期硬布线控制器_1_s_type ),
    .S_Tpyeout(id_ex_1_s_tpyeout), .Ecallin(and_3_out), .Ecallout(id_ex_1_ecallout), .W_in(ID_IR[11:7]),
    .W_out(id_ex_1_w_out));  // open: R1Forwardin, R1Forwardout, R2Forwardin, R2Forwardout, Uretin, Uretout, PredictJumpin, PredictJumpout
  Multiplexer #(.select(1), .width(32), .disabled("Z"), .enable("false")) multiplexer_6 (
    .in0(id_ex_1_imm_i_out), .in1(id_ex_1_imm_s_out), .out(multiplexer_6_out), .sel(id_ex_1_s_tpyeout));
  or or_3 (or_3_out, Jal, Jalr);
  Multiplexer #(.select(1), .width(32), .disabled("Z"), .enable("false")) multiplexer_7 (
    .in0(id_ex_1_r2out), .in1(multiplexer_6_out), .out(multiplexer_7_out), .sel(id_ex_1_alusrcbout));
  Counter #(.width(16), .max('hffff), .ongoal("wrap"), .trigger("rising"), .behavior("new")) counter_4 (
    .count(or_3_out), .Q(\无条件分支数 ), .clk(CLK), .clr(RST));  // open: load, D, carry, preset, down
  and and_4 (and_4_out, id_ex_1_beqout, equal);
  not not_4 (not_4_out, equal);
  and and_5 (and_5_out, not_4_out, id_ex_1_bneout);
  and and_6 (and_6_out, MoreAndEqu, id_ex_1_bgeuout);
  ALU alu_1 (
    .X(id_ex_1_r1out), .Y(multiplexer_7_out), .AluOP(id_ex_1_aluopout), .Equal(equal), .Result(Jalr_Addr),
    .out_4(MoreAndEqu));  // open: Result_2, out_6
  or or_4 (Branch, and_4_out, and_5_out, and_6_out);
  EX_MEM ex_mem_1 (
    .PCin(EX_PC), .Lhuin(id_ex_1_lhuout), .PCout(M_PC), .Lhuout(ex_mem_1_lhuout), .Jalrin(Jalr),
    .Jalrout(ex_mem_1_jalrout), .IRin(EX_IR), .IRout(MEM_IR), .Jalin(Jal), .Jalout(ex_mem_1_jalout),
    .MemToRegin(id_ex_1_memtoregout), .MemToRegout(MemToReg), .MemWritein(id_ex_1_memwriteout),
    .MemWriteout(MemWrite), .Imm_U_in(id_ex_1_imm_u_out), .Imm_U_out(ex_mem_1_imm_u_out),
    .Resultin(Jalr_Addr), .Resultout(ex_mem_1_resultout), .RegWritein(id_ex_1_regwriteout),
    .RegWriteout(ex_mem_1_regwriteout), .U_Typein(id_ex_1_u_tpyeout), .U_Tpyeout(ex_mem_1_u_tpyeout),
    .Haltin(id_ex_1_ecallout), .Haltout(ex_mem_1_haltout), .W_in(id_ex_1_w_out), .W_out(ex_mem_1_w_out),
    .RST(RST), .EN_H(en), .CLK(CLK), .WMdatain(id_ex_1_r2out), .WMdataout(MDin));  // open: Uretin, Uretout
  Adder #(.width(16)) adder_4 (.a(\无条件分支数 ), .b(\条件分支成功数 ), .out(adder_4_out));  // open: cin, cout
  Shifter #(.width(16), .shift("ll")) shifter_3 (.in(adder_4_out), .\dist (4'b0001), .out(\插入气泡数 ));
  RAM #(.addrWidth(10), .dataWidth(32), .bus("separate"), .Select("high")) ram_1 (
    .addr(ex_mem_1_resultout[11:2]), .din(MDin), .data(ram_1_data), .str(MemWrite), .clk(CLK), .ld(MemToReg),
    .clr(RST));  // open: sel
  MEM_WB mem_wb_1 (
    .Lhuin(ex_mem_1_lhuout), .PCin(M_PC), .Jalrin(ex_mem_1_jalrout), .Jalin(ex_mem_1_jalout), .IRin(MEM_IR),
    .MemToRegin(MemToReg), .Imm_U_in(ex_mem_1_imm_u_out), .RegWritein(ex_mem_1_regwriteout),
    .AluResultin(ex_mem_1_resultout), .U_Typein(ex_mem_1_u_tpyeout), .RMdatain(ram_1_data),
    .Haltin(ex_mem_1_haltout), .W_in(ex_mem_1_w_out), .Lhuout(mem_wb_1_lhuout), .PCout(WB_PC),
    .Jalrout(mem_wb_1_jalrout), .Jalout(mem_wb_1_jalout), .IRout(WB_IR), .MemToRegout(mem_wb_1_memtoregout),
    .Imm_U_out(mem_wb_1_imm_u_out), .RegWriteout(RegWrite), .AluResultout(mem_wb_1_aluresultout),
    .U_Tpyeout(mem_wb_1_u_tpyeout), .RMdataout(mem_wb_1_rmdataout), .Haltout(mem_wb_1_haltout),
    .W_out(W_num), .RST(RST), .EN_H(en), .CLK(CLK), .Xin(ex_mem_1_resultout[1]), .Xout(mem_wb_1_xout));  // open: Uretin, Uretout
  Multiplexer #(.select(1), .width(16), .disabled("Z"), .enable("false")) multiplexer_8 (
    .in0(mem_wb_1_rmdataout[15:0]), .in1(mem_wb_1_rmdataout[31:16]), .out(multiplexer_8_out),
    .sel(mem_wb_1_xout));
  Adder #(.width(32)) adder_5 (.a(WB_PC), .b(mem_wb_1_imm_u_out), .out(adder_5_out));  // open: cin, cout
  and and_7 (halt, mem_wb_1_haltout, ~Go);  // AND_Gate
  not not_5 (en, halt);
  Adder #(.width(32)) adder_6 (.a(32'h4), .b(WB_PC), .out(WB_PC_4));  // open: cin, cout
  or or_5 (or_5_out, mem_wb_1_jalrout, mem_wb_1_jalout, mem_wb_1_u_tpyeout);
  assign bit_extender_5_out = {{16{1'b0}}, multiplexer_8_out};  // Bit_Extender bit_extender_5
  Multiplexer #(.select(1), .width(32), .disabled("Z"), .enable("false")) multiplexer_9 (
    .in0(mem_wb_1_rmdataout), .in1(bit_extender_5_out), .out(multiplexer_9_out), .sel(mem_wb_1_lhuout));
  Multiplexer #(.select(1), .width(32), .disabled("Z"), .enable("false")) multiplexer_10 (
    .in0(WB_PC_4), .in1(adder_5_out), .out(multiplexer_10_out), .sel(mem_wb_1_u_tpyeout));
  Multiplexer #(.select(1), .width(32), .disabled("Z"), .enable("false")) multiplexer_11 (
    .in0(mem_wb_1_aluresultout), .in1(multiplexer_9_out), .out(multiplexer_11_out), .sel(mem_wb_1_memtoregout));
  Multiplexer #(.select(1), .width(32), .disabled("Z"), .enable("false")) multiplexer_12 (
    .in0(multiplexer_11_out), .in1(multiplexer_10_out), .out(RDin), .sel(or_5_out));

  // Other names for the same wires on the sheet: RD_num[4:0] = ID_IR[11:7]; ID_IR (some bits) = ID_Funct;
  //   ID_OP[4:0] = ID_IR[6:2]; MEM_PC[31:0] = M_PC; WriteBackData[31:0] = RDin

  // Notes on the sheet:
  //   中断源
  //   时空图监测，可删除
  //   中断等待指示
  //   数码管输出
  //   指令存储器
  //   指令字
  //   contents of rom_1 (hex, n*v repeats v):
  //   100493 100006f 100493 200913 300993 100006f 100493 200913 300993 100006f 100493 200913 300993
  //   100006f 100493 200913 300993 424000ef 100413 100493 1f49493 900533 2200893 73 24d493 48463 fedff06f
  //   900533 2200893 73 100493 249493 900533 2200893 73 48463 fedff06f 100493 1f49493 900533 2200893 73
  //   4034d493 900533 2200893 73 4044d493 900533 2200893 73 4044d493 900533 2200893 73 4044d493 900533
  //   2200893 73 4044d493 900533 2200893 73 4044d493 900533 2200893 73 4044d493 900533 2200893 73 4044d493
  //   900533 2200893 73 100413 1f41993 41f9d993 433 c00913 300b13 140413 f47413 800293 100313 499993
  //   89e9b3 1300533 2200893 73 406282b3 fe0294e3 140413 f00f93 1f47433 1c41413 800293 100313 49d993
  //   89e9b3 1300533 2200893 73 406282b3 fe0294e3 1c45413 406b0b33 b0463 f95ff06f 2b3 fff2c293 829293
  //   ff2e293 500533 2200893 73 fff00413 493 84a023 140413 448493 84a023 140413 448493 84a023 140413
  //   448493 84a023 140413 448493 84a023 140413 448493 84a023 140413 448493 84a023 140413 448493 84a023
  //   140413 448493 84a023 140413 448493 84a023 140413 448493 84a023 140413 448493 84a023 140413 448493
  //   84a023 140413 448493 84a023 140413 448493 84a023 140413 448493 84a023 140413 448493 140413 433
  //   3c00493 42983 4aa03 149a2b3 28663 134a023 1442023 ffc48493 fe9412e3 800533 2200893 73 440413 3c00493
  //   fc9416e3 a00893 73 100293 300313 800493 849493 7648493 1449493 900533 2200893 73 800e13 54d4b3
  //   64d4b3 900533 2200893 73 fffe0e13 fe0e14e3 a00893 73 13 430497 900533 2200893 73 430497 900533
  //   2200893 73 430497 900533 2200893 73 430497 900533 2200893 73 430497 900533 2200893 73 430497 900533
  //   2200893 73 430497 900533 2200893 73 430497 900533 2200893 73 a00893 73 313 1000e13 8400493 849493
  //   8348493 400913 891913 490913 849493 8248493 849493 8148493 891913 490913 891913 490913 932023
  //   12484b3 430313 fffe0e13 fe0e18e3 2000e13 313 35483 900533 2200893 73 230313 fffe0e13 fe0e14e3 a00893
  //   73 f00493 100913 409909b3 900533 2200893 73 fff48493 ff29f6e3 a00893 73 a00893 73 413 140413 800533
  //   2200893 73 240413 800533 2200893 73 340413 800533 2200893 73 440413 800533 2200893 73 540413 800533
  //   2200893 73 640413 800533 2200893 73 740413 800533 2200893 73 840413 800533 2200893 2200893 73 8067
  //   控制位
  //   流水调试日志用
  //   暂停节拍，不能为0
  //   rs1
  //   rs2
  //   rd
  //   戳工具置1进入计数暂停模式，ctrl+k时钟自动运行到对应节拍暂停
  //   ctrl+k关闭时钟连续运行，将控制位置零，进入单步调试模式调试
  //   Beq
  //   Bgeu
  //   Bne
  //   MemToReg
  //   MemWrite
  //   AluOP
  //   AluSrcB
  //   RegWrite
  //   U_Type
  //   S_Type
  //   可计数暂停的时钟源
  //   为方便自动评测，需要输出流水线各段保存的PC值，注意是PC不是PC+4，另外ID段寄存器写入信息，Mem段内存写入信息也要输出
  //   数据存储器
endmodule

// 寄存器有效信号判断
module \寄存器有效信号判断自动生成  (
  input  OP2,
  input  OP3,
  input  OP4,
  input  OP5,
  input  OP6,
  input  F12,
  input  F13,
  input  F14,
  input  F25,
  input  F30,
  output R1,
  output R2
);

  wire and_1_out, and_2_out, and_3_out, and_4_out, and_5_out, and_6_out, and_7_out, and_8_out, and_9_out,
       and_10_out, and_11_out, and_12_out, and_13_out, and_14_out, and_15_out, and_16_out, and_17_out,
       and_18_out, and_19_out, and_20_out, and_21_out, and_22_out, and_23_out, and_24_out, and_25_out,
       and_26_out, and_27_out, and_28_out, and_29_out, and_30_out, and_31_out, and_32_out, and_33_out,
       and_34_out, and_35_out, not_1_out, not_2_out, not_3_out, not_4_out, not_5_out, not_6_out, not_7_out,
       not_8_out, not_9_out, not_10_out, not_11_out, not_12_out, not_13_out, not_14_out, not_15_out,
       not_16_out, not_17_out, not_18_out, not_19_out, not_20_out, not_21_out, not_22_out, not_23_out,
       not_24_out, not_25_out, not_26_out, not_27_out, not_28_out, not_29_out, not_30_out, not_31_out,
       not_32_out, not_33_out, not_34_out, not_35_out, not_36_out, not_37_out, not_38_out, not_39_out,
       not_40_out, not_41_out, not_42_out, not_43_out, not_44_out, not_45_out, not_46_out, not_47_out,
       not_48_out, not_49_out, not_50_out, not_51_out, not_52_out, not_53_out, not_54_out, not_55_out,
       not_56_out, not_57_out, not_58_out, not_59_out, not_60_out, not_61_out, not_62_out, not_63_out,
       not_64_out, not_65_out, not_66_out, not_67_out, not_68_out, not_69_out, not_70_out, not_71_out,
       not_72_out, not_73_out, not_74_out, not_75_out, not_76_out, not_77_out, not_78_out, not_79_out,
       not_80_out, not_81_out, not_82_out, not_83_out, not_84_out, not_85_out, not_86_out, not_87_out,
       not_88_out, not_89_out, not_90_out, not_91_out, not_92_out, not_93_out, not_94_out, not_95_out,
       not_96_out, not_97_out, not_98_out, not_99_out, not_100_out, not_101_out, not_102_out, not_103_out,
       not_104_out, not_105_out, not_106_out, not_107_out, not_108_out, not_109_out, not_110_out,
       not_111_out, not_112_out, not_113_out, not_114_out, not_115_out, not_116_out, not_117_out,
       not_118_out, not_119_out, not_120_out, not_121_out, not_122_out, not_123_out, not_124_out,
       not_125_out, not_126_out, not_127_out, not_128_out, not_129_out, not_130_out, not_131_out,
       not_132_out, not_133_out, not_134_out, not_135_out, not_136_out, not_137_out, not_138_out,
       not_139_out, not_140_out, not_141_out, not_142_out, not_143_out, not_144_out, not_145_out,
       not_146_out, not_147_out, not_148_out, not_149_out, not_150_out, not_151_out, not_152_out,
       not_153_out, not_154_out, not_155_out, not_156_out, not_157_out, not_158_out, not_159_out,
       not_160_out, not_161_out, not_162_out, not_163_out, not_164_out, not_165_out, not_166_out,
       not_167_out, not_168_out, not_169_out, not_170_out, not_171_out, not_172_out, not_173_out,
       not_174_out, not_175_out, not_176_out, not_177_out, not_178_out, not_179_out, not_180_out,
       not_181_out, not_182_out, not_183_out, not_184_out, not_185_out, not_186_out, not_187_out,
       not_188_out, not_189_out, not_190_out, not_191_out, not_192_out, not_193_out, not_194_out,
       not_195_out, not_196_out, not_197_out, not_198_out, not_199_out, not_200_out, not_201_out,
       not_202_out, not_203_out, not_204_out, not_205_out, not_206_out, not_207_out, not_208_out,
       not_209_out, not_210_out, not_211_out;

  not not_1 (not_1_out, F30);
  not not_2 (not_2_out, F25);
  not not_3 (not_3_out, F14);
  not not_4 (not_4_out, F13);
  not not_5 (not_5_out, F12);
  not not_6 (not_6_out, OP6);
  not not_7 (not_7_out, OP3);
  not not_8 (not_8_out, OP2);
  not not_9 (not_9_out, F25);
  not not_10 (not_10_out, F14);
  not not_11 (not_11_out, F13);
  not not_12 (not_12_out, F12);
  not not_13 (not_13_out, OP6);
  not not_14 (not_14_out, OP3);
  not not_15 (not_15_out, OP2);
  not not_16 (not_16_out, F30);
  not not_17 (not_17_out, F25);
  not not_18 (not_18_out, OP6);
  not not_19 (not_19_out, OP3);
  not not_20 (not_20_out, OP2);
  not not_21 (not_21_out, F30);
  not not_22 (not_22_out, F25);
  not not_23 (not_23_out, F12);
  not not_24 (not_24_out, OP6);
  not not_25 (not_25_out, OP3);
  not not_26 (not_26_out, OP2);
  not not_27 (not_27_out, F30);
  not not_28 (not_28_out, F25);
  not not_29 (not_29_out, F14);
  not not_30 (not_30_out, F12);
  not not_31 (not_31_out, OP6);
  not not_32 (not_32_out, OP3);
  not not_33 (not_33_out, OP2);
  not not_34 (not_34_out, F30);
  not not_35 (not_35_out, F25);
  not not_36 (not_36_out, F14);
  not not_37 (not_37_out, OP6);
  not not_38 (not_38_out, OP3);
  not not_39 (not_39_out, OP2);
  not not_40 (not_40_out, F14);
  not not_41 (not_41_out, F13);
  not not_42 (not_42_out, F12);
  not not_43 (not_43_out, OP6);
  not not_44 (not_44_out, OP5);
  not not_45 (not_45_out, OP3);
  not not_46 (not_46_out, OP2);
  not not_47 (not_47_out, OP6);
  not not_48 (not_48_out, OP5);
  not not_49 (not_49_out, OP3);
  not not_50 (not_50_out, OP2);
  not not_51 (not_51_out, F12);
  not not_52 (not_52_out, OP6);
  not not_53 (not_53_out, OP5);
  not not_54 (not_54_out, OP3);
  not not_55 (not_55_out, OP2);
  not not_56 (not_56_out, F13);
  not not_57 (not_57_out, F12);
  not not_58 (not_58_out, OP6);
  not not_59 (not_59_out, OP5);
  not not_60 (not_60_out, OP3);
  not not_61 (not_61_out, OP2);
  not not_62 (not_62_out, F14);
  not not_63 (not_63_out, F12);
  not not_64 (not_64_out, OP6);
  not not_65 (not_65_out, OP5);
  not not_66 (not_66_out, OP3);
  not not_67 (not_67_out, OP2);
  not not_68 (not_68_out, F30);
  not not_69 (not_69_out, F25);
  not not_70 (not_70_out, F14);
  not not_71 (not_71_out, F13);
  not not_72 (not_72_out, OP6);
  not not_73 (not_73_out, OP5);
  not not_74 (not_74_out, OP3);
  not not_75 (not_75_out, OP2);
  not not_76 (not_76_out, F30);
  not not_77 (not_77_out, F25);
  not not_78 (not_78_out, F13);
  not not_79 (not_79_out, OP6);
  not not_80 (not_80_out, OP5);
  not not_81 (not_81_out, OP3);
  not not_82 (not_82_out, OP2);
  not not_83 (not_83_out, F25);
  not not_84 (not_84_out, F13);
  not not_85 (not_85_out, OP6);
  not not_86 (not_86_out, OP5);
  not not_87 (not_87_out, OP3);
  not not_88 (not_88_out, OP2);
  not not_89 (not_89_out, F14);
  not not_90 (not_90_out, F12);
  not not_91 (not_91_out, OP6);
  not not_92 (not_92_out, OP5);
  not not_93 (not_93_out, OP4);
  not not_94 (not_94_out, OP3);
  not not_95 (not_95_out, OP2);
  not not_96 (not_96_out, F14);
  not not_97 (not_97_out, F12);
  not not_98 (not_98_out, OP6);
  not not_99 (not_99_out, OP4);
  not not_100 (not_100_out, OP3);
  not not_101 (not_101_out, OP2);
  not not_102 (not_102_out, F30);
  not not_103 (not_103_out, F25);
  not not_104 (not_104_out, F14);
  not not_105 (not_105_out, F13);
  not not_106 (not_106_out, F12);
  not not_107 (not_107_out, OP3);
  not not_108 (not_108_out, OP2);
  not not_109 (not_109_out, F14);
  not not_110 (not_110_out, F13);
  not not_111 (not_111_out, F12);
  not not_112 (not_112_out, OP4);
  not not_113 (not_113_out, OP3);
  not not_114 (not_114_out, OP2);
  not not_115 (not_115_out, F14);
  not not_116 (not_116_out, F13);
  not not_117 (not_117_out, OP4);
  not not_118 (not_118_out, OP3);
  not not_119 (not_119_out, OP2);
  not not_120 (not_120_out, F14);
  not not_121 (not_121_out, F13);
  not not_122 (not_122_out, F12);
  not not_123 (not_123_out, OP4);
  not not_124 (not_124_out, OP3);
  not not_125 (not_125_out, F30);
  not not_126 (not_126_out, F25);
  not not_127 (not_127_out, F13);
  not not_128 (not_128_out, OP6);
  not not_129 (not_129_out, OP3);
  not not_130 (not_130_out, OP2);
  not not_131 (not_131_out, F13);
  not not_132 (not_132_out, OP6);
  not not_133 (not_133_out, OP5);
  not not_134 (not_134_out, OP4);
  not not_135 (not_135_out, OP3);
  not not_136 (not_136_out, OP2);
  not not_137 (not_137_out, OP4);
  not not_138 (not_138_out, OP3);
  not not_139 (not_139_out, OP2);
  not not_140 (not_140_out, F30);
  not not_141 (not_141_out, F25);
  not not_142 (not_142_out, F14);
  not not_143 (not_143_out, F13);
  not not_144 (not_144_out, F12);
  not not_145 (not_145_out, OP6);
  not not_146 (not_146_out, OP3);
  not not_147 (not_147_out, OP2);
  not not_148 (not_148_out, F25);
  not not_149 (not_149_out, F14);
  not not_150 (not_150_out, F13);
  not not_151 (not_151_out, F12);
  not not_152 (not_152_out, OP6);
  not not_153 (not_153_out, OP3);
  not not_154 (not_154_out, OP2);
  not not_155 (not_155_out, F30);
  not not_156 (not_156_out, F25);
  not not_157 (not_157_out, OP6);
  not not_158 (not_158_out, OP3);
  not not_159 (not_159_out, OP2);
  not not_160 (not_160_out, F30);
  not not_161 (not_161_out, F25);
  not not_162 (not_162_out, F12);
  not not_163 (not_163_out, OP6);
  not not_164 (not_164_out, OP3);
  not not_165 (not_165_out, OP2);
  not not_166 (not_166_out, F30);
  not not_167 (not_167_out, F25);
  not not_168 (not_168_out, F14);
  not not_169 (not_169_out, F12);
  not not_170 (not_170_out, OP6);
  not not_171 (not_171_out, OP3);
  not not_172 (not_172_out, OP2);
  not not_173 (not_173_out, F30);
  not not_174 (not_174_out, F25);
  not not_175 (not_175_out, F14);
  not not_176 (not_176_out, OP6);
  not not_177 (not_177_out, OP3);
  not not_178 (not_178_out, OP2);
  not not_179 (not_179_out, F14);
  not not_180 (not_180_out, F12);
  not not_181 (not_181_out, OP6);
  not not_182 (not_182_out, OP4);
  not not_183 (not_183_out, OP3);
  not not_184 (not_184_out, OP2);
  not not_185 (not_185_out, F30);
  not not_186 (not_186_out, F25);
  not not_187 (not_187_out, F14);
  not not_188 (not_188_out, F13);
  not not_189 (not_189_out, F12);
  not not_190 (not_190_out, OP3);
  not not_191 (not_191_out, OP2);
  not not_192 (not_192_out, F14);
  not not_193 (not_193_out, F13);
  not not_194 (not_194_out, F12);
  not not_195 (not_195_out, OP4);
  not not_196 (not_196_out, OP3);
  not not_197 (not_197_out, OP2);
  not not_198 (not_198_out, F14);
  not not_199 (not_199_out, F13);
  not not_200 (not_200_out, OP4);
  not not_201 (not_201_out, OP3);
  not not_202 (not_202_out, OP2);
  not not_203 (not_203_out, F30);
  not not_204 (not_204_out, F25);
  not not_205 (not_205_out, F13);
  not not_206 (not_206_out, OP6);
  not not_207 (not_207_out, OP3);
  not not_208 (not_208_out, OP2);
  not not_209 (not_209_out, OP4);
  not not_210 (not_210_out, OP3);
  not not_211 (not_211_out, OP2);
  and and_1 (and_1_out, not_1_out, not_2_out, not_3_out, not_4_out, not_5_out, not_6_out, OP5, OP4, not_7_out, not_8_out);
  and and_2 (and_2_out, F30, not_9_out, not_10_out, not_11_out, not_12_out, not_13_out, OP5, OP4, not_14_out, not_15_out);
  and and_3 (and_3_out, not_16_out, not_17_out, F14, F13, F12, not_18_out, OP5, OP4, not_19_out, not_20_out);
  and and_4 (and_4_out, not_21_out, not_22_out, F14, F13, not_23_out, not_24_out, OP5, OP4, not_25_out, not_26_out);
  and and_5 (and_5_out, not_27_out, not_28_out, not_29_out, F13, not_30_out, not_31_out, OP5, OP4, not_32_out, not_33_out);
  and and_6 (and_6_out, not_34_out, not_35_out, not_36_out, F13, F12, not_37_out, OP5, OP4, not_38_out, not_39_out);
  and and_7 (and_7_out, not_40_out, not_41_out, not_42_out, not_43_out, not_44_out, OP4, not_45_out, not_46_out);
  and and_8 (and_8_out, F14, F13, F12, not_47_out, not_48_out, OP4, not_49_out, not_50_out);
  and and_9 (and_9_out, F14, F13, not_51_out, not_52_out, not_53_out, OP4, not_54_out, not_55_out);
  and and_10 (and_10_out, F14, not_56_out, not_57_out, not_58_out, not_59_out, OP4, not_60_out, not_61_out);
  and and_11 (and_11_out, not_62_out, F13, not_63_out, not_64_out, not_65_out, OP4, not_66_out, not_67_out);
  and and_12 (and_12_out, not_68_out, not_69_out, not_70_out, not_71_out, F12, not_72_out, not_73_out, OP4, not_74_out, not_75_out);
  and and_13 (and_13_out, not_76_out, not_77_out, F14, not_78_out, F12, not_79_out, not_80_out, OP4, not_81_out, not_82_out);
  and and_14 (and_14_out, F30, not_83_out, F14, not_84_out, F12, not_85_out, not_86_out, OP4, not_87_out, not_88_out);
  and and_15 (and_15_out, not_89_out, F13, not_90_out, not_91_out, not_92_out, not_93_out, not_94_out, not_95_out);
  and and_16 (and_16_out, not_96_out, F13, not_97_out, not_98_out, OP5, not_99_out, not_100_out, not_101_out);
  and and_17 (and_17_out, not_102_out, not_103_out, not_104_out, not_105_out, not_106_out, OP6, OP5, OP4, not_107_out, not_108_out);
  and and_18 (and_18_out, not_109_out, not_110_out, not_111_out, OP6, OP5, not_112_out, not_113_out, not_114_out);
  and and_19 (and_19_out, not_115_out, not_116_out, F12, OP6, OP5, not_117_out, not_118_out, not_119_out);
  and and_20 (and_20_out, not_120_out, not_121_out, not_122_out, OP6, OP5, not_123_out, not_124_out, OP2);
  and and_21 (and_21_out, not_125_out, not_126_out, F14, not_127_out, F12, not_128_out, OP5, OP4, not_129_out, not_130_out);
  and and_22 (and_22_out, F14, not_131_out, F12, not_132_out, not_133_out, not_134_out, not_135_out, not_136_out);
  and and_23 (and_23_out, F14, F13, F12, OP6, OP5, not_137_out, not_138_out, not_139_out);
  and and_24 (and_24_out, not_140_out, not_141_out, not_142_out, not_143_out, not_144_out, not_145_out, OP5, OP4, not_146_out, not_147_out);
  and and_25 (and_25_out, F30, not_148_out, not_149_out, not_150_out, not_151_out, not_152_out, OP5, OP4, not_153_out, not_154_out);
  and and_26 (and_26_out, not_155_out, not_156_out, F14, F13, F12, not_157_out, OP5, OP4, not_158_out, not_159_out);
  and and_27 (and_27_out, not_160_out, not_161_out, F14, F13, not_162_out, not_163_out, OP5, OP4, not_164_out, not_165_out);
  and and_28 (and_28_out, not_166_out, not_167_out, not_168_out, F13, not_169_out, not_170_out, OP5, OP4, not_171_out, not_172_out);
  and and_29 (and_29_out, not_173_out, not_174_out, not_175_out, F13, F12, not_176_out, OP5, OP4, not_177_out, not_178_out);
  and and_30 (and_30_out, not_179_out, F13, not_180_out, not_181_out, OP5, not_182_out, not_183_out, not_184_out);
  and and_31 (and_31_out, not_185_out, not_186_out, not_187_out, not_188_out, not_189_out, OP6, OP5, OP4, not_190_out, not_191_out);
  and and_32 (and_32_out, not_192_out, not_193_out, not_194_out, OP6, OP5, not_195_out, not_196_out, not_197_out);
  and and_33 (and_33_out, not_198_out, not_199_out, F12, OP6, OP5, not_200_out, not_201_out, not_202_out);
  and and_34 (and_34_out, not_203_out, not_204_out, F14, not_205_out, F12, not_206_out, OP5, OP4, not_207_out, not_208_out);
  and and_35 (and_35_out, F14, F13, F12, OP6, OP5, not_209_out, not_210_out, not_211_out);
  or or_1 (R2, and_24_out, and_25_out, and_26_out, and_27_out, and_28_out, and_29_out, and_30_out, and_31_out, and_32_out, and_33_out, and_34_out, and_35_out);
  or or_2 (R1, and_1_out, and_2_out, and_3_out, and_4_out, and_5_out, and_6_out, and_7_out, and_8_out, and_9_out, and_10_out, and_11_out, and_12_out, and_13_out, and_14_out, and_15_out, and_16_out, and_17_out, and_18_out, and_19_out, and_20_out, and_21_out, and_22_out, and_23_out);
endmodule

// 数据冲突处理逻辑-气泡
module \数据冲突处理逻辑_气泡  (
  input  [4:0] ID_R1_num,
  input  [4:0] EX_W_num,
  input  EX_RegWrite,
  input  [4:0] ID_R2_num,
  input  [4:0] MEM_W_num,
  input  MEM_RegWrite,
  input  [4:0] OP,
  input  [4:0] Funct,
  output \数据相关 
);

  wire and_1_out, and_2_out, and_3_out, and_4_out, and_5_out, and_6_out, comparator_1_eq, comparator_2_eq,
       comparator_3_eq, comparator_4_eq, comparator_5_eq, comparator_6_eq, comparator_7_eq, comparator_8_eq,
       or_1_out, or_2_out, \寄存器有效信号判断自动生成_1_r1 , \寄存器有效信号判断自动生成_1_r2 ;

  \寄存器有效信号判断自动生成  \u_寄存器有效信号判断自动生成_1  (
    .OP2(OP[0]), .OP3(OP[1]), .OP4(OP[2]), .OP5(OP[3]), .OP6(OP[4]), .F12(Funct[0]), .F13(Funct[1]),
    .F14(Funct[2]), .F25(Funct[3]), .F30(Funct[4]), .R1(\寄存器有效信号判断自动生成_1_r1 ), .R2(\寄存器有效信号判断自动生成_1_r2 ));
  Comparator #(.width(5), .mode("twosComplement")) comparator_1 (
    .a(ID_R1_num), .b(EX_W_num), .eq(comparator_1_eq));  // open: gt, lt
  Comparator #(.width(5), .mode("twosComplement")) comparator_2 (
    .a(EX_W_num), .b({5{1'b0}}), .eq(comparator_2_eq));  // open: gt, lt
  Comparator #(.width(5), .mode("twosComplement")) comparator_3 (
    .a(ID_R2_num), .b(EX_W_num), .eq(comparator_3_eq));  // open: gt, lt
  Comparator #(.width(5), .mode("twosComplement")) comparator_4 (
    .a(EX_W_num), .b({5{1'b0}}), .eq(comparator_4_eq));  // open: gt, lt
  and and_1 (and_1_out, comparator_1_eq, EX_RegWrite, ~comparator_2_eq);  // AND_Gate
  and and_2 (and_2_out, comparator_3_eq, EX_RegWrite, ~comparator_4_eq);  // AND_Gate
  Comparator #(.width(5), .mode("twosComplement")) comparator_5 (
    .a(ID_R1_num), .b(MEM_W_num), .eq(comparator_5_eq));  // open: gt, lt
  Comparator #(.width(5), .mode("twosComplement")) comparator_6 (
    .a(MEM_W_num), .b({5{1'b0}}), .eq(comparator_6_eq));  // open: gt, lt
  Comparator #(.width(5), .mode("twosComplement")) comparator_7 (
    .a(ID_R2_num), .b(MEM_W_num), .eq(comparator_7_eq));  // open: gt, lt
  Comparator #(.width(5), .mode("twosComplement")) comparator_8 (
    .a(MEM_W_num), .b({5{1'b0}}), .eq(comparator_8_eq));  // open: gt, lt
  and and_3 (and_3_out, comparator_5_eq, MEM_RegWrite, ~comparator_6_eq);  // AND_Gate
  and and_4 (and_4_out, comparator_7_eq, MEM_RegWrite, ~comparator_8_eq);  // AND_Gate
  or or_1 (or_1_out, and_3_out, and_1_out);
  or or_2 (or_2_out, and_2_out, and_4_out);
  and and_5 (and_5_out, or_1_out, \寄存器有效信号判断自动生成_1_r1 );
  and and_6 (and_6_out, \寄存器有效信号判断自动生成_1_r2 , or_2_out);
  or or_3 (\数据相关 , and_5_out, and_6_out);
endmodule

// 数据冲突处理逻辑-重定向
module \数据冲突处理逻辑_重定向  (
  input  [4:0] ID_R1_num,
  input  [4:0] EX_W_num,
  input  EX_RegWrite,
  input  [4:0] EX_OP,
  input  [4:0] ID_R2_num,
  input  [4:0] MEM_W_num,
  input  MEM_RegWrite,
  input  [4:0] ID_OP,
  input  [4:0] ID_Funct,
  output \数据相关 ,
  output [1:0] R1Forward,
  output Load_Use,
  output [1:0] R2Forward
);

  wire and_3_out, and_4_out, and_5_out, and_6_out, and_9_out, and_10_out, and_11_out, and_12_out,
       comparator_1_eq, comparator_2_eq, comparator_3_eq, comparator_4_eq, comparator_5_eq, comparator_6_eq,
       comparator_7_eq, comparator_8_eq, comparator_9_eq, comparator_10_eq, \EX_R1冲突 , \EX_R2冲突 , \MEM_R1冲突 ,
       \MEM_R2冲突 , or_1_out, or_2_out, or_4_out, or_5_out, \R1使用 , \R2使用 ;

  \寄存器有效信号判断自动生成  \u_寄存器有效信号判断自动生成_1  (
    .OP2(ID_OP[0]), .OP3(ID_OP[1]), .OP4(ID_OP[2]), .OP5(ID_OP[3]), .OP6(ID_OP[4]), .F12(ID_Funct[0]),
    .F13(ID_Funct[1]), .F14(ID_Funct[2]), .F25(ID_Funct[3]), .F30(ID_Funct[4]), .R1(\R1使用 ), .R2(\R2使用 ));
  Comparator #(.width(5), .mode("twosComplement")) comparator_1 (
    .a(ID_R1_num), .b(EX_W_num), .eq(comparator_1_eq));  // open: gt, lt
  Comparator #(.width(5), .mode("twosComplement")) comparator_2 (
    .a(EX_W_num), .b({5{1'b0}}), .eq(comparator_2_eq));  // open: gt, lt
  Comparator #(.width(5), .mode("twosComplement")) comparator_3 (
    .a(ID_R2_num), .b(EX_W_num), .eq(comparator_3_eq));  // open: gt, lt
  Comparator #(.width(5), .mode("twosComplement")) comparator_4 (
    .a(EX_W_num), .b({5{1'b0}}), .eq(comparator_4_eq));  // open: gt, lt
  and and_1 (\EX_R1冲突 , comparator_1_eq, EX_RegWrite, ~comparator_2_eq);  // AND_Gate
  and and_2 (\EX_R2冲突 , comparator_3_eq, EX_RegWrite, ~comparator_4_eq);  // AND_Gate
  and and_3 (and_3_out, \R1使用 , \MEM_R1冲突 );
  and and_4 (and_4_out, \R1使用 , \EX_R1冲突 );
  and and_5 (and_5_out, \R2使用 , \MEM_R2冲突 );
  and and_6 (and_6_out, \R2使用 , \EX_R2冲突 );
  Priority_Encoder #(.select(2), .disabled("Z")) priority_encoder_1 (
    .in0(1'b1), .in1(and_3_out), .in2(and_4_out), .out(R1Forward));  // open: in3, gs, en_out, en_in
  Priority_Encoder #(.select(2), .disabled("Z")) priority_encoder_2 (
    .in0(1'b1), .in1(and_5_out), .in2(and_6_out), .out(R2Forward));  // open: in3, gs, en_out, en_in
  Comparator #(.width(5), .mode("twosComplement")) comparator_5 (
    .a(ID_R1_num), .b(MEM_W_num), .eq(comparator_5_eq));  // open: gt, lt
  Comparator #(.width(5), .mode("twosComplement")) comparator_6 (
    .a(MEM_W_num), .b({5{1'b0}}), .eq(comparator_6_eq));  // open: gt, lt
  Comparator #(.width(5), .mode("twosComplement")) comparator_7 (
    .a(ID_R2_num), .b(MEM_W_num), .eq(comparator_7_eq));  // open: gt, lt
  Comparator #(.width(5), .mode("twosComplement")) comparator_8 (
    .a(MEM_W_num), .b({5{1'b0}}), .eq(comparator_8_eq));  // open: gt, lt
  and and_7 (\MEM_R1冲突 , comparator_5_eq, MEM_RegWrite, ~comparator_6_eq);  // AND_Gate
  and and_8 (\MEM_R2冲突 , comparator_7_eq, MEM_RegWrite, ~comparator_8_eq);  // AND_Gate
  or or_1 (or_1_out, \MEM_R1冲突 , \EX_R1冲突 );
  or or_2 (or_2_out, \EX_R2冲突 , \MEM_R2冲突 );
  and and_9 (and_9_out, or_1_out, \R1使用 );
  and and_10 (and_10_out, \R2使用 , or_2_out);
  and and_11 (and_11_out, \R1使用 , \EX_R1冲突 );
  and and_12 (and_12_out, \EX_R2冲突 , \R2使用 );
  Comparator #(.width(5), .mode("twosComplement")) comparator_9 (
    .a(EX_OP), .b({5{1'b0}}), .eq(comparator_9_eq));  // open: gt, lt
  Comparator #(.width(5), .mode("twosComplement")) comparator_10 (
    .a(EX_OP), .b(5'b00101), .eq(comparator_10_eq));  // open: gt, lt
  or or_3 (\数据相关 , and_9_out, and_10_out);
  or or_4 (or_4_out, and_11_out, and_12_out);
  or or_5 (or_5_out, comparator_9_eq, comparator_10_eq);
  and and_13 (Load_Use, or_4_out, or_5_out);

  // Notes on the sheet:
  //   lw、lhu
  //   auipc
endmodule
module \气泡流水线  (
  output RegWrite,
  output MemWrite,
  output [31:0] IF_PC,
  output [31:0] ID_PC,
  output [31:0] EX_PC,
  output [31:0] M_PC,
  output [31:0] WB_PC,
  output [31:0] RDin,
  output [31:0] MDin,
  output [31:0] LedData
);

  wire and_2_out, and_3_out, and_4_out, and_5_out, and_6_out, and_7_out, and_8_out, and_9_out, Branch, CLK,
       clock_2_out, comparator_1_eq, comparator_1_lt, comparator_2_eq, controlled_buffer_1_out, d_ff_1_q, en,
       equal, ex_mem_1_haltout, ex_mem_1_jalout, ex_mem_1_jalrout, ex_mem_1_lhuout, ex_mem_1_u_tpyeout,
       EX_RegWrite_num, Go, halt, ID_ecall, id_ex_1_alusrcbout, id_ex_1_beqout, id_ex_1_bgeuout,
       id_ex_1_bneout, id_ex_1_ecallout, id_ex_1_lhuout, id_ex_1_memtoregout, id_ex_1_memwriteout,
       id_ex_1_s_tpyeout, id_ex_1_u_tpyeout, IR1, IR2, IR3, Jal, Jalr, MEM_RegWrite_num, mem_wb_1_haltout,
       mem_wb_1_jalout, mem_wb_1_jalrout, mem_wb_1_lhuout, mem_wb_1_memtoregout, mem_wb_1_u_tpyeout,
       mem_wb_1_xout, MemToReg, MoreAndEqu, nand_1_out, not_1_out, not_2_out, not_3_out, not_4_out,
       not_5_out, not_6_out, not_7_out, not_8_out, or_1_out, or_2_out, or_3_out, or_4_out, or_6_out, RST, W1,
       W2, W3, \单周期硬布线控制器_1_alu_src , \单周期硬布线控制器_1_beq , \单周期硬布线控制器_1_bgeu , \单周期硬布线控制器_1_bne ,
       \单周期硬布线控制器_1_jal , \单周期硬布线控制器_1_jalr , \单周期硬布线控制器_1_lhu , \单周期硬布线控制器_1_memtoreg ,
       \单周期硬布线控制器_1_memwrite , \单周期硬布线控制器_1_regwrite , \单周期硬布线控制器_1_s_type , \单周期硬布线控制器_1_u_type , \数据相关 ;
  wire [3:0] id_ex_1_aluopout, \单周期硬布线控制器_1_alu_op ;
  wire [4:0] EX_W_num, ID_Funct, ID_R1_num, ID_R2_num, MEM_W_num, W_num;
  wire [11:0] shifter_1_out;
  wire [12:0] CNT_num;
  wire [15:0] \LoadUse次数 , multiplexer_8_out, \总周期数 , \插入气泡数 , \无条件分支数 , \条件分支成功数 ;
  wire [19:0] shifter_2_out;
  wire [31:0] adder_1_out, adder_2_out, adder_3_out, adder_4_out, and_1_out, bit_extender_1_out,
       bit_extender_2_out, bit_extender_3_out, bit_extender_4_out, bit_extender_5_out, EX_IR,
       ex_mem_1_imm_u_out, ex_mem_1_resultout, id_ex_1_imm_i_out, id_ex_1_imm_s_out, id_ex_1_imm_u_out,
       id_ex_1_r1out, id_ex_1_r2out, ID_IR, IF_IR, imm_B, imm_J, Jalr_Addr, MEM_IR, mem_wb_1_aluresultout,
       mem_wb_1_imm_u_out, mem_wb_1_rmdataout, multiplexer_1_out, multiplexer_2_out, multiplexer_3_out,
       multiplexer_6_out, multiplexer_7_out, multiplexer_9_out, multiplexer_10_out, multiplexer_11_out, R1,
       R2, ram_1_data, WB_IR, WB_PC_4;

  Button \u_总复位  (.out(RST));
  Button _1 (.out(IR1));
  Button _2 (.out(IR2));
  Button _3 (.out(IR3));
  // Probe on \总周期数 
  // Probe on \总周期数 
  Button \u_继续运行  (.out(Go));
  LED #(.active("true")) led_1 (.in(W1));
  LED #(.active("true")) led_2 (.in(W2));
  LED #(.active("true")) led_3 (.in(W3));
  Hex_Digit_Display hex_digit_display_1 (.value(LedData[31:28]));  // open: dp
  // Probe on IF_PC[19:0]
  // RiscV_Probe riscv_probe_1: pin names not known; wires that end beside it: IF_IR
  Hex_Digit_Display hex_digit_display_2 (.value(LedData[23:20]));  // open: dp
  Hex_Digit_Display hex_digit_display_3 (.value(LedData[27:24]));  // open: dp
  // Probe on ID_PC[19:0]
  // RiscV_Probe riscv_probe_2: pin names not known; wires that end beside it: {ID_IR[31], ID_Funct[4], ID_IR[29:26], ID_Funct[3], ID_IR[24:15], ID_Funct[2:0], ID_IR[11:0]}
  Multiplexer #(.select(1), .width(32), .disabled("Z"), .enable("false")) multiplexer_1 (
    .in0(adder_3_out), .in1(adder_1_out), .out(multiplexer_1_out), .sel(Jal));
  Adder #(.width(32)) adder_1 (.a(imm_J), .b(EX_PC), .out(adder_1_out));  // open: cin, cout
  assign and_1_out = Jalr_Addr & 32'hfffffffe;  // AND_Gate and_1, 32 bits wide
  Hex_Digit_Display hex_digit_display_4 (.value(LedData[15:12]));  // open: dp
  Hex_Digit_Display hex_digit_display_5 (.value(LedData[19:16]));  // open: dp
  \数据冲突处理逻辑_气泡  \u_数据冲突处理逻辑_气泡_1  (
    .ID_R1_num(ID_R1_num), .EX_W_num(EX_W_num), .EX_RegWrite(EX_RegWrite_num), .ID_R2_num(ID_R2_num),
    .MEM_W_num(MEM_W_num), .MEM_RegWrite(MEM_RegWrite_num), .OP(ID_IR[6:2]), .Funct(ID_Funct), .\数据相关 (\数据相关 ));
  Multiplexer #(.select(1), .width(32), .disabled("Z"), .enable("false")) multiplexer_2 (
    .in0(multiplexer_1_out), .in1(and_1_out), .out(multiplexer_2_out), .sel(Jalr));
  Adder #(.width(32)) adder_2 (.a(imm_B), .b(EX_PC), .out(adder_2_out));  // open: cin, cout
  Hex_Digit_Display hex_digit_display_6 (.value(LedData[7:4]));  // open: dp
  Hex_Digit_Display hex_digit_display_7 (.value(LedData[11:8]));  // open: dp
  Clock #(.highDuration(1), .lowDuration(1)) clock_1 (.out(CLK));
  // Probe on EX_PC[19:0]
  // RiscV_Probe riscv_probe_3: pin names not known; wires that end beside it: EX_IR
  Multiplexer #(.select(1), .width(32), .disabled("Z"), .enable("false")) multiplexer_3 (
    .in0(multiplexer_2_out), .in1(adder_2_out), .out(multiplexer_3_out), .sel(Branch));
  and and_2 (and_2_out, not_2_out, not_1_out);
  not not_1 (not_1_out, halt);
  not not_2 (not_2_out, \数据相关 );
  Hex_Digit_Display hex_digit_display_8 (.value(LedData[3:0]));  // open: dp
  Register #(.width(32), .trigger("rising"), .Select("low")) PC (
    .D(multiplexer_3_out), .en(and_2_out), .Q(IF_PC), .clk(CLK), .clr(RST));
  // Probe on \总周期数 
  // Probe on M_PC[19:0]
  // RiscV_Probe riscv_probe_4: pin names not known; wires that end beside it: MEM_IR
  // Probe on \总周期数 
  // Probe on \无条件分支数 
  // Probe on \条件分支成功数 
  // Probe on \插入气泡数 
  // Probe on \LoadUse次数 
  Adder #(.width(32)) adder_3 (.a(IF_PC), .b(32'h4), .out(adder_3_out));  // open: cin, cout
  // Probe on IF_PC[11:0]
  // Probe on WB_PC[19:0]
  // RiscV_Probe riscv_probe_5: pin names not known; wires that end beside it: WB_IR
  or or_1 (or_1_out, Branch, Jal, Jalr);
  ROM #(.addrWidth(10), .dataWidth(32), .Select("high")) rom_1 (.addr(IF_PC[11:2]), .data(IF_IR));
  not not_3 (not_3_out, \数据相关 );
  // Probe on EX_PC[11:0]
  // Probe on ID_PC[11:0]
  or or_2 (or_2_out, RST, or_1_out);
  IF_ID if_id_1 (
    .PCin(IF_PC), .IRin(IF_IR), .PCout(ID_PC),
    .IRout({ID_IR[31], ID_Funct[4], ID_IR[29:26], ID_Funct[3], ID_IR[24:15], ID_Funct[2:0], ID_IR[11:0]}),
    .RST(or_2_out), .EN_H(and_3_out), .CLK(CLK));  // open: PredictJumpin, PredictJumpout
  and and_3 (and_3_out, not_3_out, en);
  // Probe on M_PC[11:0]
  D_Flip_Flop #(.trigger("high"), .Pre_Clr_Positions("LEGACY"), .NegatePresetClear("false"), .enable("true"), .NewFFLayout("false")) d_ff_1 (.Q(d_ff_1_q));  // open: clk, D, Qn, preset, en, reset
  // Probe on 13'hc
  // Probe on WB_PC[11:0]
  Comparator #(.width(13), .mode("twosComplement")) comparator_1 (
    .a(CNT_num), .b(13'hc), .eq(comparator_1_eq), .lt(comparator_1_lt));  // open: gt
  Clock #(.highDuration(1), .lowDuration(1)) clock_2 (.out(clock_2_out));
  \单周期硬布线控制器  \u_单周期硬布线控制器_1  (
    .Funct(ID_Funct), .OP(ID_IR[6:2]), .ALU_OP(\单周期硬布线控制器_1_alu_op ), .MemToReg(\单周期硬布线控制器_1_memtoreg ),
    .MemWrite(\单周期硬布线控制器_1_memwrite ), .ALU_SRC(\单周期硬布线控制器_1_alu_src ), .RegWrite(\单周期硬布线控制器_1_regwrite ),
    .ecall(ID_ecall), .S_type(\单周期硬布线控制器_1_s_type ), .Jalr(\单周期硬布线控制器_1_jalr ), .Beq(\单周期硬布线控制器_1_beq ),
    .JAL(\单周期硬布线控制器_1_jal ), .Bne(\单周期硬布线控制器_1_bne ), .U_type(\单周期硬布线控制器_1_u_type ),
    .BGEU(\单周期硬布线控制器_1_bgeu ), .LHU(\单周期硬布线控制器_1_lhu ));  // open: URET, CSRRSI, CSRRCI
  Multiplexer #(.select(1), .width(5), .disabled("Z"), .enable("false")) multiplexer_4 (
    .in0(ID_IR[24:20]), .in1(5'b01010), .out(ID_R2_num), .sel(ID_ecall));
  assign bit_extender_1_out = {{20{ID_IR[31]}}, {ID_IR[31], ID_Funct[4], ID_IR[29:26], ID_Funct[3], ID_IR[24:20]}};  // Bit_Extender bit_extender_1
  assign bit_extender_2_out = {{20{ID_IR[31]}}, {ID_IR[31], ID_Funct[4], ID_IR[29:26], ID_Funct[3], ID_IR[11:7]}};  // Bit_Extender bit_extender_2
  nand nand_1 (nand_1_out, d_ff_1_q, comparator_1_eq);
  Counter #(.width(13), .max('h1fff), .ongoal("stay"), .trigger("rising"), .behavior("old")) counter_1 (
    .count(comparator_1_lt), .Q(CNT_num), .clk(clock_2_out));  // open: load, D, carry, clr, preset
  Multiplexer #(.select(1), .width(5), .disabled("Z"), .enable("false")) multiplexer_5 (
    .in0(ID_IR[19:15]), .in1(5'b10001), .out(ID_R1_num), .sel(ID_ecall));
  Shifter #(.width(12), .shift("ll")) shifter_1 (
    .in({ID_IR[31], ID_IR[7], ID_Funct[4], ID_IR[29:26], ID_Funct[3], ID_IR[11:8]}), .\dist (4'b0001),
    .out(shifter_1_out));
  Shifter #(.width(20), .shift("ll")) shifter_2 (
    .in({ID_IR[31], ID_IR[19:15], ID_Funct[2:0], ID_IR[20], ID_Funct[4], ID_IR[29:26], ID_Funct[3], ID_IR[24:21]}),
    .\dist (5'b00001), .out(shifter_2_out));
  assign controlled_buffer_1_out = nand_1_out ? clock_2_out : 1'bz;  // Controlled_Buffer controlled_buffer_1
  assign bit_extender_3_out = {{20{shifter_1_out[11]}}, shifter_1_out};  // Bit_Extender bit_extender_3
  assign bit_extender_4_out = {{12{shifter_2_out[19]}}, shifter_2_out};  // Bit_Extender bit_extender_4
  Pull_Resistor #(.pull(1)) pull_resistor_1 (.node(controlled_buffer_1_out));
  not not_4 (not_4_out, CLK);
  Regifile regifile_1 (
    .Din(RDin), .Clk(not_4_out), .R1(R1), .R2(R2), .WE(RegWrite), .W_num(W_num), .R1_num(ID_R1_num),
    .R2_num(ID_R2_num));
  not not_5 (not_5_out, halt);
  Counter #(.width(16), .max('hffff), .ongoal("wrap"), .trigger("rising"), .behavior("new")) counter_2 (
    .count(not_5_out), .Q(\总周期数 ), .clk(CLK), .clr(RST));  // open: load, D, carry, preset, down
  not not_6 (not_6_out, comparator_2_eq);
  Comparator #(.width(32), .mode("twosComplement")) comparator_2 (
    .a(R1), .b(32'ha), .eq(comparator_2_eq));  // open: gt, lt
  and and_4 (and_4_out, ID_ecall, not_6_out);
  and and_5 (and_5_out, comparator_2_eq, ID_ecall);
  Register #(.width(32), .trigger("rising"), .Select("low")) register_1 (
    .D(R2), .en(and_4_out), .Q(LedData), .clk(CLK), .clr(RST));
  Counter #(.width(16), .max('hffff), .ongoal("wrap"), .trigger("rising"), .behavior("new")) counter_3 (
    .count(Branch), .Q(\条件分支成功数 ), .clk(CLK), .clr(RST));  // open: load, D, carry, preset, down
  or or_3 (or_3_out, or_2_out, \数据相关 );
  ID_EX id_ex_1 (
    .PCin(ID_PC), .PCout(EX_PC),
    .IRin({ID_IR[31], ID_Funct[4], ID_IR[29:26], ID_Funct[3], ID_IR[24:15], ID_Funct[2:0], ID_IR[11:0]}),
    .IRout(EX_IR), .RST(or_3_out), .EN_H(en), .CLK(CLK), .Imm_I_in(bit_extender_1_out),
    .Imm_I_out(id_ex_1_imm_i_out), .Imm_S_in(bit_extender_2_out), .Imm_S_out(id_ex_1_imm_s_out),
    .Imm_B_in(bit_extender_3_out), .Imm_B_out(imm_B), .Imm_J_in(bit_extender_4_out), .Imm_J_out(imm_J),
    .Imm_U_in({ID_IR[31], ID_Funct[4], ID_IR[29:26], ID_Funct[3], ID_IR[24:15], ID_Funct[2:0], {12{1'b0}}}),
    .Imm_U_out(id_ex_1_imm_u_out), .R1in(R1), .R1out(id_ex_1_r1out), .R2in(R2), .R2out(id_ex_1_r2out),
    .Lhuin(\单周期硬布线控制器_1_lhu ), .Lhuout(id_ex_1_lhuout), .Jalrin(\单周期硬布线控制器_1_jalr ), .Jalrout(Jalr),
    .Jalout(Jal), .Jalin(\单周期硬布线控制器_1_jal ), .Beqin(\单周期硬布线控制器_1_beq ), .Beqout(id_ex_1_beqout),
    .Bgeuin(\单周期硬布线控制器_1_bgeu ), .Bgeuout(id_ex_1_bgeuout), .Bnein(\单周期硬布线控制器_1_bne ),
    .Bneout(id_ex_1_bneout), .MemToRegin(\单周期硬布线控制器_1_memtoreg ), .MemToRegout(id_ex_1_memtoregout),
    .MemWritein(\单周期硬布线控制器_1_memwrite ), .MemWriteout(id_ex_1_memwriteout),
    .AluSrcBin(\单周期硬布线控制器_1_alu_src ), .AluSrcBout(id_ex_1_alusrcbout), .RegWritein(\单周期硬布线控制器_1_regwrite ),
    .RegWriteout(EX_RegWrite_num), .U_Typein(\单周期硬布线控制器_1_u_type ), .U_Tpyeout(id_ex_1_u_tpyeout),
    .AluOpin(\单周期硬布线控制器_1_alu_op ), .AluOpout(id_ex_1_aluopout), .S_Typein(\单周期硬布线控制器_1_s_type ),
    .S_Tpyeout(id_ex_1_s_tpyeout), .Ecallin(and_5_out), .Ecallout(id_ex_1_ecallout), .W_in(ID_IR[11:7]),
    .W_out(EX_W_num));  // open: R1Forwardin, R1Forwardout, R2Forwardin, R2Forwardout, Uretin, Uretout, PredictJumpin, PredictJumpout
  Multiplexer #(.select(1), .width(32), .disabled("Z"), .enable("false")) multiplexer_6 (
    .in0(id_ex_1_imm_i_out), .in1(id_ex_1_imm_s_out), .out(multiplexer_6_out), .sel(id_ex_1_s_tpyeout));
  not not_7 (not_7_out, equal);
  Multiplexer #(.select(1), .width(32), .disabled("Z"), .enable("false")) multiplexer_7 (
    .in0(id_ex_1_r2out), .in1(multiplexer_6_out), .out(multiplexer_7_out), .sel(id_ex_1_alusrcbout));
  or or_4 (or_4_out, Jal, Jalr);
  Counter #(.width(16), .max('hffff), .ongoal("wrap"), .trigger("rising"), .behavior("new")) counter_4 (
    .count(or_4_out), .Q(\无条件分支数 ), .clk(CLK), .clr(RST));  // open: load, D, carry, preset, down
  and and_6 (and_6_out, id_ex_1_beqout, equal);
  and and_7 (and_7_out, not_7_out, id_ex_1_bneout);
  and and_8 (and_8_out, MoreAndEqu, id_ex_1_bgeuout);
  ALU alu_1 (
    .X(id_ex_1_r1out), .Y(multiplexer_7_out), .AluOP(id_ex_1_aluopout), .Equal(equal), .Result(Jalr_Addr),
    .out_4(MoreAndEqu));  // open: Result_2, out_6
  or or_5 (Branch, and_6_out, and_7_out, and_8_out);
  not not_8 (not_8_out, halt);
  EX_MEM ex_mem_1 (
    .PCin(EX_PC), .Lhuin(id_ex_1_lhuout), .PCout(M_PC), .Lhuout(ex_mem_1_lhuout), .Jalrin(Jalr),
    .Jalrout(ex_mem_1_jalrout), .IRin(EX_IR), .IRout(MEM_IR), .Jalin(Jal), .Jalout(ex_mem_1_jalout),
    .MemToRegin(id_ex_1_memtoregout), .MemToRegout(MemToReg), .MemWritein(id_ex_1_memwriteout),
    .MemWriteout(MemWrite), .Imm_U_in(id_ex_1_imm_u_out), .Imm_U_out(ex_mem_1_imm_u_out),
    .Resultin(Jalr_Addr), .Resultout(ex_mem_1_resultout), .RegWritein(EX_RegWrite_num),
    .RegWriteout(MEM_RegWrite_num), .U_Typein(id_ex_1_u_tpyeout), .U_Tpyeout(ex_mem_1_u_tpyeout),
    .Haltin(id_ex_1_ecallout), .Haltout(ex_mem_1_haltout), .W_in(EX_W_num), .W_out(MEM_W_num), .RST(RST),
    .EN_H(en), .CLK(CLK), .WMdatain(id_ex_1_r2out), .WMdataout(MDin));  // open: Uretin, Uretout
  and and_9 (and_9_out, not_8_out, \数据相关 );
  Counter #(.width(16), .max('hffff), .ongoal("wrap"), .trigger("rising"), .behavior("new")) counter_5 (
    .count(and_9_out), .Q(\插入气泡数 ), .clk(CLK), .clr(RST));  // open: load, D, carry, preset, down
  RAM #(.addrWidth(10), .dataWidth(32), .bus("separate"), .Select("high")) ram_1 (
    .addr(ex_mem_1_resultout[11:2]), .din(MDin), .data(ram_1_data), .str(MemWrite), .clk(CLK), .ld(MemToReg),
    .clr(RST));  // open: sel
  MEM_WB mem_wb_1 (
    .Lhuin(ex_mem_1_lhuout), .PCin(M_PC), .Jalrin(ex_mem_1_jalrout), .Jalin(ex_mem_1_jalout), .IRin(MEM_IR),
    .MemToRegin(MemToReg), .Imm_U_in(ex_mem_1_imm_u_out), .RegWritein(MEM_RegWrite_num),
    .AluResultin(ex_mem_1_resultout), .U_Typein(ex_mem_1_u_tpyeout), .RMdatain(ram_1_data),
    .Haltin(ex_mem_1_haltout), .W_in(MEM_W_num), .Lhuout(mem_wb_1_lhuout), .PCout(WB_PC),
    .Jalrout(mem_wb_1_jalrout), .Jalout(mem_wb_1_jalout), .IRout(WB_IR), .MemToRegout(mem_wb_1_memtoregout),
    .Imm_U_out(mem_wb_1_imm_u_out), .RegWriteout(RegWrite), .AluResultout(mem_wb_1_aluresultout),
    .U_Tpyeout(mem_wb_1_u_tpyeout), .RMdataout(mem_wb_1_rmdataout), .Haltout(mem_wb_1_haltout),
    .W_out(W_num), .RST(RST), .EN_H(en), .CLK(CLK), .Xin(ex_mem_1_resultout[1]), .Xout(mem_wb_1_xout));  // open: Uretin, Uretout
  Multiplexer #(.select(1), .width(16), .disabled("Z"), .enable("false")) multiplexer_8 (
    .in0(mem_wb_1_rmdataout[15:0]), .in1(mem_wb_1_rmdataout[31:16]), .out(multiplexer_8_out),
    .sel(mem_wb_1_xout));
  Adder #(.width(32)) adder_4 (.a(WB_PC), .b(mem_wb_1_imm_u_out), .out(adder_4_out));  // open: cin, cout
  and and_10 (halt, mem_wb_1_haltout, ~Go);  // AND_Gate
  not not_9 (en, halt);
  Adder #(.width(32)) adder_5 (.a(32'h4), .b(WB_PC), .out(WB_PC_4));  // open: cin, cout
  or or_6 (or_6_out, mem_wb_1_jalrout, mem_wb_1_jalout, mem_wb_1_u_tpyeout);
  assign bit_extender_5_out = {{16{1'b0}}, multiplexer_8_out};  // Bit_Extender bit_extender_5
  Multiplexer #(.select(1), .width(32), .disabled("Z"), .enable("false")) multiplexer_9 (
    .in0(mem_wb_1_rmdataout), .in1(bit_extender_5_out), .out(multiplexer_9_out), .sel(mem_wb_1_lhuout));
  Multiplexer #(.select(1), .width(32), .disabled("Z"), .enable("false")) multiplexer_10 (
    .in0(WB_PC_4), .in1(adder_4_out), .out(multiplexer_10_out), .sel(mem_wb_1_u_tpyeout));
  Multiplexer #(.select(1), .width(32), .disabled("Z"), .enable("false")) multiplexer_11 (
    .in0(mem_wb_1_aluresultout), .in1(multiplexer_9_out), .out(multiplexer_11_out), .sel(mem_wb_1_memtoregout));
  Multiplexer #(.select(1), .width(32), .disabled("Z"), .enable("false")) multiplexer_12 (
    .in0(multiplexer_11_out), .in1(multiplexer_10_out), .out(RDin), .sel(or_6_out));

  // Other names for the same wires on the sheet: ID_RD_num[4:0] = ID_IR[11:7]; ID_IR (some bits) = ID_Funct;
  //   ID_OP[4:0] = ID_IR[6:2]; MEM_PC[31:0] = M_PC; WriteBackData[31:0] = RDin

  // Notes on the sheet:
  //   中断源
  //   时空图监测，可删除
  //   中断等待指示
  //   数码管输出
  //   指令存储器
  //   指令字
  //   contents of rom_1 (hex, n*v repeats v):
  //   100493 100006f 100493 200913 300993 100006f 100493 200913 300993 100006f 100493 200913 300993
  //   100006f 100493 200913 300993 424000ef 100413 100493 1f49493 900533 2200893 73 24d493 48463 fedff06f
  //   900533 2200893 73 100493 249493 900533 2200893 73 48463 fedff06f 100493 1f49493 900533 2200893 73
  //   4034d493 900533 2200893 73 4044d493 900533 2200893 73 4044d493 900533 2200893 73 4044d493 900533
  //   2200893 73 4044d493 900533 2200893 73 4044d493 900533 2200893 73 4044d493 900533 2200893 73 4044d493
  //   900533 2200893 73 100413 1f41993 41f9d993 433 c00913 300b13 140413 f47413 800293 100313 499993
  //   89e9b3 1300533 2200893 73 406282b3 fe0294e3 140413 f00f93 1f47433 1c41413 800293 100313 49d993
  //   89e9b3 1300533 2200893 73 406282b3 fe0294e3 1c45413 406b0b33 b0463 f95ff06f 2b3 fff2c293 829293
  //   ff2e293 500533 2200893 73 fff00413 493 84a023 140413 448493 84a023 140413 448493 84a023 140413
  //   448493 84a023 140413 448493 84a023 140413 448493 84a023 140413 448493 84a023 140413 448493 84a023
  //   140413 448493 84a023 140413 448493 84a023 140413 448493 84a023 140413 448493 84a023 140413 448493
  //   84a023 140413 448493 84a023 140413 448493 84a023 140413 448493 84a023 140413 448493 140413 433
  //   3c00493 42983 4aa03 149a2b3 28663 134a023 1442023 ffc48493 fe9412e3 800533 2200893 73 440413 3c00493
  //   fc9416e3 a00893 73 100293 300313 800493 849493 7648493 1449493 900533 2200893 73 800e13 54d4b3
  //   64d4b3 900533 2200893 73 fffe0e13 fe0e14e3 a00893 73 13 430497 900533 2200893 73 430497 900533
  //   2200893 73 430497 900533 2200893 73 430497 900533 2200893 73 430497 900533 2200893 73 430497 900533
  //   2200893 73 430497 900533 2200893 73 430497 900533 2200893 73 a00893 73 313 1000e13 8400493 849493
  //   8348493 400913 891913 490913 849493 8248493 849493 8148493 891913 490913 891913 490913 932023
  //   12484b3 430313 fffe0e13 fe0e18e3 2000e13 313 35483 900533 2200893 73 230313 fffe0e13 fe0e14e3 a00893
  //   73 f00493 100913 409909b3 900533 2200893 73 fff48493 ff29f6e3 a00893 73 a00893 73 413 140413 800533
  //   2200893 73 240413 800533 2200893 73 340413 800533 2200893 73 440413 800533 2200893 73 540413 800533
  //   2200893 73 640413 800533 2200893 73 740413 800533 2200893 73 840413 800533 2200893 2200893 73 8067
  //   控制位
  //   流水调试日志用
  //   暂停节拍，不能为0
  //   rs1
  //   rs2
  //   rd
  //   戳工具置1进入计数暂停模式，ctrl+k时钟自动运行到对应节拍暂停
  //   ctrl+k关闭时钟连续运行，将控制位置零，进入单步调试模式调试
  //   Beq
  //   Bgeu
  //   Bne
  //   MemToReg
  //   MemWrite
  //   AluOP
  //   AluSrcB
  //   RegWrite
  //   U_Type
  //   S_Type
  //   可计数暂停的时钟源
  //   为方便自动评测，需要输出流水线各段保存的PC值，注意是PC不是PC+4，另外ID段寄存器写入信息，Mem段内存写入信息也要输出
  //   数据存储器
endmodule

module \重定向流水线  (
  output RegWrite,
  output MemWrite,
  output [31:0] IF_PC,
  output [31:0] ID_PC,
  output [31:0] EX_PC,
  output [31:0] M_PC,
  output [31:0] WB_PC,
  output [31:0] RDin,
  output [31:0] MDin,
  output [31:0] LedData
);

  wire and_2_out, and_3_out, and_4_out, and_5_out, and_6_out, and_7_out, and_8_out, and_9_out, Branch, CLK,
       clock_2_out, comparator_1_eq, comparator_1_lt, comparator_2_eq, controlled_buffer_1_out, d_ff_1_q, en,
       equal, EX_ecall, ex_mem_1_haltout, ex_mem_1_jalout, ex_mem_1_jalrout, ex_mem_1_lhuout,
       ex_mem_1_u_tpyeout, EX_RegWrite_num, Go, halt, ID_ecall, id_ex_1_alusrcbout, id_ex_1_beqout,
       id_ex_1_bgeuout, id_ex_1_bneout, id_ex_1_lhuout, id_ex_1_memtoregout, id_ex_1_memwriteout,
       id_ex_1_s_tpyeout, id_ex_1_u_tpyeout, IR1, IR2, IR3, Jal, Jalr, Load_Use, MEM_RegWrite_num,
       mem_wb_1_haltout, mem_wb_1_jalout, mem_wb_1_jalrout, mem_wb_1_lhuout, mem_wb_1_memtoregout,
       mem_wb_1_u_tpyeout, mem_wb_1_xout, MemToReg, MoreAndEqu, nand_1_out, not_1_out, not_2_out, not_3_out,
       not_4_out, not_5_out, not_6_out, not_7_out, not_8_out, or_1_out, or_2_out, or_3_out, or_4_out,
       or_6_out, RST, W1, W2, W3, \单周期硬布线控制器_1_alu_src , \单周期硬布线控制器_1_beq , \单周期硬布线控制器_1_bgeu ,
       \单周期硬布线控制器_1_bne , \单周期硬布线控制器_1_jal , \单周期硬布线控制器_1_jalr , \单周期硬布线控制器_1_lhu , \单周期硬布线控制器_1_memtoreg ,
       \单周期硬布线控制器_1_memwrite , \单周期硬布线控制器_1_regwrite , \单周期硬布线控制器_1_s_type , \单周期硬布线控制器_1_u_type , \数据相关 ;
  wire [1:0] id_ex_1_r1forwardout, id_ex_1_r2forwardout, R1Forward, R2Forward;
  wire [3:0] id_ex_1_aluopout, \单周期硬布线控制器_1_alu_op ;
  wire [4:0] EX_W_num, ID_Funct, ID_R1_num, ID_R2_num, MEM_W_num, W_num;
  wire [11:0] shifter_1_out;
  wire [12:0] CNT_num;
  wire [15:0] adder_4_out, \LoadUse次数 , multiplexer_10_out, shifter_3_out, \总周期数 , \插入气泡数 , \无条件分支数 ,
       \条件分支成功数 ;
  wire [19:0] shifter_2_out;
  wire [31:0] adder_1_out, adder_2_out, adder_3_out, adder_7_out, and_1_out, bit_extender_1_out,
       bit_extender_2_out, bit_extender_3_out, bit_extender_4_out, bit_extender_5_out, EX_IR,
       ex_mem_1_imm_u_out, EX_R1, EX_R2, id_ex_1_imm_i_out, id_ex_1_imm_s_out, id_ex_1_imm_u_out,
       id_ex_1_r1out, id_ex_1_r2out, ID_IR, ID_R1, ID_R2, IF_IR, imm_B, imm_J, Jalr_Addr, MEM_IR,
       mem_wb_1_aluresultout, mem_wb_1_imm_u_out, mem_wb_1_rmdataout, multiplexer_1_out, multiplexer_2_out,
       multiplexer_3_out, multiplexer_8_out, multiplexer_9_out, multiplexer_11_out, multiplexer_12_out,
       multiplexer_13_out, ram_1_data, RT, WB_IR, WB_PC_4;

  Button \u_总复位  (.out(RST));
  Button _1 (.out(IR1));
  Button _2 (.out(IR2));
  Button _3 (.out(IR3));
  // Probe on \总周期数 
  // Probe on \总周期数 
  Button \u_继续运行  (.out(Go));
  LED #(.active("true")) led_1 (.in(W1));
  LED #(.active("true")) led_2 (.in(W2));
  LED #(.active("true")) led_3 (.in(W3));
  Hex_Digit_Display hex_digit_display_1 (.value(LedData[31:28]));  // open: dp
  // Probe on IF_PC[19:0]
  // RiscV_Probe riscv_probe_1: pin names not known; wires that end beside it: IF_IR
  Hex_Digit_Display hex_digit_display_2 (.value(LedData[27:24]));  // open: dp
  Hex_Digit_Display hex_digit_display_3 (.value(LedData[23:20]));  // open: dp
  // Probe on ID_PC[19:0]
  // RiscV_Probe riscv_probe_2: pin names not known; wires that end beside it: {ID_IR[31], ID_Funct[4], ID_IR[29:26], ID_Funct[3], ID_IR[24:15], ID_Funct[2:0], ID_IR[11:0]}
  Multiplexer #(.select(1), .width(32), .disabled("Z"), .enable("false")) multiplexer_1 (
    .in0(adder_3_out), .in1(adder_1_out), .out(multiplexer_1_out), .sel(Jal));
  Adder #(.width(32)) adder_1 (.a(imm_J), .b(EX_PC), .out(adder_1_out));  // open: cin, cout
  assign and_1_out = Jalr_Addr & 32'hfffffffe;  // AND_Gate and_1, 32 bits wide
  Hex_Digit_Display hex_digit_display_4 (.value(LedData[15:12]));  // open: dp
  Hex_Digit_Display hex_digit_display_5 (.value(LedData[19:16]));  // open: dp
  \数据冲突处理逻辑_重定向  \u_数据冲突处理逻辑_重定向_1  (
    .ID_R1_num(ID_R1_num), .EX_W_num(EX_W_num), .EX_RegWrite(EX_RegWrite_num), .EX_OP(EX_IR[6:2]),
    .ID_R2_num(ID_R2_num), .MEM_W_num(MEM_W_num), .MEM_RegWrite(MEM_RegWrite_num), .ID_OP(ID_IR[6:2]),
    .ID_Funct(ID_Funct), .\数据相关 (\数据相关 ), .R1Forward(R1Forward), .Load_Use(Load_Use), .R2Forward(R2Forward));
  Multiplexer #(.select(1), .width(32), .disabled("Z"), .enable("false")) multiplexer_2 (
    .in0(multiplexer_1_out), .in1(and_1_out), .out(multiplexer_2_out), .sel(Jalr));
  Adder #(.width(32)) adder_2 (.a(imm_B), .b(EX_PC), .out(adder_2_out));  // open: cin, cout
  Hex_Digit_Display hex_digit_display_6 (.value(LedData[11:8]));  // open: dp
  Hex_Digit_Display hex_digit_display_7 (.value(LedData[7:4]));  // open: dp
  Clock #(.highDuration(1), .lowDuration(1)) clock_1 (.out(CLK));
  // Probe on EX_PC[19:0]
  // RiscV_Probe riscv_probe_3: pin names not known; wires that end beside it: EX_IR
  Multiplexer #(.select(1), .width(32), .disabled("Z"), .enable("false")) multiplexer_3 (
    .in0(multiplexer_2_out), .in1(adder_2_out), .out(multiplexer_3_out), .sel(Branch));
  and and_2 (and_2_out, not_2_out, not_1_out);
  not not_1 (not_1_out, halt);
  not not_2 (not_2_out, Load_Use);
  Hex_Digit_Display hex_digit_display_8 (.value(LedData[3:0]));  // open: dp
  Register #(.width(32), .trigger("rising"), .Select("low")) PC (
    .D(multiplexer_3_out), .en(and_2_out), .Q(IF_PC), .clk(CLK), .clr(RST));
  // Probe on \总周期数 
  // Probe on M_PC[19:0]
  // RiscV_Probe riscv_probe_4: pin names not known; wires that end beside it: MEM_IR
  // Probe on \总周期数 
  // Probe on \无条件分支数 
  // Probe on \条件分支成功数 
  // Probe on \插入气泡数 
  // Probe on \LoadUse次数 
  ROM #(.addrWidth(10), .dataWidth(32), .Select("high")) rom_1 (.addr(IF_PC[11:2]), .data(IF_IR));
  Adder #(.width(32)) adder_3 (.a(IF_PC), .b(32'h4), .out(adder_3_out));  // open: cin, cout
  // Probe on IF_PC[11:0]
  // Probe on WB_PC[19:0]
  // RiscV_Probe riscv_probe_5: pin names not known; wires that end beside it: WB_IR
  or or_1 (or_1_out, Branch, Jal, Jalr);
  not not_3 (not_3_out, Load_Use);
  and and_3 (and_3_out, not_3_out, en);
  // Probe on ID_PC[11:0]
  // Probe on EX_PC[11:0]
  or or_2 (or_2_out, RST, or_1_out);
  IF_ID if_id_1 (
    .PCin(IF_PC), .IRin(IF_IR), .PCout(ID_PC),
    .IRout({ID_IR[31], ID_Funct[4], ID_IR[29:26], ID_Funct[3], ID_IR[24:15], ID_Funct[2:0], ID_IR[11:0]}),
    .RST(or_2_out), .EN_H(and_3_out), .CLK(CLK));  // open: PredictJumpin, PredictJumpout
  // Probe on M_PC[11:0]
  D_Flip_Flop #(.trigger("high"), .Pre_Clr_Positions("LEGACY"), .NegatePresetClear("false"), .enable("true"), .NewFFLayout("false")) d_ff_1 (.Q(d_ff_1_q));  // open: clk, D, Qn, preset, en, reset
  // Probe on 13'hc
  // Probe on WB_PC[11:0]
  Comparator #(.width(13), .mode("twosComplement")) comparator_1 (
    .a(CNT_num), .b(13'hc), .eq(comparator_1_eq), .lt(comparator_1_lt));  // open: gt
  Clock #(.highDuration(1), .lowDuration(1)) clock_2 (.out(clock_2_out));
  \单周期硬布线控制器  \u_单周期硬布线控制器_1  (
    .Funct(ID_Funct), .OP(ID_IR[6:2]), .ALU_OP(\单周期硬布线控制器_1_alu_op ), .MemToReg(\单周期硬布线控制器_1_memtoreg ),
    .MemWrite(\单周期硬布线控制器_1_memwrite ), .ALU_SRC(\单周期硬布线控制器_1_alu_src ), .RegWrite(\单周期硬布线控制器_1_regwrite ),
    .ecall(ID_ecall), .S_type(\单周期硬布线控制器_1_s_type ), .Jalr(\单周期硬布线控制器_1_jalr ), .Beq(\单周期硬布线控制器_1_beq ),
    .JAL(\单周期硬布线控制器_1_jal ), .Bne(\单周期硬布线控制器_1_bne ), .U_type(\单周期硬布线控制器_1_u_type ),
    .BGEU(\单周期硬布线控制器_1_bgeu ), .LHU(\单周期硬布线控制器_1_lhu ));  // open: URET, CSRRSI, CSRRCI
  Multiplexer #(.select(1), .width(5), .disabled("Z"), .enable("false")) multiplexer_4 (
    .in0(ID_IR[24:20]), .in1(5'b01010), .out(ID_R2_num), .sel(ID_ecall));
  assign bit_extender_1_out = {{20{ID_IR[31]}}, {ID_IR[31], ID_Funct[4], ID_IR[29:26], ID_Funct[3], ID_IR[24:20]}};  // Bit_Extender bit_extender_1
  assign bit_extender_2_out = {{20{ID_IR[31]}}, {ID_IR[31], ID_Funct[4], ID_IR[29:26], ID_Funct[3], ID_IR[11:7]}};  // Bit_Extender bit_extender_2
  nand nand_1 (nand_1_out, d_ff_1_q, comparator_1_eq);
  Counter #(.width(13), .max('h1fff), .ongoal("stay"), .trigger("rising"), .behavior("old")) counter_1 (
    .count(comparator_1_lt), .Q(CNT_num), .clk(clock_2_out));  // open: load, D, carry, clr, preset
  Multiplexer #(.select(1), .width(5), .disabled("Z"), .enable("false")) multiplexer_5 (
    .in0(ID_IR[19:15]), .in1(5'b10001), .out(ID_R1_num), .sel(ID_ecall));
  Shifter #(.width(12), .shift("ll")) shifter_1 (
    .in({ID_IR[31], ID_IR[7], ID_Funct[4], ID_IR[29:26], ID_Funct[3], ID_IR[11:8]}), .\dist (4'b0001),
    .out(shifter_1_out));
  Shifter #(.width(20), .shift("ll")) shifter_2 (
    .in({ID_IR[31], ID_IR[19:15], ID_Funct[2:0], ID_IR[20], ID_Funct[4], ID_IR[29:26], ID_Funct[3], ID_IR[24:21]}),
    .\dist (5'b00001), .out(shifter_2_out));
  assign controlled_buffer_1_out = nand_1_out ? clock_2_out : 1'bz;  // Controlled_Buffer controlled_buffer_1
  assign bit_extender_3_out = {{20{shifter_1_out[11]}}, shifter_1_out};  // Bit_Extender bit_extender_3
  assign bit_extender_4_out = {{12{shifter_2_out[19]}}, shifter_2_out};  // Bit_Extender bit_extender_4
  Pull_Resistor #(.pull(1)) pull_resistor_1 (.node(controlled_buffer_1_out));
  not not_4 (not_4_out, CLK);
  Regifile regifile_1 (
    .Din(RDin), .Clk(not_4_out), .R1(ID_R1), .R2(ID_R2), .WE(RegWrite), .W_num(W_num), .R1_num(ID_R1_num),
    .R2_num(ID_R2_num));
  not not_5 (not_5_out, halt);
  Counter #(.width(16), .max('hffff), .ongoal("wrap"), .trigger("rising"), .behavior("new")) counter_2 (
    .count(not_5_out), .Q(\总周期数 ), .clk(CLK), .clr(RST));  // open: load, D, carry, preset, down
  Counter #(.width(16), .max('hffff), .ongoal("wrap"), .trigger("rising"), .behavior("new")) counter_3 (
    .count(Branch), .Q(\条件分支成功数 ), .clk(CLK), .clr(RST));  // open: load, D, carry, preset, down
  or or_3 (or_3_out, or_2_out, Load_Use);
  ID_EX id_ex_1 (
    .PCin(ID_PC), .PCout(EX_PC),
    .IRin({ID_IR[31], ID_Funct[4], ID_IR[29:26], ID_Funct[3], ID_IR[24:15], ID_Funct[2:0], ID_IR[11:0]}),
    .IRout(EX_IR), .RST(or_3_out), .EN_H(en), .CLK(CLK), .Imm_I_in(bit_extender_1_out),
    .Imm_I_out(id_ex_1_imm_i_out), .Imm_S_in(bit_extender_2_out), .Imm_S_out(id_ex_1_imm_s_out),
    .Imm_B_in(bit_extender_3_out), .Imm_B_out(imm_B), .Imm_J_in(bit_extender_4_out), .Imm_J_out(imm_J),
    .Imm_U_in({ID_IR[31], ID_Funct[4], ID_IR[29:26], ID_Funct[3], ID_IR[24:15], ID_Funct[2:0], {12{1'b0}}}),
    .Imm_U_out(id_ex_1_imm_u_out), .R1in(ID_R1), .R1out(id_ex_1_r1out), .R2in(ID_R2), .R2out(id_ex_1_r2out),
    .Lhuin(\单周期硬布线控制器_1_lhu ), .Lhuout(id_ex_1_lhuout), .Jalrin(\单周期硬布线控制器_1_jalr ), .Jalrout(Jalr),
    .Jalout(Jal), .Jalin(\单周期硬布线控制器_1_jal ), .Beqin(\单周期硬布线控制器_1_beq ), .Beqout(id_ex_1_beqout),
    .Bgeuin(\单周期硬布线控制器_1_bgeu ), .Bgeuout(id_ex_1_bgeuout), .Bnein(\单周期硬布线控制器_1_bne ),
    .Bneout(id_ex_1_bneout), .MemToRegin(\单周期硬布线控制器_1_memtoreg ), .MemToRegout(id_ex_1_memtoregout),
    .MemWritein(\单周期硬布线控制器_1_memwrite ), .MemWriteout(id_ex_1_memwriteout),
    .AluSrcBin(\单周期硬布线控制器_1_alu_src ), .AluSrcBout(id_ex_1_alusrcbout), .RegWritein(\单周期硬布线控制器_1_regwrite ),
    .RegWriteout(EX_RegWrite_num), .U_Typein(\单周期硬布线控制器_1_u_type ), .U_Tpyeout(id_ex_1_u_tpyeout),
    .AluOpin(\单周期硬布线控制器_1_alu_op ), .AluOpout(id_ex_1_aluopout), .S_Typein(\单周期硬布线控制器_1_s_type ),
    .S_Tpyeout(id_ex_1_s_tpyeout), .Ecallin(ID_ecall), .Ecallout(EX_ecall), .W_in(ID_IR[11:7]),
    .W_out(EX_W_num), .R1Forwardin(R1Forward), .R1Forwardout(id_ex_1_r1forwardout), .R2Forwardin(R2Forward),
    .R2Forwardout(id_ex_1_r2forwardout));  // open: Uretin, Uretout, PredictJumpin, PredictJumpout
  Multiplexer #(.select(2), .width(32), .disabled("Z"), .enable("false")) multiplexer_6 (
    .in0(id_ex_1_r1out), .in1(RDin), .in2(RT), .out(EX_R1), .sel(id_ex_1_r1forwardout));  // open: in3
  Multiplexer #(.select(2), .width(32), .disabled("Z"), .enable("false")) multiplexer_7 (
    .in0(id_ex_1_r2out), .in1(RDin), .in2(RT), .out(EX_R2), .sel(id_ex_1_r2forwardout));  // open: in3
  Multiplexer #(.select(1), .width(32), .disabled("Z"), .enable("false")) multiplexer_8 (
    .in0(id_ex_1_imm_i_out), .in1(id_ex_1_imm_s_out), .out(multiplexer_8_out), .sel(id_ex_1_s_tpyeout));
  not not_6 (not_6_out, equal);
  Multiplexer #(.select(1), .width(32), .disabled("Z"), .enable("false")) multiplexer_9 (
    .in0(EX_R2), .in1(multiplexer_8_out), .out(multiplexer_9_out), .sel(id_ex_1_alusrcbout));
  not not_7 (not_7_out, comparator_2_eq);
  Comparator #(.width(32), .mode("twosComplement")) comparator_2 (
    .a(EX_R1), .b(32'ha), .eq(comparator_2_eq));  // open: gt, lt
  or or_4 (or_4_out, Jal, Jalr);
  Counter #(.width(16), .max('hffff), .ongoal("wrap"), .trigger("rising"), .behavior("new")) counter_4 (
    .count(or_4_out), .Q(\无条件分支数 ), .clk(CLK), .clr(RST));  // open: load, D, carry, preset, down
  and and_4 (and_4_out, id_ex_1_beqout, equal);
  and and_5 (and_5_out, not_6_out, id_ex_1_bneout);
  and and_6 (and_6_out, MoreAndEqu, id_ex_1_bgeuout);
  ALU alu_1 (
    .X(EX_R1), .Y(multiplexer_9_out), .AluOP(id_ex_1_aluopout), .Equal(equal), .Result(Jalr_Addr),
    .out_4(MoreAndEqu));  // open: Result_2, out_6
  and and_7 (and_7_out, EX_ecall, not_7_out);
  and and_8 (and_8_out, comparator_2_eq, EX_ecall);
  or or_5 (Branch, and_4_out, and_5_out, and_6_out);
  Register #(.width(32), .trigger("rising"), .Select("low")) register_1 (
    .D(EX_R2), .en(and_7_out), .Q(LedData), .clk(CLK), .clr(RST));
  EX_MEM ex_mem_1 (
    .PCin(EX_PC), .Lhuin(id_ex_1_lhuout), .PCout(M_PC), .Lhuout(ex_mem_1_lhuout), .Jalrin(Jalr),
    .Jalrout(ex_mem_1_jalrout), .IRin(EX_IR), .IRout(MEM_IR), .Jalin(Jal), .Jalout(ex_mem_1_jalout),
    .MemToRegin(id_ex_1_memtoregout), .MemToRegout(MemToReg), .MemWritein(id_ex_1_memwriteout),
    .MemWriteout(MemWrite), .Imm_U_in(id_ex_1_imm_u_out), .Imm_U_out(ex_mem_1_imm_u_out),
    .Resultin(Jalr_Addr), .Resultout(RT), .RegWritein(EX_RegWrite_num), .RegWriteout(MEM_RegWrite_num),
    .U_Typein(id_ex_1_u_tpyeout), .U_Tpyeout(ex_mem_1_u_tpyeout), .Haltin(and_8_out),
    .Haltout(ex_mem_1_haltout), .W_in(EX_W_num), .W_out(MEM_W_num), .RST(RST), .EN_H(en), .CLK(CLK),
    .WMdatain(EX_R2), .WMdataout(MDin));  // open: Uretin, Uretout
  Adder #(.width(16)) adder_4 (.a(\条件分支成功数 ), .b(\无条件分支数 ), .out(adder_4_out));  // open: cin, cout
  not not_8 (not_8_out, halt);
  and and_9 (and_9_out, not_8_out, Load_Use);
  Shifter #(.width(16), .shift("ll")) shifter_3 (.in(adder_4_out), .\dist (4'b0001), .out(shifter_3_out));
  Counter #(.width(16), .max('hffff), .ongoal("wrap"), .trigger("rising"), .behavior("new")) counter_5 (
    .count(and_9_out), .Q(\LoadUse次数 ), .clk(CLK), .clr(RST));  // open: load, D, carry, preset, down
  Adder #(.width(16)) adder_5 (.a(shifter_3_out), .b(\LoadUse次数 ), .out(\插入气泡数 ));  // open: cin, cout
  RAM #(.addrWidth(10), .dataWidth(32), .bus("separate"), .Select("high")) ram_1 (
    .addr(RT[11:2]), .din(MDin), .data(ram_1_data), .str(MemWrite), .clk(CLK), .ld(MemToReg), .clr(RST));  // open: sel
  MEM_WB mem_wb_1 (
    .Lhuin(ex_mem_1_lhuout), .PCin(M_PC), .Jalrin(ex_mem_1_jalrout), .Jalin(ex_mem_1_jalout), .IRin(MEM_IR),
    .MemToRegin(MemToReg), .Imm_U_in(ex_mem_1_imm_u_out), .RegWritein(MEM_RegWrite_num), .AluResultin(RT),
    .U_Typein(ex_mem_1_u_tpyeout), .RMdatain(ram_1_data), .Haltin(ex_mem_1_haltout), .W_in(MEM_W_num),
    .Lhuout(mem_wb_1_lhuout), .PCout(WB_PC), .Jalrout(mem_wb_1_jalrout), .Jalout(mem_wb_1_jalout),
    .IRout(WB_IR), .MemToRegout(mem_wb_1_memtoregout), .Imm_U_out(mem_wb_1_imm_u_out),
    .RegWriteout(RegWrite), .AluResultout(mem_wb_1_aluresultout), .U_Tpyeout(mem_wb_1_u_tpyeout),
    .RMdataout(mem_wb_1_rmdataout), .Haltout(mem_wb_1_haltout), .W_out(W_num), .RST(RST), .EN_H(en),
    .CLK(CLK), .Xin(RT[1]), .Xout(mem_wb_1_xout));  // open: Uretin, Uretout
  Adder #(.width(32)) adder_6 (.a(32'h4), .b(WB_PC), .out(WB_PC_4));  // open: cin, cout
  Multiplexer #(.select(1), .width(16), .disabled("Z"), .enable("false")) multiplexer_10 (
    .in0(mem_wb_1_rmdataout[15:0]), .in1(mem_wb_1_rmdataout[31:16]), .out(multiplexer_10_out),
    .sel(mem_wb_1_xout));
  Adder #(.width(32)) adder_7 (.a(WB_PC), .b(mem_wb_1_imm_u_out), .out(adder_7_out));  // open: cin, cout
  and and_10 (halt, mem_wb_1_haltout, ~Go);  // AND_Gate
  not not_9 (en, halt);
  or or_6 (or_6_out, mem_wb_1_jalrout, mem_wb_1_jalout, mem_wb_1_u_tpyeout);
  assign bit_extender_5_out = {{16{1'b0}}, multiplexer_10_out};  // Bit_Extender bit_extender_5
  Multiplexer #(.select(1), .width(32), .disabled("Z"), .enable("false")) multiplexer_11 (
    .in0(WB_PC_4), .in1(adder_7_out), .out(multiplexer_11_out), .sel(mem_wb_1_u_tpyeout));
  Multiplexer #(.select(1), .width(32), .disabled("Z"), .enable("false")) multiplexer_12 (
    .in0(mem_wb_1_rmdataout), .in1(bit_extender_5_out), .out(multiplexer_12_out), .sel(mem_wb_1_lhuout));
  Multiplexer #(.select(1), .width(32), .disabled("Z"), .enable("false")) multiplexer_13 (
    .in0(mem_wb_1_aluresultout), .in1(multiplexer_12_out), .out(multiplexer_13_out),
    .sel(mem_wb_1_memtoregout));
  Multiplexer #(.select(1), .width(32), .disabled("Z"), .enable("false")) multiplexer_14 (
    .in0(multiplexer_13_out), .in1(multiplexer_11_out), .out(RDin), .sel(or_6_out));

  // Other names for the same wires on the sheet: ID_RD_num[4:0] = ID_IR[11:7]; ID_IR (some bits) = ID_Funct;
  //   ID_OP[4:0] = ID_IR[6:2]; MEM_PC[31:0] = M_PC; WD[31:0] = RDin; WriteBackData[31:0] = RDin

  // Notes on the sheet:
  //   中断源
  //   时空图监测，可删除
  //   中断等待指示
  //   数码管输出
  //   指令存储器
  //   contents of rom_1 (hex, n*v repeats v):
  //   7d000113 100413 1f41993 41f9d993 433 c00913 800b13 140413 f47413 800293 100313 499993 89e9b3 1300533
  //   2200893 73 406282b3 fe0294e3 140413 f00f93 1f47433 1c41413 800293 100313 49d993 89e9b3 1300533
  //   2200893 73 406282b3 fe0294e3 1c45413 406b0b33 b0463 f95ff06f 2b3 fff2c293 1029293 fff2e293 500533
  //   2200893 73 f5dff06f 1112023 410113 a12023 410113 812023 410113 1312023 410113 1412023 410113 1512023
  //   410113 1612023 410113 100b13 300a13 100a93 1600433 441413 14469b3 1300533 2200893 73 fe0416e3
  //   415a0a33 fe0a10e3 ffc10113 12b03 ffc10113 12a83 ffc10113 12a03 ffc10113 12983 ffc10113 12403
  //   ffc10113 12503 ffc10113 12883 200073 1112023 410113 a12023 410113 812023 410113 1312023 410113
  //   1412023 410113 1512023 410113 1612023 410113 200b13 300a13 100a93 1600433 441413 14469b3 1300533
  //   2200893 73 fe0416e3 415a0a33 fe0a10e3 ffc10113 12b03 ffc10113 12a83 ffc10113 12a03 ffc10113 12983
  //   ffc10113 12403 ffc10113 12503 ffc10113 12883 200073 1112023 410113 a12023 410113 812023 410113
  //   1312023 410113 1412023 410113 1512023 410113 1612023 410113 300b13 300a13 100a93 1600433 441413
  //   14469b3 1300533 2200893 73 fe0416e3 415a0a33 fe0a10e3 ffc10113 12b03 ffc10113 12a83 ffc10113 12a03
  //   ffc10113 12983 ffc10113 12403 ffc10113 12503 ffc10113 12883 200073
  //   指令字
  //   控制位
  //   流水调试日志用
  //   暂停节拍，不能为0
  //   rs1
  //   rs2
  //   rd
  //   戳工具置1进入计数暂停模式，ctrl+k时钟自动运行到对应节拍暂停
  //   ctrl+k关闭时钟连续运行，将控制位置零，进入单步调试模式调试
  //   Beq
  //   Bgeu
  //   Bne
  //   MemToReg
  //   MemWrite
  //   AluOP
  //   AluSrcB
  //   RegWrite
  //   U_Type
  //   S_Type
  //   可计数暂停的时钟源
  //   为方便自动评测，需要输出流水线各段保存的PC值，注意是PC不是PC+4，另外ID段寄存器写入信息，Mem段内存写入信息也要输出
  //   数据存储器
endmodule

module \动态分支预测  (
  output RegWrite,
  output MemWrite,
  output [31:0] IF_PC,
  output [31:0] ID_PC,
  output [31:0] EX_PC,
  output [31:0] M_PC,
  output [31:0] WB_PC,
  output [31:0] RDin,
  output [31:0] MDin,
  output [31:0] LedData
);

  wire and_1_out, and_3_out, and_4_out, and_5_out, and_6_out, and_7_out, and_8_out, and_9_out, and_10_out,
       Branch, BranchTaken, CLK, clock_2_out, comparator_1_eq, comparator_2_eq, comparator_2_lt,
       comparator_3_eq, controlled_buffer_1_out, d_ff_1_q, en, equal, EX_ecall, ex_mem_1_haltout,
       ex_mem_1_jalout, ex_mem_1_jalrout, ex_mem_1_lhuout, ex_mem_1_u_tpyeout, EX_PredictErr, EX_PredictJump,
       EX_RegWrite_num, Go, halt, ID_ecall, id_ex_1_alusrcbout, id_ex_1_beqout, id_ex_1_bgeuout,
       id_ex_1_bneout, id_ex_1_lhuout, id_ex_1_memtoregout, id_ex_1_memwriteout, id_ex_1_s_tpyeout,
       id_ex_1_u_tpyeout, if_id_1_predictjumpout, IR1, IR2, IR3, Jal, Jalr, Load_Use, MEM_RegWrite_num,
       mem_wb_1_haltout, mem_wb_1_jalout, mem_wb_1_jalrout, mem_wb_1_lhuout, mem_wb_1_memtoregout,
       mem_wb_1_u_tpyeout, mem_wb_1_xout, MemToReg, MoreAndEqu, nand_1_out, not_1_out, not_2_out, not_4_out,
       not_5_out, not_6_out, not_7_out, not_8_out, not_9_out, or_1_out, or_2_out, or_3_out, or_4_out,
       or_5_out, or_6_out, or_7_out, or_10_out, PredictJump, RST, W1, W2, W3, \单周期硬布线控制器_1_alu_src ,
       \单周期硬布线控制器_1_beq , \单周期硬布线控制器_1_bgeu , \单周期硬布线控制器_1_bne , \单周期硬布线控制器_1_jal , \单周期硬布线控制器_1_jalr ,
       \单周期硬布线控制器_1_lhu , \单周期硬布线控制器_1_memtoreg , \单周期硬布线控制器_1_memwrite , \单周期硬布线控制器_1_regwrite ,
       \单周期硬布线控制器_1_s_type , \单周期硬布线控制器_1_u_type , \数据相关 ;
  wire [1:0] id_ex_1_r1forwardout, id_ex_1_r2forwardout, R1Forward, R2Forward;
  wire [3:0] id_ex_1_aluopout, \单周期硬布线控制器_1_alu_op ;
  wire [4:0] EX_W_num, ID_Funct, ID_R1_num, ID_R2_num, MEM_W_num, W_num;
  wire [11:0] shifter_1_out;
  wire [12:0] CNT_num;
  wire [15:0] adder_5_out, \LoadUse次数 , multiplexer_13_out, shifter_3_out, \分支预测成功数 , \总周期数 , \插入气泡数 ,
       \无条件分支数 , \条件分支成功数 ;
  wire [19:0] shifter_2_out;
  wire [31:0] adder_1_out, adder_2_out, adder_3_out, adder_8_out, and_2_out, bit_extender_1_out,
       bit_extender_2_out, bit_extender_3_out, bit_extender_4_out, bit_extender_5_out, BranchAddr, EX_IR,
       ex_mem_1_imm_u_out, EX_R1, EX_R2, id_ex_1_imm_i_out, id_ex_1_imm_s_out, id_ex_1_imm_u_out,
       id_ex_1_r1out, id_ex_1_r2out, ID_IR, ID_R1, ID_R2, IF_IR, IF_PC_4, imm_B, imm_J, Jalr_Addr, JumpAddr,
       MEM_IR, mem_wb_1_aluresultout, mem_wb_1_imm_u_out, mem_wb_1_rmdataout, multiplexer_1_out,
       multiplexer_3_out, multiplexer_4_out, multiplexer_5_out, multiplexer_6_out, multiplexer_11_out,
       multiplexer_12_out, multiplexer_14_out, multiplexer_15_out, multiplexer_16_out, ram_1_data, RT, WB_IR,
       WB_PC_4;

  Button \u_总复位  (.out(RST));
  Button _1 (.out(IR1));
  Button _2 (.out(IR2));
  Button _3 (.out(IR3));
  // Probe on \总周期数 
  // Probe on \总周期数 
  Button \u_继续运行  (.out(Go));
  LED #(.active("true")) led_1 (.in(W1));
  LED #(.active("true")) led_2 (.in(W2));
  LED #(.active("true")) led_3 (.in(W3));
  or or_1 (or_1_out, Branch, Jal, Jalr);
  Adder #(.width(32)) adder_1 (.a(imm_J), .b(EX_PC), .out(adder_1_out));  // open: cin, cout
  Hex_Digit_Display hex_digit_display_1 (.value(LedData[31:28]));  // open: dp
  // Probe on IF_PC[19:0]
  // RiscV_Probe riscv_probe_1: pin names not known; wires that end beside it: IF_IR
  and and_1 (and_1_out, or_1_out, ~EX_PredictErr);  // AND_Gate
  Multiplexer #(.select(1), .width(32), .disabled("Z"), .enable("false")) multiplexer_1 (
    .in0(IF_PC_4), .in1(adder_1_out), .out(multiplexer_1_out), .sel(Jal));
  Adder #(.width(32)) adder_2 (.a(imm_B), .b(EX_PC), .out(adder_2_out));  // open: cin, cout
  Hex_Digit_Display hex_digit_display_2 (.value(LedData[27:24]));  // open: dp
  Hex_Digit_Display hex_digit_display_3 (.value(LedData[23:20]));  // open: dp
  // Probe on ID_PC[19:0]
  // RiscV_Probe riscv_probe_2: pin names not known; wires that end beside it: {ID_IR[31], ID_Funct[4], ID_IR[29:26], ID_Funct[3], ID_IR[24:15], ID_Funct[2:0], ID_IR[11:0]}
  // Probe on \分支预测成功数 
  Counter #(.width(16), .max('hffff), .ongoal("wrap"), .trigger("rising"), .behavior("new")) counter_1 (
    .count(and_1_out), .Q(\分支预测成功数 ), .clk(CLK), .clr(RST));  // open: load, D, carry, preset, down
  Multiplexer #(.select(1), .width(32), .disabled("Z"), .enable("false")) multiplexer_2 (
    .in0(multiplexer_1_out), .in1(adder_2_out), .out(BranchAddr), .sel(Branch));
  Hex_Digit_Display hex_digit_display_4 (.value(LedData[19:16]));  // open: dp
  Hex_Digit_Display hex_digit_display_5 (.value(LedData[15:12]));  // open: dp
  \数据冲突处理逻辑_重定向  \u_数据冲突处理逻辑_重定向_1  (
    .ID_R1_num(ID_R1_num), .EX_W_num(EX_W_num), .EX_RegWrite(EX_RegWrite_num), .EX_OP(EX_IR[6:2]),
    .ID_R2_num(ID_R2_num), .MEM_W_num(MEM_W_num), .MEM_RegWrite(MEM_RegWrite_num), .ID_OP(ID_IR[6:2]),
    .ID_Funct(ID_Funct), .\数据相关 (\数据相关 ), .R1Forward(R1Forward), .Load_Use(Load_Use), .R2Forward(R2Forward));
  Adder #(.width(32)) adder_3 (.a(EX_PC), .b(32'h4), .out(adder_3_out));  // open: cin, cout
  Hex_Digit_Display hex_digit_display_6 (.value(LedData[11:8]));  // open: dp
  Hex_Digit_Display hex_digit_display_7 (.value(LedData[7:4]));  // open: dp
  Clock #(.highDuration(1), .lowDuration(1)) clock_1 (.out(CLK));
  // Probe on EX_PC[19:0]
  // RiscV_Probe riscv_probe_3: pin names not known; wires that end beside it: EX_IR
  Multiplexer #(.select(1), .width(32), .disabled("Z"), .enable("false")) multiplexer_3 (
    .in0(multiplexer_6_out), .in1(multiplexer_4_out), .out(multiplexer_3_out), .sel(EX_PredictErr));
  Multiplexer #(.select(1), .width(32), .disabled("Z"), .enable("false")) multiplexer_4 (
    .in0(adder_3_out), .in1(BranchAddr), .out(multiplexer_4_out), .sel(or_3_out));
  Hex_Digit_Display hex_digit_display_8 (.value(LedData[3:0]));  // open: dp
  Multiplexer #(.select(1), .width(32), .disabled("Z"), .enable("false")) multiplexer_5 (
    .in0(multiplexer_3_out), .in1(and_2_out), .out(multiplexer_5_out), .sel(Jalr));
  assign and_2_out = Jalr_Addr & 32'hfffffffe;  // AND_Gate and_2, 32 bits wide
  not not_1 (not_1_out, Load_Use);
  // Probe on \总周期数 
  // Probe on M_PC[19:0]
  // RiscV_Probe riscv_probe_4: pin names not known; wires that end beside it: MEM_IR
  or or_2 (or_2_out, Branch, Jal);
  or or_3 (or_3_out, Jal, BranchTaken);
  Register #(.width(32), .trigger("rising"), .Select("low")) PC (
    .D(multiplexer_5_out), .en(and_3_out), .Q(IF_PC), .clk(CLK), .clr(RST));
  and and_3 (and_3_out, not_1_out, not_2_out);
  not not_2 (not_2_out, halt);
  // Probe on \总周期数 
  // Probe on \无条件分支数 
  // Probe on \条件分支成功数 
  // Probe on \插入气泡数 
  // Probe on \LoadUse次数 
  // Probe on IF_PC[11:0]
  // Probe on WB_PC[19:0]
  // RiscV_Probe riscv_probe_5: pin names not known; wires that end beside it: WB_IR
  or or_4 (or_4_out, BranchTaken, Jal, Jalr);
  BHT bht_1 (
    .Clk(CLK), .EX_Branch(or_2_out), .PC(IF_PC), .EX_PC(EX_PC), .EX_BranchAddr(BranchAddr),
    .EX_Branched(or_3_out), .JumpAddr(JumpAddr), .PredictJump(PredictJump));
  // Probe on ID_PC[11:0]
  // Probe on EX_PC[11:0]
  Comparator #(.width(1), .mode("twosComplement")) comparator_1 (
    .a(or_4_out), .b(EX_PredictJump), .eq(comparator_1_eq));  // open: gt, lt
  Multiplexer #(.select(1), .width(32), .disabled("Z"), .enable("false")) multiplexer_6 (
    .in0(IF_PC_4), .in1(JumpAddr), .out(multiplexer_6_out), .sel(PredictJump));
  ROM #(.addrWidth(10), .dataWidth(32), .Select("high")) rom_1 (.addr(IF_PC[11:2]), .data(IF_IR));
  Adder #(.width(32)) adder_4 (.a(IF_PC), .b(32'h4), .out(IF_PC_4));  // open: cin, cout
  // Probe on M_PC[11:0]
  D_Flip_Flop #(.trigger("high"), .Pre_Clr_Positions("LEGACY"), .NegatePresetClear("false"), .enable("true"), .NewFFLayout("false")) d_ff_1 (.Q(d_ff_1_q));  // open: clk, D, Qn, preset, en, reset
  // Probe on 13'hc
  or or_5 (or_5_out, RST, EX_PredictErr);
  not not_3 (EX_PredictErr, comparator_1_eq);
  not not_4 (not_4_out, Load_Use);
  and and_4 (and_4_out, not_4_out, en);
  // Probe on WB_PC[11:0]
  Comparator #(.width(13), .mode("twosComplement")) comparator_2 (
    .a(CNT_num), .b(13'hc), .eq(comparator_2_eq), .lt(comparator_2_lt));  // open: gt
  Clock #(.highDuration(1), .lowDuration(1)) clock_2 (.out(clock_2_out));
  IF_ID if_id_1 (
    .PCin(IF_PC), .IRin(IF_IR), .PCout(ID_PC),
    .IRout({ID_IR[31], ID_Funct[4], ID_IR[29:26], ID_Funct[3], ID_IR[24:15], ID_Funct[2:0], ID_IR[11:0]}),
    .RST(or_5_out), .EN_H(and_4_out), .CLK(CLK), .PredictJumpin(PredictJump),
    .PredictJumpout(if_id_1_predictjumpout));
  nand nand_1 (nand_1_out, d_ff_1_q, comparator_2_eq);
  Counter #(.width(13), .max('h1fff), .ongoal("stay"), .trigger("rising"), .behavior("old")) counter_2 (
    .count(comparator_2_lt), .Q(CNT_num), .clk(clock_2_out));  // open: load, D, carry, clr, preset
  assign controlled_buffer_1_out = nand_1_out ? clock_2_out : 1'bz;  // Controlled_Buffer controlled_buffer_1
  \单周期硬布线控制器  \u_单周期硬布线控制器_1  (
    .Funct(ID_Funct), .OP(ID_IR[6:2]), .ALU_OP(\单周期硬布线控制器_1_alu_op ), .MemToReg(\单周期硬布线控制器_1_memtoreg ),
    .MemWrite(\单周期硬布线控制器_1_memwrite ), .ALU_SRC(\单周期硬布线控制器_1_alu_src ), .RegWrite(\单周期硬布线控制器_1_regwrite ),
    .ecall(ID_ecall), .S_type(\单周期硬布线控制器_1_s_type ), .Jalr(\单周期硬布线控制器_1_jalr ), .Beq(\单周期硬布线控制器_1_beq ),
    .JAL(\单周期硬布线控制器_1_jal ), .Bne(\单周期硬布线控制器_1_bne ), .U_type(\单周期硬布线控制器_1_u_type ),
    .BGEU(\单周期硬布线控制器_1_bgeu ), .LHU(\单周期硬布线控制器_1_lhu ));  // open: URET, CSRRSI, CSRRCI
  Multiplexer #(.select(1), .width(5), .disabled("Z"), .enable("false")) multiplexer_7 (
    .in0(ID_IR[19:15]), .in1(5'b10001), .out(ID_R1_num), .sel(ID_ecall));
  Multiplexer #(.select(1), .width(5), .disabled("Z"), .enable("false")) multiplexer_8 (
    .in0(ID_IR[24:20]), .in1(5'b01010), .out(ID_R2_num), .sel(ID_ecall));
  assign bit_extender_1_out = {{20{ID_IR[31]}}, {ID_IR[31], ID_Funct[4], ID_IR[29:26], ID_Funct[3], ID_IR[24:20]}};  // Bit_Extender bit_extender_1
  assign bit_extender_2_out = {{20{ID_IR[31]}}, {ID_IR[31], ID_Funct[4], ID_IR[29:26], ID_Funct[3], ID_IR[11:7]}};  // Bit_Extender bit_extender_2
  Shifter #(.width(12), .shift("ll")) shifter_1 (
    .in({ID_IR[31], ID_IR[7], ID_Funct[4], ID_IR[29:26], ID_Funct[3], ID_IR[11:8]}), .\dist (4'b0001),
    .out(shifter_1_out));
  Shifter #(.width(20), .shift("ll")) shifter_2 (
    .in({ID_IR[31], ID_IR[19:15], ID_Funct[2:0], ID_IR[20], ID_Funct[4], ID_IR[29:26], ID_Funct[3], ID_IR[24:21]}),
    .\dist (5'b00001), .out(shifter_2_out));
  Pull_Resistor #(.pull(1)) pull_resistor_1 (.node(controlled_buffer_1_out));
  assign bit_extender_3_out = {{20{shifter_1_out[11]}}, shifter_1_out};  // Bit_Extender bit_extender_3
  assign bit_extender_4_out = {{12{shifter_2_out[19]}}, shifter_2_out};  // Bit_Extender bit_extender_4
  not not_5 (not_5_out, halt);
  Counter #(.width(16), .max('hffff), .ongoal("wrap"), .trigger("rising"), .behavior("new")) counter_3 (
    .count(not_5_out), .Q(\总周期数 ), .clk(CLK), .clr(RST));  // open: load, D, carry, preset, down
  not not_6 (not_6_out, CLK);
  Regifile regifile_1 (
    .Din(RDin), .Clk(not_6_out), .R1(ID_R1), .R2(ID_R2), .WE(RegWrite), .W_num(W_num), .R1_num(ID_R1_num),
    .R2_num(ID_R2_num));
  Counter #(.width(16), .max('hffff), .ongoal("wrap"), .trigger("rising"), .behavior("new")) counter_4 (
    .count(Branch), .Q(\条件分支成功数 ), .clk(CLK), .clr(RST));  // open: load, D, carry, preset, down
  or or_6 (or_6_out, or_5_out, Load_Use);
  ID_EX id_ex_1 (
    .PCin(ID_PC), .PCout(EX_PC),
    .IRin({ID_IR[31], ID_Funct[4], ID_IR[29:26], ID_Funct[3], ID_IR[24:15], ID_Funct[2:0], ID_IR[11:0]}),
    .IRout(EX_IR), .RST(or_6_out), .EN_H(en), .CLK(CLK), .Imm_I_in(bit_extender_1_out),
    .Imm_I_out(id_ex_1_imm_i_out), .Imm_S_in(bit_extender_2_out), .Imm_S_out(id_ex_1_imm_s_out),
    .Imm_B_in(bit_extender_3_out), .Imm_B_out(imm_B), .Imm_J_in(bit_extender_4_out), .Imm_J_out(imm_J),
    .Imm_U_in({ID_IR[31], ID_Funct[4], ID_IR[29:26], ID_Funct[3], ID_IR[24:15], ID_Funct[2:0], {12{1'b0}}}),
    .Imm_U_out(id_ex_1_imm_u_out), .R1in(ID_R1), .R1out(id_ex_1_r1out), .R2in(ID_R2), .R2out(id_ex_1_r2out),
    .Lhuin(\单周期硬布线控制器_1_lhu ), .Lhuout(id_ex_1_lhuout), .Jalrin(\单周期硬布线控制器_1_jalr ), .Jalrout(Jalr),
    .Jalout(Jal), .Jalin(\单周期硬布线控制器_1_jal ), .Beqin(\单周期硬布线控制器_1_beq ), .Beqout(id_ex_1_beqout),
    .Bgeuin(\单周期硬布线控制器_1_bgeu ), .Bgeuout(id_ex_1_bgeuout), .Bnein(\单周期硬布线控制器_1_bne ),
    .Bneout(id_ex_1_bneout), .MemToRegin(\单周期硬布线控制器_1_memtoreg ), .MemToRegout(id_ex_1_memtoregout),
    .MemWritein(\单周期硬布线控制器_1_memwrite ), .MemWriteout(id_ex_1_memwriteout),
    .AluSrcBin(\单周期硬布线控制器_1_alu_src ), .AluSrcBout(id_ex_1_alusrcbout), .RegWritein(\单周期硬布线控制器_1_regwrite ),
    .RegWriteout(EX_RegWrite_num), .U_Typein(\单周期硬布线控制器_1_u_type ), .U_Tpyeout(id_ex_1_u_tpyeout),
    .AluOpin(\单周期硬布线控制器_1_alu_op ), .AluOpout(id_ex_1_aluopout), .S_Typein(\单周期硬布线控制器_1_s_type ),
    .S_Tpyeout(id_ex_1_s_tpyeout), .Ecallin(ID_ecall), .Ecallout(EX_ecall), .W_in(ID_IR[11:7]),
    .W_out(EX_W_num), .R1Forwardin(R1Forward), .R1Forwardout(id_ex_1_r1forwardout), .R2Forwardin(R2Forward),
    .R2Forwardout(id_ex_1_r2forwardout), .PredictJumpin(if_id_1_predictjumpout),
    .PredictJumpout(EX_PredictJump));  // open: Uretin, Uretout
  or or_7 (or_7_out, Jal, Jalr);
  Counter #(.width(16), .max('hffff), .ongoal("wrap"), .trigger("rising"), .behavior("new")) counter_5 (
    .count(or_7_out), .Q(\无条件分支数 ), .clk(CLK), .clr(RST));  // open: load, D, carry, preset, down
  or or_8 (Branch, id_ex_1_beqout, id_ex_1_bneout, id_ex_1_bgeuout);
  Multiplexer #(.select(2), .width(32), .disabled("Z"), .enable("false")) multiplexer_9 (
    .in0(id_ex_1_r1out), .in1(RDin), .in2(RT), .out(EX_R1), .sel(id_ex_1_r1forwardout));  // open: in3
  Multiplexer #(.select(2), .width(32), .disabled("Z"), .enable("false")) multiplexer_10 (
    .in0(id_ex_1_r2out), .in1(RDin), .in2(RT), .out(EX_R2), .sel(id_ex_1_r2forwardout));  // open: in3
  Multiplexer #(.select(1), .width(32), .disabled("Z"), .enable("false")) multiplexer_11 (
    .in0(id_ex_1_imm_i_out), .in1(id_ex_1_imm_s_out), .out(multiplexer_11_out), .sel(id_ex_1_s_tpyeout));
  Comparator #(.width(32), .mode("twosComplement")) comparator_3 (
    .a(EX_R1), .b(32'ha), .eq(comparator_3_eq));  // open: gt, lt
  not not_7 (not_7_out, equal);
  ALU alu_1 (
    .X(EX_R1), .Y(multiplexer_12_out), .AluOP(id_ex_1_aluopout), .Equal(equal), .Result(Jalr_Addr),
    .out_4(MoreAndEqu));  // open: Result_2, out_6
  Multiplexer #(.select(1), .width(32), .disabled("Z"), .enable("false")) multiplexer_12 (
    .in0(EX_R2), .in1(multiplexer_11_out), .out(multiplexer_12_out), .sel(id_ex_1_alusrcbout));
  and and_5 (and_5_out, EX_ecall, not_8_out);
  not not_8 (not_8_out, comparator_3_eq);
  and and_6 (and_6_out, comparator_3_eq, EX_ecall);
  and and_7 (and_7_out, id_ex_1_beqout, equal);
  or or_9 (BranchTaken, and_7_out, and_8_out, and_9_out);
  and and_8 (and_8_out, not_7_out, id_ex_1_bneout);
  and and_9 (and_9_out, MoreAndEqu, id_ex_1_bgeuout);
  Register #(.width(32), .trigger("rising"), .Select("low")) register_1 (
    .D(EX_R2), .en(and_5_out), .Q(LedData), .clk(CLK), .clr(RST));
  Adder #(.width(16)) adder_5 (.a(\条件分支成功数 ), .b(\无条件分支数 ), .out(adder_5_out));  // open: cin, cout
  not not_9 (not_9_out, halt);
  and and_10 (and_10_out, not_9_out, Load_Use);
  EX_MEM ex_mem_1 (
    .PCin(EX_PC), .Lhuin(id_ex_1_lhuout), .PCout(M_PC), .Lhuout(ex_mem_1_lhuout), .Jalrin(Jalr),
    .Jalrout(ex_mem_1_jalrout), .IRin(EX_IR), .IRout(MEM_IR), .Jalin(Jal), .Jalout(ex_mem_1_jalout),
    .MemToRegin(id_ex_1_memtoregout), .MemToRegout(MemToReg), .MemWritein(id_ex_1_memwriteout),
    .MemWriteout(MemWrite), .Imm_U_in(id_ex_1_imm_u_out), .Imm_U_out(ex_mem_1_imm_u_out),
    .Resultin(Jalr_Addr), .Resultout(RT), .RegWritein(EX_RegWrite_num), .RegWriteout(MEM_RegWrite_num),
    .U_Typein(id_ex_1_u_tpyeout), .U_Tpyeout(ex_mem_1_u_tpyeout), .Haltin(and_6_out),
    .Haltout(ex_mem_1_haltout), .W_in(EX_W_num), .W_out(MEM_W_num), .RST(RST), .EN_H(en), .CLK(CLK),
    .WMdatain(EX_R2), .WMdataout(MDin));  // open: Uretin, Uretout
  Shifter #(.width(16), .shift("ll")) shifter_3 (.in(adder_5_out), .\dist (4'b0001), .out(shifter_3_out));
  Counter #(.width(16), .max('hffff), .ongoal("wrap"), .trigger("rising"), .behavior("new")) counter_6 (
    .count(and_10_out), .Q(\LoadUse次数 ), .clk(CLK), .clr(RST));  // open: load, D, carry, preset, down
  Adder #(.width(16)) adder_6 (.a(shifter_3_out), .b(\LoadUse次数 ), .out(\插入气泡数 ));  // open: cin, cout
  RAM #(.addrWidth(10), .dataWidth(32), .bus("separate"), .Select("high")) ram_1 (
    .addr(RT[11:2]), .din(MDin), .data(ram_1_data), .str(MemWrite), .clk(CLK), .ld(MemToReg), .clr(RST));  // open: sel
  MEM_WB mem_wb_1 (
    .Lhuin(ex_mem_1_lhuout), .PCin(M_PC), .Jalrin(ex_mem_1_jalrout), .Jalin(ex_mem_1_jalout), .IRin(MEM_IR),
    .MemToRegin(MemToReg), .Imm_U_in(ex_mem_1_imm_u_out), .RegWritein(MEM_RegWrite_num), .AluResultin(RT),
    .U_Typein(ex_mem_1_u_tpyeout), .RMdatain(ram_1_data), .Haltin(ex_mem_1_haltout), .W_in(MEM_W_num),
    .Lhuout(mem_wb_1_lhuout), .PCout(WB_PC), .Jalrout(mem_wb_1_jalrout), .Jalout(mem_wb_1_jalout),
    .IRout(WB_IR), .MemToRegout(mem_wb_1_memtoregout), .Imm_U_out(mem_wb_1_imm_u_out),
    .RegWriteout(RegWrite), .AluResultout(mem_wb_1_aluresultout), .U_Tpyeout(mem_wb_1_u_tpyeout),
    .RMdataout(mem_wb_1_rmdataout), .Haltout(mem_wb_1_haltout), .W_out(W_num), .RST(RST), .EN_H(en),
    .CLK(CLK), .Xin(RT[1]), .Xout(mem_wb_1_xout));  // open: Uretin, Uretout
  and and_11 (halt, mem_wb_1_haltout, ~Go);  // AND_Gate
  Adder #(.width(32)) adder_7 (.a(32'h4), .b(WB_PC), .out(WB_PC_4));  // open: cin, cout
  or or_10 (or_10_out, mem_wb_1_jalrout, mem_wb_1_jalout, mem_wb_1_u_tpyeout);
  Multiplexer #(.select(1), .width(16), .disabled("Z"), .enable("false")) multiplexer_13 (
    .in0(mem_wb_1_rmdataout[15:0]), .in1(mem_wb_1_rmdataout[31:16]), .out(multiplexer_13_out),
    .sel(mem_wb_1_xout));
  Adder #(.width(32)) adder_8 (.a(WB_PC), .b(mem_wb_1_imm_u_out), .out(adder_8_out));  // open: cin, cout
  not not_10 (en, halt);
  Multiplexer #(.select(1), .width(32), .disabled("Z"), .enable("false")) multiplexer_14 (
    .in0(mem_wb_1_rmdataout), .in1(bit_extender_5_out), .out(multiplexer_14_out), .sel(mem_wb_1_lhuout));
  assign bit_extender_5_out = {{16{1'b0}}, multiplexer_13_out};  // Bit_Extender bit_extender_5
  Multiplexer #(.select(1), .width(32), .disabled("Z"), .enable("false")) multiplexer_15 (
    .in0(WB_PC_4), .in1(adder_8_out), .out(multiplexer_15_out), .sel(mem_wb_1_u_tpyeout));
  Multiplexer #(.select(1), .width(32), .disabled("Z"), .enable("false")) multiplexer_16 (
    .in0(mem_wb_1_aluresultout), .in1(multiplexer_14_out), .out(multiplexer_16_out),
    .sel(mem_wb_1_memtoregout));
  Multiplexer #(.select(1), .width(32), .disabled("Z"), .enable("false")) multiplexer_17 (
    .in0(multiplexer_16_out), .in1(multiplexer_15_out), .out(RDin), .sel(or_10_out));

  // Other names for the same wires on the sheet: ID_RD_num[4:0] = ID_IR[11:7]; ID_IR (some bits) = ID_Funct;
  //   ID_OP[4:0] = ID_IR[6:2]; MEM_PC[31:0] = M_PC; WD[31:0] = RDin; WriteBackData[31:0] = RDin

  // Notes on the sheet:
  //   中断源
  //   中断等待指示
  //   数码管输出
  //   指令存储器
  //   控制位
  //   指令字
  //   contents of rom_1 (hex, n*v repeats v):
  //   100493 100006f 100493 200913 300993 100006f 100493 200913 300993 100006f 100493 200913 300993
  //   100006f 100493 200913 300993 424000ef 100413 100493 1f49493 900533 2200893 73 24d493 48463 fedff06f
  //   900533 2200893 73 100493 249493 900533 2200893 73 48463 fedff06f 100493 1f49493 900533 2200893 73
  //   4034d493 900533 2200893 73 4044d493 900533 2200893 73 4044d493 900533 2200893 73 4044d493 900533
  //   2200893 73 4044d493 900533 2200893 73 4044d493 900533 2200893 73 4044d493 900533 2200893 73 4044d493
  //   900533 2200893 73 100413 1f41993 41f9d993 433 c00913 300b13 140413 f47413 800293 100313 499993
  //   89e9b3 1300533 2200893 73 406282b3 fe0294e3 140413 f00f93 1f47433 1c41413 800293 100313 49d993
  //   89e9b3 1300533 2200893 73 406282b3 fe0294e3 1c45413 406b0b33 b0463 f95ff06f 2b3 fff2c293 829293
  //   ff2e293 500533 2200893 73 fff00413 493 84a023 140413 448493 84a023 140413 448493 84a023 140413
  //   448493 84a023 140413 448493 84a023 140413 448493 84a023 140413 448493 84a023 140413 448493 84a023
  //   140413 448493 84a023 140413 448493 84a023 140413 448493 84a023 140413 448493 84a023 140413 448493
  //   84a023 140413 448493 84a023 140413 448493 84a023 140413 448493 84a023 140413 448493 140413 433
  //   3c00493 42983 4aa03 149a2b3 28663 134a023 1442023 ffc48493 fe9412e3 800533 2200893 73 440413 3c00493
  //   fc9416e3 a00893 73 100293 300313 800493 849493 7648493 1449493 900533 2200893 73 800e13 54d4b3
  //   64d4b3 900533 2200893 73 fffe0e13 fe0e14e3 a00893 73 13 430497 900533 2200893 73 430497 900533
  //   2200893 73 430497 900533 2200893 73 430497 900533 2200893 73 430497 900533 2200893 73 430497 900533
  //   2200893 73 430497 900533 2200893 73 430497 900533 2200893 73 a00893 73 313 1000e13 8400493 849493
  //   8348493 400913 891913 490913 849493 8248493 849493 8148493 891913 490913 891913 490913 932023
  //   12484b3 430313 fffe0e13 fe0e18e3 2000e13 313 35483 900533 2200893 73 230313 fffe0e13 fe0e14e3 a00893
  //   73 f00493 100913 409909b3 900533 2200893 73 fff48493 ff29f6e3 a00893 73 a00893 73 413 140413 800533
  //   2200893 73 240413 800533 2200893 73 340413 800533 2200893 73 440413 800533 2200893 73 540413 800533
  //   2200893 73 640413 800533 2200893 73 740413 800533 2200893 73 840413 800533 2200893 2200893 73 8067
  //   流水调试日志用
  //   暂停节拍，不能为0
  //   戳工具置1进入计数暂停模式，ctrl+k时钟自动运行到对应节拍暂停
  //   ctrl+k关闭时钟连续运行，将控制位置零，进入单步调试模式调试
  //   rs1
  //   rs2
  //   rd
  //   可计数暂停的时钟源
  //   Beq
  //   Bgeu
  //   Bne
  //   MemToReg
  //   MemWrite
  //   AluOP
  //   AluSrcB
  //   RegWrite
  //   U_Type
  //   S_Type
  //   为方便自动评测，需要输出流水线各段保存的PC值，注意是PC不是PC+4，另外ID段寄存器写入信息，Mem段内存写入信息也要输出
  //   数据存储器
endmodule

// BTB
module BTB (
  input  CLK,
  input  EX_Branch,
  input  [31:0] EX_PC,
  input  [31:0] EX_BranchAddr,
  input  [31:0] PC,
  input  EX_BranchTaken,
  output PredictJump,
  output [31:0] JumpAddr,
  output [1:0] JumpState,
  output IF_Hit,
  output EX_Hit
);

  wire and_1_out, comparator_1_eq, comparator_2_eq, comparator_3_eq, comparator_4_eq, comparator_5_eq,
       comparator_6_eq, comparator_7_eq, comparator_8_eq, comparator_9_eq, comparator_10_eq,
       comparator_11_eq, comparator_12_eq, comparator_13_eq, comparator_14_eq, comparator_15_eq,
       comparator_16_eq, EX_Miss, EX_Write0, EX_Write1, EX_Write2, EX_Write3, EX_Write4, EX_Write5,
       EX_Write6, EX_Write7, full, L0, L1, L2, L3, L4, L5, L6, L7, Miss, not_1_out, not_2_out, not_3_out,
       not_4_out, not_5_out, not_6_out, not_7_out, not_8_out, V0, V1, V2, V3, V4, V5, V6, V7, Write0, Write1,
       Write2, Write3, Write4, Write5, Write6, Write7;
  wire [0:0] controlled_buffer_9_out, controlled_buffer_10_out, controlled_buffer_11_out,
       controlled_buffer_12_out, controlled_buffer_13_out, controlled_buffer_14_out,
       controlled_buffer_15_out, controlled_buffer_16_out;
  wire [1:0] adder_1_out, multiplexer_2_out, multiplexer_3_out, multiplexer_4_out, multiplexer_5_out,
       multiplexer_6_out, \分支预测历史位_2_q , \分支预测历史位_3_q , \分支预测历史位_4_q , \分支预测历史位_5_q , \分支预测历史位_6_q ,
       \分支预测历史位_7_q , \分支预测历史位_8_q , \分支预测历史位_q ;
  wire [2:0] max2_1_max_num, max2_2_max_num, max2_3_max_num, max2_4_max_num, max2_5_max_num, max2_6_max_num,
       max2_7_max_num, multiplexer_1_out, priority_encoder_1_out;
  wire [15:0] C0, C1, C2, C3, C4, C5, C6, C7, max2_1_max, max2_2_max, max2_3_max, max2_4_max, max2_5_max,
       max2_6_max;
  wire [31:0] Tag0, Tag1, Tag2, Tag3, Tag4, Tag5, Tag6, Tag7, \分支目标地址_2_q , \分支目标地址_3_q , \分支目标地址_4_q ,
       \分支目标地址_5_q , \分支目标地址_6_q , \分支目标地址_7_q , \分支目标地址_8_q , \分支目标地址_q ;

  Register #(.width(1), .trigger("rising"), .Select("low")) Valid (
    .D(1'b1), .en(Write0), .Q(V0), .clk(CLK));  // open: clr
  Register #(.width(1), .trigger("rising"), .Select("low")) Valid_2 (
    .D(1'b1), .en(Write1), .Q(V1), .clk(CLK));  // open: clr
  Register #(.width(1), .trigger("rising"), .Select("low")) Valid_3 (
    .D(1'b1), .en(Write2), .Q(V2), .clk(CLK));  // open: clr
  Register #(.width(1), .trigger("rising"), .Select("low")) Valid_4 (
    .D(1'b1), .en(Write3), .Q(V3), .clk(CLK));  // open: clr
  Register #(.width(1), .trigger("rising"), .Select("low")) Valid_5 (
    .D(1'b1), .en(Write4), .Q(V4), .clk(CLK));  // open: clr
  Register #(.width(1), .trigger("rising"), .Select("low")) Valid_6 (
    .D(1'b1), .en(Write5), .Q(V5), .clk(CLK));  // open: clr
  Register #(.width(1), .trigger("rising"), .Select("low")) Valid_7 (
    .D(1'b1), .en(Write6), .Q(V6), .clk(CLK));  // open: clr
  Register #(.width(1), .trigger("rising"), .Select("low")) Valid_8 (
    .D(1'b1), .en(Write7), .Q(V7), .clk(CLK));  // open: clr
  MAX2 max2_1 (.Y(C1), .X(C0), .Y_num(3'b001), .X_num(3'b000), .MAX(max2_1_max), .MAX_num(max2_1_max_num));
  MAX2 max2_2 (.Y(C3), .X(C2), .Y_num(3'b011), .X_num(3'b010), .MAX(max2_2_max), .MAX_num(max2_2_max_num));
  MAX2 max2_3 (.Y(C5), .X(C4), .Y_num(3'b101), .X_num(3'b100), .MAX(max2_3_max), .MAX_num(max2_3_max_num));
  MAX2 max2_4 (.Y(C7), .X(C6), .Y_num(3'b111), .X_num(3'b110), .MAX(max2_4_max), .MAX_num(max2_4_max_num));
  Register #(.width(32), .trigger("rising"), .Select("low")) \u_分支指令地址  (
    .D(EX_PC), .en(Write0), .Q(Tag0), .clk(CLK));  // open: clr
  Register #(.width(32), .trigger("rising"), .Select("low")) \u_分支指令地址_2  (
    .D(EX_PC), .en(Write1), .Q(Tag1), .clk(CLK));  // open: clr
  Register #(.width(32), .trigger("rising"), .Select("low")) \u_分支指令地址_3  (
    .D(EX_PC), .en(Write2), .Q(Tag2), .clk(CLK));  // open: clr
  Register #(.width(32), .trigger("rising"), .Select("low")) \u_分支指令地址_4  (
    .D(EX_PC), .en(Write3), .Q(Tag3), .clk(CLK));  // open: clr
  Register #(.width(32), .trigger("rising"), .Select("low")) \u_分支指令地址_5  (
    .D(EX_PC), .en(Write4), .Q(Tag4), .clk(CLK));  // open: clr
  Register #(.width(32), .trigger("rising"), .Select("low")) \u_分支指令地址_6  (
    .D(EX_PC), .en(Write5), .Q(Tag5), .clk(CLK));  // open: clr
  Register #(.width(32), .trigger("rising"), .Select("low")) \u_分支指令地址_7  (
    .D(EX_PC), .en(Write6), .Q(Tag6), .clk(CLK));  // open: clr
  Register #(.width(32), .trigger("rising"), .Select("low")) \u_分支指令地址_8  (
    .D(EX_PC), .en(Write7), .Q(Tag7), .clk(CLK));  // open: clr
  not not_1 (not_1_out, V0);
  not not_2 (not_2_out, V1);
  not not_3 (not_3_out, V2);
  not not_4 (not_4_out, V3);
  not not_5 (not_5_out, V4);
  not not_6 (not_6_out, V5);
  not not_7 (not_7_out, V6);
  not not_8 (not_8_out, V7);
  Priority_Encoder #(.select(3), .disabled("Z")) priority_encoder_1 (
    .in0(not_1_out), .in1(not_2_out), .in2(not_3_out), .in3(not_4_out), .in4(not_5_out), .in5(not_6_out),
    .in6(not_7_out), .in7(not_8_out), .out(priority_encoder_1_out), .en_out(full), .en_in(1'b1));  // open: gs
  MAX2 max2_5 (
    .Y(max2_2_max), .X(max2_1_max), .Y_num(max2_2_max_num), .X_num(max2_1_max_num), .MAX(max2_5_max),
    .MAX_num(max2_5_max_num));
  MAX2 max2_6 (
    .Y(max2_4_max), .X(max2_3_max), .Y_num(max2_4_max_num), .X_num(max2_3_max_num), .MAX(max2_6_max),
    .MAX_num(max2_6_max_num));
  Counter #(.width(16), .max('hffff), .ongoal("wrap"), .trigger("rising"), .behavior("new")) \u_淘汰记数  (
    .Q(C0), .clk(CLK), .clr(L0));  // open: load, D, count, carry, preset, down
  Counter #(.width(16), .max('hffff), .ongoal("wrap"), .trigger("rising"), .behavior("new")) \u_淘汰记数_2  (
    .Q(C1), .clk(CLK), .clr(L1));  // open: load, D, count, carry, preset, down
  Counter #(.width(16), .max('hffff), .ongoal("wrap"), .trigger("rising"), .behavior("new")) \u_淘汰记数_3  (
    .Q(C2), .clk(CLK), .clr(L2));  // open: load, D, count, carry, preset, down
  Counter #(.width(16), .max('hffff), .ongoal("wrap"), .trigger("rising"), .behavior("new")) \u_淘汰记数_4  (
    .Q(C3), .clk(CLK), .clr(L3));  // open: load, D, count, carry, preset, down
  Counter #(.width(16), .max('hffff), .ongoal("wrap"), .trigger("rising"), .behavior("new")) \u_淘汰记数_5  (
    .Q(C4), .clk(CLK), .clr(L4));  // open: load, D, count, carry, preset, down
  Counter #(.width(16), .max('hffff), .ongoal("wrap"), .trigger("rising"), .behavior("new")) \u_淘汰记数_6  (
    .Q(C5), .clk(CLK), .clr(L5));  // open: load, D, count, carry, preset, down
  Counter #(.width(16), .max('hffff), .ongoal("wrap"), .trigger("rising"), .behavior("new")) \u_淘汰记数_7  (
    .Q(C6), .clk(CLK), .clr(L6));  // open: load, D, count, carry, preset, down
  Counter #(.width(16), .max('hffff), .ongoal("wrap"), .trigger("rising"), .behavior("new")) \u_淘汰记数_8  (
    .Q(C7), .clk(CLK), .clr(L7));  // open: load, D, count, carry, preset, down
  MAX2 max2_7 (
    .Y(max2_6_max), .X(max2_5_max), .Y_num(max2_6_max_num), .X_num(max2_5_max_num), .MAX_num(max2_7_max_num));  // open: MAX
  and and_1 (and_1_out, EX_Branch, EX_Miss);
  Multiplexer #(.select(1), .width(3), .disabled("Z"), .enable("false")) multiplexer_1 (
    .in0(priority_encoder_1_out), .in1(max2_7_max_num), .out(multiplexer_1_out), .sel(full));
  Register #(.width(32), .trigger("rising"), .Select("low")) \u_分支目标地址  (
    .D(EX_BranchAddr), .en(Write0), .Q(\分支目标地址_q ), .clk(CLK));  // open: clr
  Register #(.width(32), .trigger("rising"), .Select("low")) \u_分支目标地址_2  (
    .D(EX_BranchAddr), .en(Write1), .Q(\分支目标地址_2_q ), .clk(CLK));  // open: clr
  Register #(.width(32), .trigger("rising"), .Select("low")) \u_分支目标地址_3  (
    .D(EX_BranchAddr), .en(Write2), .Q(\分支目标地址_3_q ), .clk(CLK));  // open: clr
  Register #(.width(32), .trigger("rising"), .Select("low")) \u_分支目标地址_4  (
    .D(EX_BranchAddr), .en(Write3), .Q(\分支目标地址_4_q ), .clk(CLK));  // open: clr
  Register #(.width(32), .trigger("rising"), .Select("low")) \u_分支目标地址_5  (
    .D(EX_BranchAddr), .en(Write4), .Q(\分支目标地址_5_q ), .clk(CLK));  // open: clr
  Register #(.width(32), .trigger("rising"), .Select("low")) \u_分支目标地址_6  (
    .D(EX_BranchAddr), .en(Write5), .Q(\分支目标地址_6_q ), .clk(CLK));  // open: clr
  Register #(.width(32), .trigger("rising"), .Select("low")) \u_分支目标地址_7  (
    .D(EX_BranchAddr), .en(Write6), .Q(\分支目标地址_7_q ), .clk(CLK));  // open: clr
  Register #(.width(32), .trigger("rising"), .Select("low")) \u_分支目标地址_8  (
    .D(EX_BranchAddr), .en(Write7), .Q(\分支目标地址_8_q ), .clk(CLK));  // open: clr
  Demultiplexer #(.select(3), .width(1), .tristate("false"), .disabled("Z"), .enable("false")) demultiplexer_1 (
    .out0(Write0), .out1(Write1), .out2(Write2), .out3(Write3), .out4(Write4), .out5(Write5), .out6(Write6),
    .out7(Write7), .in(and_1_out), .sel(multiplexer_1_out));
  assign JumpAddr = L0 ? \分支目标地址_q  : 32'bz;  // Controlled_Buffer controlled_buffer_1
  assign JumpAddr = L1 ? \分支目标地址_2_q  : 32'bz;  // Controlled_Buffer controlled_buffer_2
  assign JumpAddr = L2 ? \分支目标地址_3_q  : 32'bz;  // Controlled_Buffer controlled_buffer_3
  assign JumpAddr = L3 ? \分支目标地址_4_q  : 32'bz;  // Controlled_Buffer controlled_buffer_4
  assign JumpAddr = L4 ? \分支目标地址_5_q  : 32'bz;  // Controlled_Buffer controlled_buffer_5
  assign JumpAddr = L5 ? \分支目标地址_6_q  : 32'bz;  // Controlled_Buffer controlled_buffer_6
  assign JumpAddr = L6 ? \分支目标地址_7_q  : 32'bz;  // Controlled_Buffer controlled_buffer_7
  assign JumpAddr = L7 ? \分支目标地址_8_q  : 32'bz;  // Controlled_Buffer controlled_buffer_8
  assign {PredictJump, controlled_buffer_9_out[0]} = L0 ? \分支预测历史位_q  : 2'bz;  // Controlled_Buffer controlled_buffer_9
  Register #(.width(2), .trigger("rising"), .Select("low")) \u_分支预测历史位  (
    .D(JumpState), .en(Write0), .Q(\分支预测历史位_q ), .clk(CLK));  // open: clr
  assign {PredictJump, controlled_buffer_10_out[0]} = L1 ? \分支预测历史位_2_q  : 2'bz;  // Controlled_Buffer controlled_buffer_10
  Register #(.width(2), .trigger("rising"), .Select("low")) \u_分支预测历史位_2  (
    .D(JumpState), .en(Write1), .Q(\分支预测历史位_2_q ), .clk(CLK));  // open: clr
  Register #(.width(2), .trigger("rising"), .Select("low")) \u_分支预测历史位_3  (
    .D(JumpState), .en(Write2), .Q(\分支预测历史位_3_q ), .clk(CLK));  // open: clr
  assign {PredictJump, controlled_buffer_11_out[0]} = L2 ? \分支预测历史位_3_q  : 2'bz;  // Controlled_Buffer controlled_buffer_11
  Register #(.width(2), .trigger("rising"), .Select("low")) \u_分支预测历史位_4  (
    .D(JumpState), .en(Write3), .Q(\分支预测历史位_4_q ), .clk(CLK));  // open: clr
  assign {PredictJump, controlled_buffer_12_out[0]} = L3 ? \分支预测历史位_4_q  : 2'bz;  // Controlled_Buffer controlled_buffer_12
  Register #(.width(2), .trigger("rising"), .Select("low")) \u_分支预测历史位_5  (
    .D(JumpState), .en(Write4), .Q(\分支预测历史位_5_q ), .clk(CLK));  // open: clr
  assign {PredictJump, controlled_buffer_13_out[0]} = L4 ? \分支预测历史位_5_q  : 2'bz;  // Controlled_Buffer controlled_buffer_13
  Register #(.width(2), .trigger("rising"), .Select("low")) \u_分支预测历史位_6  (
    .D(JumpState), .en(Write5), .Q(\分支预测历史位_6_q ), .clk(CLK));  // open: clr
  assign {PredictJump, controlled_buffer_14_out[0]} = L5 ? \分支预测历史位_6_q  : 2'bz;  // Controlled_Buffer controlled_buffer_14
  Register #(.width(2), .trigger("rising"), .Select("low")) \u_分支预测历史位_7  (
    .D(JumpState), .en(Write6), .Q(\分支预测历史位_7_q ), .clk(CLK));  // open: clr
  assign {PredictJump, controlled_buffer_15_out[0]} = L6 ? \分支预测历史位_7_q  : 2'bz;  // Controlled_Buffer controlled_buffer_15
  assign {PredictJump, controlled_buffer_16_out[0]} = L7 ? \分支预测历史位_8_q  : 2'bz;  // Controlled_Buffer controlled_buffer_16
  Register #(.width(2), .trigger("rising"), .Select("low")) \u_分支预测历史位_8  (
    .D(JumpState), .en(Write7), .Q(\分支预测历史位_8_q ), .clk(CLK));  // open: clr
  Pull_Resistor #(.pull(0)) pull_resistor_1 (.node(PredictJump));
  Comparator #(.width(32), .mode("unsigned")) comparator_1 (.a(EX_PC), .b(Tag0), .eq(comparator_1_eq));  // open: gt, lt
  Comparator #(.width(32), .mode("unsigned")) comparator_2 (.a(EX_PC), .b(Tag1), .eq(comparator_2_eq));  // open: gt, lt
  Comparator #(.width(32), .mode("unsigned")) comparator_3 (.a(EX_PC), .b(Tag2), .eq(comparator_3_eq));  // open: gt, lt
  Comparator #(.width(32), .mode("unsigned")) comparator_4 (.a(EX_PC), .b(Tag3), .eq(comparator_4_eq));  // open: gt, lt
  Comparator #(.width(32), .mode("unsigned")) comparator_5 (.a(EX_PC), .b(Tag4), .eq(comparator_5_eq));  // open: gt, lt
  Comparator #(.width(32), .mode("unsigned")) comparator_6 (.a(EX_PC), .b(Tag5), .eq(comparator_6_eq));  // open: gt, lt
  Comparator #(.width(32), .mode("unsigned")) comparator_7 (.a(EX_PC), .b(Tag6), .eq(comparator_7_eq));  // open: gt, lt
  Comparator #(.width(32), .mode("unsigned")) comparator_8 (.a(EX_PC), .b(Tag7), .eq(comparator_8_eq));  // open: gt, lt
  and and_2 (EX_Write0, comparator_1_eq, V0);
  and and_3 (EX_Write1, comparator_2_eq, V1);
  and and_4 (EX_Write2, comparator_3_eq, V2);
  and and_5 (EX_Write3, comparator_4_eq, V3);
  and and_6 (EX_Write4, comparator_5_eq, V4);
  and and_7 (EX_Write5, comparator_6_eq, V5);
  and and_8 (EX_Write6, comparator_7_eq, V6);
  and and_9 (EX_Write7, comparator_8_eq, V7);
  Comparator #(.width(32), .mode("unsigned")) comparator_9 (.a(PC), .b(Tag0), .eq(comparator_9_eq));  // open: gt, lt
  Comparator #(.width(32), .mode("unsigned")) comparator_10 (.a(PC), .b(Tag1), .eq(comparator_10_eq));  // open: gt, lt
  Comparator #(.width(32), .mode("unsigned")) comparator_11 (.a(PC), .b(Tag2), .eq(comparator_11_eq));  // open: gt, lt
  Comparator #(.width(32), .mode("unsigned")) comparator_12 (.a(PC), .b(Tag3), .eq(comparator_12_eq));  // open: gt, lt
  Comparator #(.width(32), .mode("unsigned")) comparator_13 (.a(PC), .b(Tag4), .eq(comparator_13_eq));  // open: gt, lt
  Comparator #(.width(32), .mode("unsigned")) comparator_14 (.a(PC), .b(Tag5), .eq(comparator_14_eq));  // open: gt, lt
  Comparator #(.width(32), .mode("unsigned")) comparator_15 (.a(PC), .b(Tag6), .eq(comparator_15_eq));  // open: gt, lt
  Comparator #(.width(32), .mode("unsigned")) comparator_16 (.a(PC), .b(Tag7), .eq(comparator_16_eq));  // open: gt, lt
  or or_1 (EX_Hit, EX_Write0, EX_Write1, EX_Write2, EX_Write3, EX_Write4, EX_Write5, EX_Write6, EX_Write7);
  not not_9 (EX_Miss, EX_Hit);
  Multiplexer #(.select(1), .width(2), .disabled("Z"), .enable("false")) multiplexer_2 (
    .in0(2'b00), .in1(2'b01), .out(multiplexer_2_out), .sel(EX_BranchTaken));
  Multiplexer #(.select(1), .width(2), .disabled("Z"), .enable("false")) multiplexer_3 (
    .in0(2'b11), .in1(2'b01), .out(multiplexer_3_out), .sel(EX_BranchTaken));
  Multiplexer #(.select(1), .width(2), .disabled("Z"), .enable("false")) multiplexer_4 (
    .in0(2'b01), .in1(2'b00), .out(multiplexer_4_out), .sel(EX_BranchTaken));
  Multiplexer #(.select(1), .width(2), .disabled("Z"), .enable("false")) multiplexer_5 (
    .in0(2'b01), .in1(2'b11), .out(multiplexer_5_out), .sel(EX_BranchTaken));
  and and_10 (L0, comparator_9_eq, V0);
  and and_11 (L1, comparator_10_eq, V1);
  and and_12 (L2, comparator_11_eq, V2);
  and and_13 (L3, comparator_12_eq, V3);
  and and_14 (L4, comparator_13_eq, V4);
  and and_15 (L5, comparator_14_eq, V5);
  and and_16 (L6, comparator_15_eq, V6);
  and and_17 (L7, comparator_16_eq, V7);
  Multiplexer #(.select(2), .width(2), .disabled("Z"), .enable("false")) multiplexer_6 (
    .in0(multiplexer_2_out), .in1(multiplexer_3_out), .in2(multiplexer_4_out), .in3(multiplexer_5_out),
    .out(multiplexer_6_out), .sel(JumpState));
  Adder #(.width(2)) adder_1 (.a(multiplexer_6_out), .b(JumpState), .out(adder_1_out));  // open: cin, cout
  or or_2 (IF_Hit, L0, L1, L2, L3, L4, L5, L6, L7);
  Register #(.width(2), .trigger("rising"), .Select("low")) \u_双位预测状态_2位  (
    .D(adder_1_out), .en(EX_Branch), .Q(JumpState), .clk(CLK));  // open: clr
  not not_10 (Miss, IF_Hit);

  // Other names for the same wires on the sheet: Hit = IF_Hit

  // Notes on the sheet:
  //   IF段控制
  //   EX段控制
endmodule

// MAX2
module MAX2 (
  input  [15:0] Y,
  input  [15:0] X,
  input  [2:0] Y_num,
  input  [2:0] X_num,
  output [15:0] MAX,
  output [2:0] MAX_num
);

  wire comparator_1_eq, comparator_1_gt, or_1_out;

  Comparator #(.width(16), .mode("unsigned")) comparator_1 (
    .a(X), .b(Y), .gt(comparator_1_gt), .eq(comparator_1_eq));  // open: lt
  Multiplexer #(.select(1), .width(16), .disabled("Z"), .enable("false")) multiplexer_1 (
    .in0(Y), .in1(X), .out(MAX), .sel(or_1_out));
  or or_1 (or_1_out, comparator_1_gt, comparator_1_eq);
  Multiplexer #(.select(1), .width(3), .disabled("Z"), .enable("false")) multiplexer_2 (
    .in0(Y_num), .in1(X_num), .out(MAX_num), .sel(or_1_out));
endmodule

module \中断按键参考电路  (
  input  \同步清零信号 ,
  output \与中断屏蔽位与 
);

  wire \_1号中断_out , and_1_out, clock_1_out, d_ff_1_q, or_1_out, or_2_out;

  Clock #(.highDuration(1), .lowDuration(1)) clock_1 (.out(clock_1_out));
  Button \_1号中断  (.out(\_1号中断_out ));
  or or_1 (or_1_out, \与中断屏蔽位与 , d_ff_1_q);
  LED #(.active("true")) \_1号中断等待指示灯  (.in(or_1_out));
  D_Flip_Flop #(.trigger("rising"), .Pre_Clr_Positions("LEGACY"), .NegatePresetClear("false"), .enable("true"), .NewFFLayout("false")) d_ff_1 (
    .clk(\_1号中断_out ), .D(1'b1), .Q(d_ff_1_q), .reset(\与中断屏蔽位与 ));  // open: Qn, preset, en
  or or_2 (or_2_out, d_ff_1_q, \与中断屏蔽位与 );
  and and_1 (and_1_out, or_2_out, ~\同步清零信号 );  // AND_Gate
  D_Flip_Flop #(.trigger("rising"), .Pre_Clr_Positions("LEGACY"), .NegatePresetClear("false"), .enable("true"), .NewFFLayout("false")) IR1 (
    .clk(clock_1_out), .D(and_1_out), .Q(\与中断屏蔽位与 ));  // open: Qn, preset, en, reset

  // Notes on the sheet:
  //   中断信号采样参考电路
  //   Reset 
endmodule

module \单周期_单级中断  (
  input  IR1,
  input  IR2,
  input  IR3,
  output RegWrite,
  output MemWrite,
  output [31:0] PC,
  output [31:0] IR,
  output [31:0] RDin,
  output [31:0] MDin,
  output [31:0] LedData
);

  wire _1_out, _2_out, _3_out, AluSrcB, and_2_out, and_3_out, and_4_out, and_5_out, and_6_out, and_8_out,
       and_11_out, and_12_out, beq, bgeu, bne, Branch, CLK, comparator_1_eq, comparator_2_eq,
       comparator_3_eq, comparator_4_eq, comparator_5_eq, comparator_6_eq, comparator_7_eq, d_ff_1_q,
       d_ff_2_q, d_ff_3_q, decoder_1_out1, decoder_1_out2, decoder_1_out3, ecall, equal, Go, halt, IE_q,
       Inter1, Inter2, Inter3, Interr, Interrupt, IR1_t, IR2_t, IR3_t, IRA, IRB, IRC, jal, jalr, lhu,
       MemToReg, MoreAndEqu, not_1_out, not_2_out, not_3_out, not_4_out, not_5_out, not_6_out, or_1_out,
       or_6_out, or_7_out, or_11_out, or_13_out, or_14_out, PCToReg, Ret1, Ret2, Ret3, RST, S_type, U_type,
       uret, W1, W2, W3, \单周期硬布线控制器_1_ecall , \单周期硬布线控制器_1_uret ;
  wire [1:0] priority_encoder_1_out, \中断号_q ;
  wire [3:0] AluOP;
  wire [4:0] multiplexer_7_out, multiplexer_8_out;
  wire [11:0] imm12_B;
  wire [15:0] multiplexer_14_out, \分支成功数 , \总周期数 ;
  wire [19:0] imm20_J;
  wire [31:0] adder_1_out, adder_2_out, adder_3_out, and_1_out, bit_extender_1_out, bit_extender_2_out,
       bit_extender_3_out, bit_extender_4_out, bit_extender_5_out, EPC, InterAddr, MDout, multiplexer_1_out,
       multiplexer_2_out, multiplexer_4_out, multiplexer_5_out, multiplexer_9_out, multiplexer_11_out,
       multiplexer_12_out, nextPC, PC_4, R1, ram_1_data, Result, RPCin;

  Clock #(.highDuration(1), .lowDuration(1)) clock_1 (.out(CLK));
  Button _1 (.out(_1_out));
  Button _2 (.out(_2_out));
  Button _3 (.out(_3_out));
  Button \u_继续运行  (.out(Go));
  LED #(.active("true")) led_1 (.in(W1));
  LED #(.active("true")) led_2 (.in(W2));
  LED #(.active("true")) led_3 (.in(W3));
  Hex_Digit_Display hex_digit_display_1 (.value(LedData[31:28]));  // open: dp
  Comparator #(.width(16), .mode("twosComplement")) comparator_1 (
    .a(16'h23b), .b(\总周期数 ), .eq(comparator_1_eq));  // open: gt, lt
  Comparator #(.width(16), .mode("twosComplement")) comparator_2 (
    .a(\总周期数 ), .b(16'h1), .eq(comparator_2_eq));  // open: gt, lt
  Comparator #(.width(16), .mode("twosComplement")) comparator_3 (
    .a(\总周期数 ), .b(16'h4), .eq(comparator_3_eq));  // open: gt, lt
  Comparator #(.width(16), .mode("twosComplement")) comparator_4 (
    .a(\总周期数 ), .b(16'h7), .eq(comparator_4_eq));  // open: gt, lt
  Hex_Digit_Display hex_digit_display_2 (.value(LedData[23:20]));  // open: dp
  Hex_Digit_Display hex_digit_display_3 (.value(LedData[27:24]));  // open: dp
  or or_1 (or_1_out, comparator_1_eq, comparator_2_eq);
  assign IRA = or_1_out ? ~CLK : 1'bz;  // Controlled_Inverter controlled_inverter_1
  assign IRB = comparator_3_eq ? ~CLK : 1'bz;  // Controlled_Inverter controlled_inverter_2
  assign IRC = comparator_4_eq ? ~CLK : 1'bz;  // Controlled_Inverter controlled_inverter_3
  assign bit_extender_1_out = {{12{imm20_J[19]}}, imm20_J};  // Bit_Extender bit_extender_1
  Hex_Digit_Display hex_digit_display_4 (.value(LedData[19:16]));  // open: dp
  Hex_Digit_Display hex_digit_display_5 (.value(LedData[15:12]));  // open: dp
  Pull_Resistor #(.pull(0)) pull_resistor_1 (.node(IRA));
  Pull_Resistor #(.pull(0)) pull_resistor_2 (.node(IRB));
  Pull_Resistor #(.pull(0)) pull_resistor_3 (.node(IRC));
  Adder #(.width(32)) adder_1 (.a(bit_extender_1_out), .b(PC), .out(adder_1_out));  // open: cin, cout
  assign and_1_out = Result & 32'hfffffffe;  // AND_Gate and_1, 32 bits wide
  assign bit_extender_2_out = {{20{imm12_B[11]}}, imm12_B};  // Bit_Extender bit_extender_2
  Hex_Digit_Display hex_digit_display_6 (.value(LedData[7:4]));  // open: dp
  Hex_Digit_Display hex_digit_display_7 (.value(LedData[11:8]));  // open: dp
  // Probe on \总周期数 
  not not_1 (not_1_out, equal);
  Comparator #(.width(32), .mode("twosComplement")) comparator_5 (
    .a(R1), .b(32'ha), .eq(comparator_5_eq));  // open: gt, lt
  Multiplexer #(.select(1), .width(32), .disabled("Z"), .enable("false")) multiplexer_1 (
    .in0(PC_4), .in1(adder_1_out), .out(multiplexer_1_out), .sel(jal));
  Multiplexer #(.select(1), .width(32), .disabled("Z"), .enable("false")) multiplexer_2 (
    .in0(multiplexer_1_out), .in1(and_1_out), .out(multiplexer_2_out), .sel(jalr));
  Adder #(.width(32)) adder_2 (.a(bit_extender_2_out), .b(PC), .out(adder_2_out));  // open: cin, cout
  Hex_Digit_Display hex_digit_display_8 (.value(LedData[3:0]));  // open: dp
  and and_2 (and_2_out, beq, equal);
  or or_2 (Branch, and_2_out, and_3_out, and_4_out);
  and and_3 (and_3_out, not_1_out, bne);
  and and_4 (and_4_out, MoreAndEqu, bgeu);
  and and_5 (and_5_out, ecall, not_2_out);
  not not_2 (not_2_out, comparator_5_eq);
  and and_6 (and_6_out, comparator_5_eq, ecall);
  not not_3 (not_3_out, Go);
  Multiplexer #(.select(1), .width(32), .disabled("Z"), .enable("false")) multiplexer_3 (
    .in0(multiplexer_2_out), .in1(adder_2_out), .out(nextPC), .sel(Branch));
  D_Flip_Flop #(.trigger("rising"), .Pre_Clr_Positions("LEGACY"), .NegatePresetClear("false"), .enable("true"), .NewFFLayout("false")) d_ff_1 (
    .clk(IR1_t), .D(1'b1), .Q(d_ff_1_q), .reset(Inter1));  // open: Qn, preset, en
  or or_3 (W1, Inter1, d_ff_1_q);
  Counter #(.width(16), .max('hffff), .ongoal("wrap"), .trigger("rising"), .behavior("new")) counter_1 (
    .count(Branch), .Q(\分支成功数 ), .clk(CLK), .clr(RST));  // open: load, D, carry, preset, down
  Register #(.width(32), .trigger("rising"), .Select("low")) register_1 (
    .D(MDin), .en(and_5_out), .Q(LedData), .clk(CLK), .clr(RST));
  and and_7 (halt, and_6_out, not_3_out);
  Multiplexer #(.select(1), .width(32), .disabled("Z"), .enable("false")) multiplexer_4 (
    .in0(nextPC), .in1(InterAddr), .out(multiplexer_4_out), .sel(Interrupt));
  or or_4 (IR1_t, IR1, IRA);
  Register #(.width(32), .trigger("rising"), .Select("low")) u_PC (
    .D(multiplexer_5_out), .en(not_4_out), .Q(PC), .clk(CLK), .clr(RST));
  Multiplexer #(.select(1), .width(32), .disabled("Z"), .enable("false")) multiplexer_5 (
    .in0(multiplexer_4_out), .in1(EPC), .out(multiplexer_5_out), .sel(uret));
  not not_4 (not_4_out, halt);
  or or_5 (IR2_t, IR2, IRB);
  or or_6 (or_6_out, d_ff_1_q, Inter1);
  and and_8 (and_8_out, or_6_out, ~Ret1);  // AND_Gate
  not not_5 (not_5_out, halt);
  D_Flip_Flop #(.trigger("rising"), .Pre_Clr_Positions("LEGACY"), .NegatePresetClear("false"), .enable("true"), .NewFFLayout("false")) u_IR1 (
    .clk(CLK), .D(and_8_out), .Q(Inter1));  // open: Qn, preset, en, reset
  Counter #(.width(16), .max('hffff), .ongoal("wrap"), .trigger("rising"), .behavior("new")) counter_2 (
    .count(not_5_out), .Q(\总周期数 ), .clk(CLK), .clr(RST));  // open: load, D, carry, preset, down
  or or_7 (or_7_out, jal, jalr);
  Adder #(.width(32)) adder_3 (.a({IR[31:12], {12{1'b0}}}), .b(PC), .out(adder_3_out));  // open: cin, cout
  // RiscV_Probe riscv_probe_1: pin names not known; wires that end beside it: IR
  or or_8 (IR3_t, IR3, IRC);
  or or_9 (PCToReg, or_7_out, U_type);
  Multiplexer #(.select(1), .width(32), .disabled("Z"), .enable("false")) multiplexer_6 (
    .in0(PC_4), .in1(adder_3_out), .out(RPCin), .sel(U_type));
  ROM #(.addrWidth(10), .dataWidth(32), .Select("high")) rom_1 (.addr(PC[11:2]), .data(IR));
  Adder #(.width(32)) adder_4 (.a(PC), .b(32'h4), .out(PC_4));  // open: cin, cout
  or or_10 (W2, Inter2, d_ff_2_q);
  and and_9 (ecall, \单周期硬布线控制器_1_ecall , comparator_6_eq);
  Comparator #(.width(5), .mode("twosComplement")) comparator_6 (
    .a(IR[24:20]), .b({5{1'b0}}), .eq(comparator_6_eq));  // open: gt, lt
  and and_10 (uret, \单周期硬布线控制器_1_uret , comparator_7_eq);
  Comparator #(.width(5), .mode("twosComplement")) comparator_7 (
    .a(IR[24:20]), .b(5'b00010), .eq(comparator_7_eq));  // open: gt, lt
  \单周期硬布线控制器  \u_单周期硬布线控制器_1  (
    .Funct({IR[30], IR[25], IR[14:12]}), .OP(IR[6:2]), .ALU_OP(AluOP), .MemToReg(MemToReg),
    .MemWrite(MemWrite), .ALU_SRC(AluSrcB), .RegWrite(RegWrite), .ecall(\单周期硬布线控制器_1_ecall ),
    .S_type(S_type), .Jalr(jalr), .Beq(beq), .JAL(jal), .Bne(bne), .U_type(U_type), .BGEU(bgeu), .LHU(lhu),
    .URET(\单周期硬布线控制器_1_uret ));  // open: CSRRSI, CSRRCI
  Multiplexer #(.select(1), .width(5), .disabled("Z"), .enable("false")) multiplexer_7 (
    .in0(IR[19:15]), .in1(5'b10001), .out(multiplexer_7_out), .sel(ecall));
  Multiplexer #(.select(1), .width(5), .disabled("Z"), .enable("false")) multiplexer_8 (
    .in0(IR[24:20]), .in1(5'b01010), .out(multiplexer_8_out), .sel(ecall));
  Multiplexer #(.select(1), .width(32), .disabled("Z"), .enable("false")) multiplexer_9 (
    .in0(Result), .in1(MDout), .out(multiplexer_9_out), .sel(MemToReg));
  Shifter #(.width(20), .shift("ll")) shifter_1 (
    .in({IR[31], IR[19:12], IR[20], IR[30:21]}), .\dist (5'b00001), .out(imm20_J));
  D_Flip_Flop #(.trigger("rising"), .Pre_Clr_Positions("LEGACY"), .NegatePresetClear("false"), .enable("true"), .NewFFLayout("false")) d_ff_2 (
    .clk(IR2_t), .D(1'b1), .Q(d_ff_2_q), .reset(Inter2));  // open: Qn, preset, en
  Multiplexer #(.select(1), .width(32), .disabled("Z"), .enable("false")) multiplexer_10 (
    .in0(multiplexer_9_out), .in1(RPCin), .out(RDin), .sel(PCToReg));
  Shifter #(.width(12), .shift("ll")) shifter_2 (
    .in({IR[31], IR[7], IR[30:25], IR[11:8]}), .\dist (4'b0001), .out(imm12_B));
  or or_11 (or_11_out, d_ff_2_q, Inter2);
  and and_11 (and_11_out, or_11_out, ~Ret2);  // AND_Gate
  Regifile regifile_1 (
    .Din(RDin), .Clk(CLK), .R1(R1), .R2(MDin), .WE(RegWrite), .W_num(IR[11:7]), .R1_num(multiplexer_7_out),
    .R2_num(multiplexer_8_out));
  assign bit_extender_3_out = {{20{IR[31]}}, IR[31:20]};  // Bit_Extender bit_extender_3
  assign bit_extender_4_out = {{20{IR[31]}}, {IR[31:25], IR[11:7]}};  // Bit_Extender bit_extender_4
  D_Flip_Flop #(.trigger("rising"), .Pre_Clr_Positions("LEGACY"), .NegatePresetClear("false"), .enable("true"), .NewFFLayout("false")) u_IR2 (
    .clk(CLK), .D(and_11_out), .Q(Inter2));  // open: Qn, preset, en, reset
  Multiplexer #(.select(1), .width(32), .disabled("Z"), .enable("false")) multiplexer_11 (
    .in0(bit_extender_3_out), .in1(bit_extender_4_out), .out(multiplexer_11_out), .sel(S_type));
  Multiplexer #(.select(1), .width(32), .disabled("Z"), .enable("false")) multiplexer_12 (
    .in0(MDin), .in1(multiplexer_11_out), .out(multiplexer_12_out), .sel(AluSrcB));
  Priority_Encoder #(.select(2), .disabled("Z")) priority_encoder_1 (
    .in0(1'b0), .in1(Inter1), .in2(Inter2), .in3(Inter3), .out(priority_encoder_1_out), .gs(Interr));  // open: en_out, en_in
  Register #(.width(32), .trigger("rising"), .Select("low")) u_EPC (
    .D(nextPC), .en(Interrupt), .Q(EPC), .clk(CLK));  // open: clr
  ALU alu_1 (
    .X(R1), .Y(multiplexer_12_out), .AluOP(AluOP), .Equal(equal), .Result(Result), .out_4(MoreAndEqu));  // open: Result_2, out_6
  D_Flip_Flop #(.trigger("rising"), .Pre_Clr_Positions("LEGACY"), .NegatePresetClear("false"), .enable("true"), .NewFFLayout("false")) d_ff_3 (
    .clk(IR3_t), .D(1'b1), .Q(d_ff_3_q), .reset(Inter3));  // open: Qn, preset, en
  or or_12 (W3, Inter3, d_ff_3_q);
  Multiplexer #(.select(2), .width(32), .disabled("Z"), .enable("false")) multiplexer_13 (
    .in1(32'h30ac), .in2(32'h3150), .in3(32'h31f4), .out(InterAddr), .sel(priority_encoder_1_out));  // open: in0
  or or_13 (or_13_out, d_ff_3_q, Inter3);
  and and_12 (and_12_out, or_13_out, ~Ret3);  // AND_Gate
  Register #(.width(1), .trigger("rising"), .Select("low")) IE (
    .D(Interrupt), .en(or_14_out), .Q(IE_q), .clk(CLK));  // open: clr
  or or_14 (or_14_out, Interrupt, uret);
  D_Flip_Flop #(.trigger("rising"), .Pre_Clr_Positions("LEGACY"), .NegatePresetClear("false"), .enable("true"), .NewFFLayout("false")) u_IR3 (
    .clk(CLK), .D(and_12_out), .Q(Inter3));  // open: Qn, preset, en, reset
  Register #(.width(2), .trigger("rising"), .Select("low")) \u_中断号  (
    .D(priority_encoder_1_out), .en(Interrupt), .Q(\中断号_q ), .clk(CLK));  // open: clr
  Decoder #(.select(2), .tristate("false"), .disabled("Z"), .enable("false")) decoder_1 (
    .out1(decoder_1_out1), .out2(decoder_1_out2), .out3(decoder_1_out3), .sel(\中断号_q ));  // open: out0
  not not_6 (not_6_out, IE_q);
  and and_13 (Interrupt, not_6_out, Interr);
  RAM #(.addrWidth(10), .dataWidth(32), .bus("separate"), .Select("high")) ram_1 (
    .addr(Result[11:2]), .din(MDin), .data(ram_1_data), .str(MemWrite), .clk(CLK), .ld(MemToReg), .clr(RST));  // open: sel
  and and_14 (Ret1, uret, decoder_1_out1);
  and and_15 (Ret2, decoder_1_out2, uret);
  and and_16 (Ret3, decoder_1_out3, uret);
  Multiplexer #(.select(1), .width(16), .disabled("Z"), .enable("false")) multiplexer_14 (
    .in0(ram_1_data[15:0]), .in1(ram_1_data[31:16]), .out(multiplexer_14_out), .sel(Result[1]));
  assign bit_extender_5_out = {{16{1'b0}}, multiplexer_14_out};  // Bit_Extender bit_extender_5
  Multiplexer #(.select(1), .width(32), .disabled("Z"), .enable("false")) multiplexer_15 (
    .in0(ram_1_data), .in1(bit_extender_5_out), .out(MDout), .sel(lhu));

  // Other names for the same wires on the sheet: imm12_S[11:0] = {IR[31:25], IR[11:7]}; imm32_U[31:12] = IR[31:12];
  //   imm12_I[11:0] = IR[31:20]; R2_num[4:0] = IR[24:20]; R2[31:0] = MDin; X = Result[1]

  // Notes on the sheet:
  //   中断源
  //   中断等待指示
  //   总复位信号应将除ROM以外所有存储组件全部清零
  //   单级中断测试信号模拟器
  //   数码管输出
  //   数码管输出应该用寄存器锁存，否则显示数据只能一闪而过
  //   Reset 
  //   指令存储器
  //   指令字
  //   contents of rom_1 (hex, n*v repeats v):
  //   7d000113 100413 1f41993 41f9d993 433 c00913 800b13 140413 f47413 800293 100313 499993 89e9b3 1300533
  //   2200893 73 406282b3 fe0294e3 140413 f00f93 1f47433 1c41413 800293 100313 49d993 89e9b3 1300533
  //   2200893 73 406282b3 fe0294e3 1c45413 406b0b33 b0463 f95ff06f 2b3 fff2c293 1029293 fff2e293 500533
  //   2200893 73 f5dff06f 1112023 410113 a12023 410113 812023 410113 1312023 410113 1412023 410113 1512023
  //   410113 1612023 410113 100b13 300a13 100a93 1600433 441413 14469b3 1300533 2200893 73 fe0416e3
  //   415a0a33 fe0a10e3 ffc10113 12b03 ffc10113 12a83 ffc10113 12a03 ffc10113 12983 ffc10113 12403
  //   ffc10113 12503 ffc10113 12883 200073 1112023 410113 a12023 410113 812023 410113 1312023 410113
  //   1412023 410113 1512023 410113 1612023 410113 200b13 300a13 100a93 1600433 441413 14469b3 1300533
  //   2200893 73 fe0416e3 415a0a33 fe0a10e3 ffc10113 12b03 ffc10113 12a83 ffc10113 12a03 ffc10113 12983
  //   ffc10113 12403 ffc10113 12503 ffc10113 12883 200073 1112023 410113 a12023 410113 812023 410113
  //   1312023 410113 1412023 410113 1512023 410113 1612023 410113 300b13 300a13 100a93 1600433 441413
  //   14469b3 1300533 2200893 73 fe0416e3 415a0a33 fe0a10e3 ffc10113 12b03 ffc10113 12a83 ffc10113 12a03
  //   ffc10113 12983 ffc10113 12403 ffc10113 12503 ffc10113 12883 200073
  //   rs1
  //   rs2
  //   rd
  //   Beq
  //   Bgeu
  //   Bne
  //   MemToReg
  //   MemWrite
  //   AluOP
  //   AluSrcB
  //   RegWrite
  //   为方便自动评测，需要输出PC，IR，寄存器堆写如数据RDin
  //   RAM写使能MemWrite、RAM写入数据MDin等信号
  //   Reset 
  //   Reset 
  //   数据存储器
endmodule
module \单周期_多级中断  (
  input  IR1,
  input  IR2,
  input  IR3,
  output RegWrite,
  output MemWrite,
  output [31:0] PC,
  output [31:0] IR,
  output [31:0] RDin,
  output [31:0] MDin,
  output [31:0] LedData
);

  wire AluSrcB, and_2_out, and_3_out, and_4_out, and_5_out, and_6_out, and_8_out, and_11_out, and_13_out,
       and_14_out, beq, bgeu, bne, Branch, CLK, comparator_2_eq, comparator_3_eq, comparator_4_eq,
       comparator_5_eq, comparator_6_eq, comparator_7_eq, comparator_8_eq, csrrci, csrrsi, d_ff_1_q,
       d_ff_2_q, d_ff_3_q, decoder_1_out1, decoder_1_out2, decoder_1_out3, demultiplexer_1_out1,
       demultiplexer_1_out2, demultiplexer_1_out3, demultiplexer_2_out0, demultiplexer_2_out1,
       demultiplexer_2_out2, ecall, equal, Go, halt, IE, init, Inter1, Inter2, Inter3, Interrupt, IR1_t,
       IR2_t, IR3_t, IRA, IRB, IRC, jal, jalr, lhu, MemToReg, MoreAndEqu, not_1_out, not_2_out, not_3_out,
       not_4_out, not_5_out, or_1_out, or_6_out, or_7_out, or_11_out, or_13_out, or_14_out, or_15_out,
       PCToReg, priority_encoder_1_gs, pull_resistor_1_node, pull_resistor_2_node, pull_resistor_3_node,
       Ret1, Ret2, Ret3, RST, S_type, shield, U_type, uret, W1, W2, W3, \单周期硬布线控制器_1_ecall ,
       \单周期硬布线控制器_1_uret ;
  wire [1:0] counter_3_q, Inter_Num, Inter_Num_Pri, IR1_2_q, IR2_2_q, IR3_2_q;
  wire [3:0] AluOP;
  wire [4:0] multiplexer_7_out, multiplexer_9_out;
  wire [11:0] imm12_B;
  wire [15:0] multiplexer_15_out, \分支成功数 , \总周期数 ;
  wire [19:0] imm20_J;
  wire [31:0] adder_1_out, adder_2_out, adder_3_out, and_1_out, bit_extender_1_out, bit_extender_2_out,
       bit_extender_3_out, bit_extender_4_out, bit_extender_5_out, EPC, EPC1_q, EPC2_q, EPC3_q, InterAddr,
       MDout, multiplexer_1_out, multiplexer_2_out, multiplexer_4_out, multiplexer_5_out, multiplexer_8_out,
       multiplexer_11_out, multiplexer_12_out, nextPC, PC_4, R1, ram_1_data, Result, RPCin;

  Clock #(.highDuration(1), .lowDuration(1)) clock_1 (.out(CLK));
  Button _1 (.out(IRA));
  Button _2 (.out(IRB));
  Button _3 (.out(IRC));
  Button \u_继续运行  (.out(Go));
  LED #(.active("true")) led_1 (.in(W1));
  LED #(.active("true")) led_2 (.in(W2));
  LED #(.active("true")) led_3 (.in(W3));
  Hex_Digit_Display hex_digit_display_1 (.value(LedData[31:28]));  // open: dp
  Hex_Digit_Display hex_digit_display_2 (.value(LedData[27:24]));  // open: dp
  Hex_Digit_Display hex_digit_display_3 (.value(LedData[23:20]));  // open: dp
  Comparator #(.width(16), .mode("twosComplement")) comparator_1 (
    .a({16{1'b0}}), .b(\总周期数 ), .eq(init));  // open: gt, lt
  Comparator #(.width(16), .mode("twosComplement")) comparator_2 (
    .a(16'h23b), .b(\总周期数 ), .eq(comparator_2_eq));  // open: gt, lt
  Comparator #(.width(16), .mode("twosComplement")) comparator_3 (
    .a(\总周期数 ), .b(16'h1), .eq(comparator_3_eq));  // open: gt, lt
  Comparator #(.width(16), .mode("twosComplement")) comparator_4 (
    .a(\总周期数 ), .b(16'h4), .eq(comparator_4_eq));  // open: gt, lt
  Comparator #(.width(16), .mode("twosComplement")) comparator_5 (
    .a(\总周期数 ), .b(16'h7), .eq(comparator_5_eq));  // open: gt, lt
  assign bit_extender_1_out = {{12{imm20_J[19]}}, imm20_J};  // Bit_Extender bit_extender_1
  Hex_Digit_Display hex_digit_display_4 (.value(LedData[19:16]));  // open: dp
  Hex_Digit_Display hex_digit_display_5 (.value(LedData[15:12]));  // open: dp
  or or_1 (or_1_out, comparator_2_eq, comparator_3_eq);
  Pull_Resistor #(.pull(0)) pull_resistor_1 (.node(pull_resistor_1_node));
  assign pull_resistor_1_node = or_1_out ? ~CLK : 1'bz;  // Controlled_Inverter controlled_inverter_1
  Pull_Resistor #(.pull(0)) pull_resistor_2 (.node(pull_resistor_2_node));
  assign pull_resistor_2_node = comparator_4_eq ? ~CLK : 1'bz;  // Controlled_Inverter controlled_inverter_2
  Pull_Resistor #(.pull(0)) pull_resistor_3 (.node(pull_resistor_3_node));
  assign pull_resistor_3_node = comparator_5_eq ? ~CLK : 1'bz;  // Controlled_Inverter controlled_inverter_3
  Adder #(.width(32)) adder_1 (.a(bit_extender_1_out), .b(PC), .out(adder_1_out));  // open: cin, cout
  assign bit_extender_2_out = {{20{imm12_B[11]}}, imm12_B};  // Bit_Extender bit_extender_2
  Hex_Digit_Display hex_digit_display_6 (.value(LedData[11:8]));  // open: dp
  Hex_Digit_Display hex_digit_display_7 (.value(LedData[7:4]));  // open: dp
  // Probe on \总周期数 
  not not_1 (not_1_out, equal);
  Multiplexer #(.select(1), .width(32), .disabled("Z"), .enable("false")) multiplexer_1 (
    .in0(PC_4), .in1(adder_1_out), .out(multiplexer_1_out), .sel(jal));
  assign and_1_out = Result & 32'hfffffffe;  // AND_Gate and_1, 32 bits wide
  Adder #(.width(32)) adder_2 (.a(bit_extender_2_out), .b(PC), .out(adder_2_out));  // open: cin, cout
  Hex_Digit_Display hex_digit_display_8 (.value(LedData[3:0]));  // open: dp
  and and_2 (and_2_out, beq, equal);
  and and_3 (and_3_out, not_1_out, bne);
  and and_4 (and_4_out, MoreAndEqu, bgeu);
  not not_2 (not_2_out, comparator_6_eq);
  Comparator #(.width(32), .mode("twosComplement")) comparator_6 (
    .a(R1), .b(32'ha), .eq(comparator_6_eq));  // open: gt, lt
  and and_5 (and_5_out, comparator_6_eq, ecall);
  Multiplexer #(.select(1), .width(32), .disabled("Z"), .enable("false")) multiplexer_2 (
    .in0(multiplexer_1_out), .in1(and_1_out), .out(multiplexer_2_out), .sel(jalr));
  Multiplexer #(.select(1), .width(32), .disabled("Z"), .enable("false")) multiplexer_3 (
    .in0(multiplexer_2_out), .in1(adder_2_out), .out(nextPC), .sel(Branch));
  or or_2 (W1, Inter1, d_ff_1_q);
  or or_3 (Branch, and_2_out, and_3_out, and_4_out);
  Counter #(.width(16), .max('hffff), .ongoal("wrap"), .trigger("rising"), .behavior("new")) counter_1 (
    .count(Branch), .Q(\分支成功数 ), .clk(CLK), .clr(RST));  // open: load, D, carry, preset, down
  Register #(.width(32), .trigger("rising"), .Select("low")) register_1 (
    .D(MDin), .en(and_6_out), .Q(LedData), .clk(CLK), .clr(RST));
  and and_6 (and_6_out, ecall, not_2_out);
  and and_7 (halt, and_5_out, not_3_out);
  not not_3 (not_3_out, Go);
  Multiplexer #(.select(1), .width(32), .disabled("Z"), .enable("false")) multiplexer_4 (
    .in0(nextPC), .in1(InterAddr), .out(multiplexer_4_out), .sel(Interrupt));
  or or_4 (IR1_t, IR1, IRA);
  D_Flip_Flop #(.trigger("rising"), .Pre_Clr_Positions("LEGACY"), .NegatePresetClear("false"), .enable("true"), .NewFFLayout("false")) d_ff_1 (
    .clk(IR1_t), .D(1'b1), .Q(d_ff_1_q), .reset(Inter1));  // open: Qn, preset, en
  Multiplexer #(.select(1), .width(32), .disabled("Z"), .enable("false")) multiplexer_5 (
    .in0(multiplexer_4_out), .in1(EPC), .out(multiplexer_5_out), .sel(uret));
  not not_4 (not_4_out, halt);
  or or_5 (IR2_t, IR2, IRB);
  or or_6 (or_6_out, d_ff_1_q, Inter1);
  Register #(.width(32), .trigger("rising"), .Select("low")) u_PC (
    .D(multiplexer_5_out), .en(not_4_out), .Q(PC), .clk(CLK), .clr(RST));
  and and_8 (and_8_out, or_6_out, ~Ret1);  // AND_Gate
  not not_5 (not_5_out, halt);
  Counter #(.width(16), .max('hffff), .ongoal("wrap"), .trigger("rising"), .behavior("new")) counter_2 (
    .count(not_5_out), .Q(\总周期数 ), .clk(CLK), .clr(RST));  // open: load, D, carry, preset, down
  or or_7 (or_7_out, jal, jalr);
  Adder #(.width(32)) adder_3 (.a({IR[31:12], {12{1'b0}}}), .b(PC), .out(adder_3_out));  // open: cin, cout
  or or_8 (IR3_t, IR3, IRC);
  D_Flip_Flop #(.trigger("rising"), .Pre_Clr_Positions("LEGACY"), .NegatePresetClear("false"), .enable("true"), .NewFFLayout("false")) u_IR1 (
    .clk(CLK), .D(and_8_out), .Q(Inter1));  // open: Qn, preset, en, reset
  or or_9 (PCToReg, or_7_out, U_type);
  Multiplexer #(.select(1), .width(32), .disabled("Z"), .enable("false")) multiplexer_6 (
    .in0(PC_4), .in1(adder_3_out), .out(RPCin), .sel(U_type));
  // RiscV_Probe riscv_probe_1: pin names not known; wires that end beside it: IR
  ROM #(.addrWidth(10), .dataWidth(32), .Select("high")) rom_1 (.addr(PC[11:2]), .data(IR));
  Adder #(.width(32)) adder_4 (.a(PC), .b(32'h4), .out(PC_4));  // open: cin, cout
  or or_10 (W2, Inter2, d_ff_2_q);
  Comparator #(.width(5), .mode("twosComplement")) comparator_7 (
    .a(IR[24:20]), .b({5{1'b0}}), .eq(comparator_7_eq));  // open: gt, lt
  Comparator #(.width(5), .mode("twosComplement")) comparator_8 (
    .a(IR[24:20]), .b(5'b00010), .eq(comparator_8_eq));  // open: gt, lt
  \单周期硬布线控制器  \u_单周期硬布线控制器_1  (
    .Funct({IR[30], IR[25], IR[14:12]}), .OP(IR[6:2]), .ALU_OP(AluOP), .MemToReg(MemToReg),
    .MemWrite(MemWrite), .ALU_SRC(AluSrcB), .RegWrite(RegWrite), .ecall(\单周期硬布线控制器_1_ecall ),
    .S_type(S_type), .Jalr(jalr), .Beq(beq), .JAL(jal), .Bne(bne), .U_type(U_type), .BGEU(bgeu), .LHU(lhu),
    .URET(\单周期硬布线控制器_1_uret ), .CSRRSI(csrrsi), .CSRRCI(csrrci));
  Multiplexer #(.select(1), .width(5), .disabled("Z"), .enable("false")) multiplexer_7 (
    .in0(IR[24:20]), .in1(5'b01010), .out(multiplexer_7_out), .sel(ecall));
  Multiplexer #(.select(1), .width(32), .disabled("Z"), .enable("false")) multiplexer_8 (
    .in0(Result), .in1(MDout), .out(multiplexer_8_out), .sel(MemToReg));
  D_Flip_Flop #(.trigger("rising"), .Pre_Clr_Positions("LEGACY"), .NegatePresetClear("false"), .enable("true"), .NewFFLayout("false")) d_ff_2 (
    .clk(IR2_t), .D(1'b1), .Q(d_ff_2_q), .reset(Inter2));  // open: Qn, preset, en
  and and_9 (ecall, \单周期硬布线控制器_1_ecall , comparator_7_eq);
  and and_10 (uret, \单周期硬布线控制器_1_uret , comparator_8_eq);
  Multiplexer #(.select(1), .width(5), .disabled("Z"), .enable("false")) multiplexer_9 (
    .in0(IR[19:15]), .in1(5'b10001), .out(multiplexer_9_out), .sel(ecall));
  Shifter #(.width(12), .shift("ll")) shifter_1 (
    .in({IR[31], IR[7], IR[30:25], IR[11:8]}), .\dist (4'b0001), .out(imm12_B));
  Shifter #(.width(20), .shift("ll")) shifter_2 (
    .in({IR[31], IR[19:12], IR[20], IR[30:21]}), .\dist (5'b00001), .out(imm20_J));
  or or_11 (or_11_out, d_ff_2_q, Inter2);
  Multiplexer #(.select(1), .width(32), .disabled("Z"), .enable("false")) multiplexer_10 (
    .in0(multiplexer_8_out), .in1(RPCin), .out(RDin), .sel(PCToReg));
  and and_11 (and_11_out, or_11_out, ~Ret2);  // AND_Gate
  Regifile regifile_1 (
    .Din(RDin), .Clk(CLK), .R1(R1), .R2(MDin), .WE(RegWrite), .W_num(IR[11:7]), .R1_num(multiplexer_9_out),
    .R2_num(multiplexer_7_out));
  D_Flip_Flop #(.trigger("rising"), .Pre_Clr_Positions("LEGACY"), .NegatePresetClear("false"), .enable("true"), .NewFFLayout("false")) u_IR2 (
    .clk(CLK), .D(and_11_out), .Q(Inter2));  // open: Qn, preset, en, reset
  assign bit_extender_3_out = {{20{IR[31]}}, IR[31:20]};  // Bit_Extender bit_extender_3
  Multiplexer #(.select(1), .width(32), .disabled("Z"), .enable("false")) multiplexer_11 (
    .in0(bit_extender_3_out), .in1(bit_extender_4_out), .out(multiplexer_11_out), .sel(S_type));
  assign bit_extender_4_out = {{20{IR[31]}}, {IR[31:25], IR[11:7]}};  // Bit_Extender bit_extender_4
  Multiplexer #(.select(1), .width(32), .disabled("Z"), .enable("false")) multiplexer_12 (
    .in0(MDin), .in1(multiplexer_11_out), .out(multiplexer_12_out), .sel(AluSrcB));
  Priority_Encoder #(.select(2), .disabled("Z")) priority_encoder_1 (
    .in0(1'b0), .in1(Inter1), .in2(Inter2), .in3(Inter3), .out(Inter_Num), .gs(priority_encoder_1_gs));  // open: en_out, en_in
  or or_12 (W3, Inter3, d_ff_3_q);
  and and_12 (Interrupt, priority_encoder_1_gs, shield, IE);
  and and_13 (and_13_out, ~Interrupt, ~csrrci);  // AND_Gate
  Register #(.width(1), .trigger("rising"), .Select("low")) u_IE (
    .D(and_13_out), .en(or_13_out), .Q(IE), .clk(CLK));  // open: clr
  or or_13 (or_13_out, Interrupt, csrrci, csrrsi, uret, init);
  ALU alu_1 (
    .X(R1), .Y(multiplexer_12_out), .AluOP(AluOP), .Equal(equal), .Result(Result), .out_4(MoreAndEqu));  // open: Result_2, out_6
  D_Flip_Flop #(.trigger("rising"), .Pre_Clr_Positions("LEGACY"), .NegatePresetClear("false"), .enable("true"), .NewFFLayout("false")) d_ff_3 (
    .clk(IR3_t), .D(1'b1), .Q(d_ff_3_q), .reset(Inter3));  // open: Qn, preset, en
  Decoder #(.select(2), .tristate("false"), .disabled("Z"), .enable("false")) decoder_1 (
    .out1(decoder_1_out1), .out2(decoder_1_out2), .out3(decoder_1_out3), .sel(Inter_Num));  // open: out0
  Pull_Resistor #(.pull(0)) pull_resistor_4 (.node(decoder_1_out1));
  Pull_Resistor #(.pull(0)) pull_resistor_5 (.node(decoder_1_out2));
  Pull_Resistor #(.pull(0)) pull_resistor_6 (.node(decoder_1_out3));
  or or_14 (or_14_out, d_ff_3_q, Inter3);
  and and_14 (and_14_out, or_14_out, ~Ret3);  // AND_Gate
  and and_15 (Ret1, uret, decoder_1_out1);
  and and_16 (Ret2, decoder_1_out2, uret);
  and and_17 (Ret3, decoder_1_out3, uret);
  Demultiplexer #(.select(2), .width(1), .tristate("false"), .disabled("Z"), .enable("false")) demultiplexer_1 (
    .out1(demultiplexer_1_out1), .out2(demultiplexer_1_out2), .out3(demultiplexer_1_out3), .in(Interrupt),
    .sel(Inter_Num));  // open: out0
  Pull_Resistor #(.pull(0)) pull_resistor_7 (.node(demultiplexer_1_out1));
  Pull_Resistor #(.pull(0)) pull_resistor_8 (.node(demultiplexer_1_out2));
  Pull_Resistor #(.pull(0)) pull_resistor_9 (.node(demultiplexer_1_out3));
  D_Flip_Flop #(.trigger("rising"), .Pre_Clr_Positions("LEGACY"), .NegatePresetClear("false"), .enable("true"), .NewFFLayout("false")) u_IR3 (
    .clk(CLK), .D(and_14_out), .Q(Inter3));  // open: Qn, preset, en, reset
  Register #(.width(32), .trigger("rising"), .Select("low")) EPC1 (
    .D(nextPC), .en(demultiplexer_1_out1), .Q(EPC1_q), .clk(CLK));  // open: clr
  Register #(.width(32), .trigger("rising"), .Select("low")) EPC2 (
    .D(nextPC), .en(demultiplexer_1_out2), .Q(EPC2_q), .clk(CLK));  // open: clr
  Register #(.width(32), .trigger("rising"), .Select("low")) EPC3 (
    .D(nextPC), .en(demultiplexer_1_out3), .Q(EPC3_q), .clk(CLK));  // open: clr
  RAM #(.addrWidth(10), .dataWidth(32), .bus("separate"), .Select("high")) ram_1 (
    .addr(Result[11:2]), .din(MDin), .data(ram_1_data), .str(MemWrite), .clk(CLK), .ld(MemToReg), .clr(RST));  // open: sel
  Multiplexer #(.select(2), .width(32), .disabled("Z"), .enable("false")) multiplexer_13 (
    .in1(32'h30ac), .in2(32'h3158), .in3(32'h3204), .out(InterAddr), .sel(Inter_Num));  // open: in0
  Multiplexer #(.select(2), .width(32), .disabled("Z"), .enable("false")) multiplexer_14 (
    .in1(EPC1_q), .in2(EPC2_q), .in3(EPC3_q), .out(EPC), .sel(Inter_Num_Pri));  // open: in0
  Multiplexer #(.select(1), .width(16), .disabled("Z"), .enable("false")) multiplexer_15 (
    .in0(ram_1_data[15:0]), .in1(ram_1_data[31:16]), .out(multiplexer_15_out), .sel(Result[1]));
  assign bit_extender_5_out = {{16{1'b0}}, multiplexer_15_out};  // Bit_Extender bit_extender_5
  or or_15 (or_15_out, uret, Interrupt);
  Counter #(.width(2), .max('h3), .ongoal("wrap"), .trigger("rising"), .behavior("new")) counter_3 (
    .count(or_15_out), .Q(counter_3_q), .clk(CLK), .down(uret));  // open: load, D, carry, clr, preset
  Demultiplexer #(.select(2), .width(1), .tristate("false"), .disabled("Z"), .enable("false")) demultiplexer_2 (
    .out0(demultiplexer_2_out0), .out1(demultiplexer_2_out1), .out2(demultiplexer_2_out2), .in(Interrupt),
    .sel(counter_3_q));  // open: out3
  Multiplexer #(.select(1), .width(32), .disabled("Z"), .enable("false")) multiplexer_16 (
    .in0(ram_1_data), .in1(bit_extender_5_out), .out(MDout), .sel(lhu));
  Pull_Resistor #(.pull(0)) pull_resistor_10 (.node(demultiplexer_2_out0));
  Pull_Resistor #(.pull(0)) pull_resistor_11 (.node(demultiplexer_2_out1));
  Pull_Resistor #(.pull(0)) pull_resistor_12 (.node(demultiplexer_2_out2));
  Register #(.width(2), .trigger("rising"), .Select("low")) IR1_2 (
    .D(Inter_Num), .en(demultiplexer_2_out0), .Q(IR1_2_q), .clk(CLK));  // open: clr
  Register #(.width(2), .trigger("rising"), .Select("low")) IR2_2 (
    .D(Inter_Num), .en(demultiplexer_2_out1), .Q(IR2_2_q), .clk(CLK));  // open: clr
  Register #(.width(2), .trigger("rising"), .Select("low")) IR3_2 (
    .D(Inter_Num), .en(demultiplexer_2_out2), .Q(IR3_2_q), .clk(CLK));  // open: clr
  Multiplexer #(.select(2), .width(2), .disabled("Z"), .enable("false")) multiplexer_17 (
    .in1(IR1_2_q), .in2(IR2_2_q), .in3(IR3_2_q), .out(Inter_Num_Pri), .sel(counter_3_q));  // open: in0
  Comparator #(.width(2), .mode("unsigned")) comparator_9 (
    .a(Inter_Num_Pri), .b(Inter_Num), .lt(shield));  // open: gt, eq
  Pull_Resistor #(.pull(1)) pull_resistor_13 (.node(shield));

  // Other names for the same wires on the sheet: imm12_S[11:0] = {IR[31:25], IR[11:7]}; imm32_U[31:12] = IR[31:12];
  //   imm12_I[11:0] = IR[31:20]; R2_num[4:0] = IR[24:20]; R2[31:0] = MDin; X = Result[1]

  // Notes on the sheet:
  //   中断源
  //   中断等待指示
  //   总复位信号应将除ROM以外所有存储组件全部清零
  //   单级中断测试信号模拟器
  //   数码管输出
  //   数码管输出应该用寄存器锁存，否则显示数据只能一闪而过
  //   Reset 
  //   指令存储器
  //   contents of rom_1 (hex, n*v repeats v):
  //   7d000113 100413 1f41993 41f9d993 433 c00913 800b13 140413 f47413 800293 100313 499993 89e9b3 1300533
  //   2200893 73 406282b3 fe0294e3 140413 f00f93 1f47433 1c41413 800293 100313 49d993 89e9b3 1300533
  //   2200893 73 406282b3 fe0294e3 1c45413 406b0b33 b0463 f95ff06f 2b3 fff2c293 1029293 fff2e293 500533
  //   2200893 73 f5dff06f 1112023 410113 a12023 410113 812023 410113 1312023 410113 1412023 410113 1512023
  //   410113 1612023 410113 40e073 100b13 300a13 100a93 1600433 441413 14469b3 1300533 2200893 73 fe0416e3
  //   415a0a33 fe0a10e3 40f073 ffc10113 12b03 ffc10113 12a83 ffc10113 12a03 ffc10113 12983 ffc10113 12403
  //   ffc10113 12503 ffc10113 12883 200073 1112023 410113 a12023 410113 812023 410113 1312023 410113
  //   1412023 410113 1512023 410113 1612023 410113 40e073 200b13 300a13 100a93 1600433 441413 14469b3
  //   1300533 2200893 73 fe0416e3 415a0a33 fe0a10e3 40f073 ffc10113 12b03 ffc10113 12a83 ffc10113 12a03
  //   ffc10113 12983 ffc10113 12403 ffc10113 12503 ffc10113 12883 200073 1112023 410113 a12023 410113
  //   812023 410113 1312023 410113 1412023 410113 1512023 410113 1612023 410113 40e073 300b13 300a13
  //   100a93 1600433 441413 14469b3 1300533 2200893 73 fe0416e3 415a0a33 fe0a10e3 40f073 ffc10113 12b03
  //   ffc10113 12a83 ffc10113 12a03 ffc10113 12983 ffc10113 12403 ffc10113 12503 ffc10113 12883 200073
  //   rs1
  //   rs2
  //   指令字
  //   rd
  //   Beq
  //   Bgeu
  //   Bne
  //   为方便自动评测，需要输出PC，IR，寄存器堆写如数据RDin
  //   MemToReg
  //   MemWrite
  //   AluOP
  //   AluSrcB
  //   RegWrite
  //   RAM写使能MemWrite、RAM写入数据MDin等信号
  //   Reset 
  //   Reset 
  //   数据存储器
endmodule

module \流水线中断  (
  input  IR1,
  input  IR2,
  input  IR3,
  output RegWrite,
  output MemWrite,
  output [31:0] IF_PC,
  output [31:0] ID_PC,
  output [31:0] EX_PC,
  output [31:0] M_PC,
  output [31:0] WB_PC,
  output [31:0] RDin,
  output [31:0] MDin,
  output [31:0] LedData
);

  wire and_2_out, and_3_out, and_4_out, and_6_out, and_7_out, and_8_out, and_9_out, and_10_out, and_11_out,
       and_12_out, and_13_out, and_14_out, and_15_out, Branch, CLK, clock_2_out, comparator_1_eq,
       comparator_2_eq, comparator_3_eq, comparator_4_eq, comparator_5_eq, comparator_5_lt, comparator_6_eq,
       comparator_7_eq, comparator_8_eq, comparator_9_eq, controlled_buffer_1_out, d_ff_1_q, d_ff_2_q,
       d_ff_3_q, d_ff_4_q, decoder_1_out1, decoder_1_out2, decoder_1_out3, en, equal, EX_ecall,
       ex_mem_1_haltout, ex_mem_1_jalout, ex_mem_1_jalrout, ex_mem_1_lhuout, ex_mem_1_u_tpyeout,
       ex_mem_1_uretout, EX_RegWrite_num, EXlode, Go, halt, ID_ecall, id_ex_1_alusrcbout, id_ex_1_beqout,
       id_ex_1_bgeuout, id_ex_1_bneout, id_ex_1_lhuout, id_ex_1_memtoregout, id_ex_1_memwriteout,
       id_ex_1_s_tpyeout, id_ex_1_u_tpyeout, id_ex_1_uretout, IE_q, Inter1, Inter2, Inter3, Interr,
       Interrupt, IR1_t, IR2_t, IR3_t, IRA, IRB, IRC, Jal, Jalr, Load_Use, MEM_RegWrite_num,
       mem_wb_1_haltout, mem_wb_1_jalout, mem_wb_1_jalrout, mem_wb_1_lhuout, mem_wb_1_memtoregout,
       mem_wb_1_u_tpyeout, mem_wb_1_xout, MemToReg, MoreAndEqu, nand_1_out, not_1_out, not_2_out, not_3_out,
       not_4_out, not_5_out, not_6_out, not_7_out, not_8_out, not_9_out, or_1_out, or_5_out, or_7_out,
       or_8_out, or_10_out, or_12_out, or_13_out, or_14_out, or_16_out, or_17_out, or_18_out, or_19_out,
       pull_resistor_3_node, Ret1, Ret2, Ret3, riscv_probe_2_p1, riscv_probe_2_p2, RST, uret, W1, W2, W3,
       \单周期硬布线控制器_1_alu_src , \单周期硬布线控制器_1_beq , \单周期硬布线控制器_1_bgeu , \单周期硬布线控制器_1_bne , \单周期硬布线控制器_1_ecall ,
       \单周期硬布线控制器_1_jal , \单周期硬布线控制器_1_jalr , \单周期硬布线控制器_1_lhu , \单周期硬布线控制器_1_memtoreg ,
       \单周期硬布线控制器_1_memwrite , \单周期硬布线控制器_1_regwrite , \单周期硬布线控制器_1_s_type , \单周期硬布线控制器_1_u_type ,
       \单周期硬布线控制器_1_uret , \数据相关 ;
  wire [1:0] id_ex_1_r1forwardout, id_ex_1_r2forwardout, priority_encoder_1_out, R1Forward, R2Forward,
       \中断号_q ;
  wire [3:0] id_ex_1_aluopout, \单周期硬布线控制器_1_alu_op ;
  wire [4:0] EX_W_num, ID_Funct, ID_R1_num, ID_R2_num, MEM_W_num, W_num;
  wire [11:0] shifter_1_out;
  wire [12:0] CNT_num;
  wire [15:0] adder_4_out, \LoadUse次数 , multiplexer_13_out, shifter_3_out, \总周期数 , \插入气泡数 , \无条件分支数 ,
       \条件分支成功数 ;
  wire [19:0] shifter_2_out;
  wire [31:0] adder_1_out, adder_2_out, adder_3_out, adder_6_out, and_1_out, bit_extender_1_out,
       bit_extender_2_out, bit_extender_3_out, bit_extender_4_out, bit_extender_5_out, EPC, EX_IR,
       ex_mem_1_imm_u_out, EX_R1, EX_R2, id_ex_1_imm_i_out, id_ex_1_imm_s_out, id_ex_1_imm_u_out,
       id_ex_1_r1out, id_ex_1_r2out, ID_IR, ID_R1, ID_R2, IF_IR, imm_B, imm_J, InterAddr, Jalr_Addr, MEM_IR,
       mem_wb_1_aluresultout, mem_wb_1_imm_u_out, mem_wb_1_rmdataout, multiplexer_1_out, multiplexer_2_out,
       multiplexer_3_out, multiplexer_4_out, multiplexer_5_out, multiplexer_10_out, multiplexer_11_out,
       multiplexer_14_out, multiplexer_15_out, multiplexer_16_out, ram_1_data, RT, WB_IR, WB_PC_4;

  Button \u_总复位  (.out(RST));
  Button _1 (.out(IRA));
  Button _2 (.out(IRB));
  Button _3 (.out(IRC));
  // Probe on \总周期数 
  // Probe on \总周期数 
  Button \u_继续运行  (.out(Go));
  LED #(.active("true")) led_1 (.in(W1));
  LED #(.active("true")) led_2 (.in(W2));
  LED #(.active("true")) led_3 (.in(W3));
  // Probe on IF_PC[19:0]
  // RiscV_Probe riscv_probe_1: pin names not known; wires that end beside it: IF_IR
  Hex_Digit_Display hex_digit_display_1 (.value(LedData[27:24]));  // open: dp
  Hex_Digit_Display hex_digit_display_2 (.value(LedData[31:28]));  // open: dp
  Comparator #(.width(16), .mode("twosComplement")) comparator_1 (
    .a(16'h23b), .b(\总周期数 ), .eq(comparator_1_eq));  // open: gt, lt
  or or_1 (or_1_out, comparator_1_eq, comparator_2_eq);
  Comparator #(.width(16), .mode("twosComplement")) comparator_2 (
    .a(\总周期数 ), .b(16'h1), .eq(comparator_2_eq));  // open: gt, lt
  Comparator #(.width(16), .mode("twosComplement")) comparator_3 (
    .a(\总周期数 ), .b(16'h4), .eq(comparator_3_eq));  // open: gt, lt
  Comparator #(.width(16), .mode("twosComplement")) comparator_4 (
    .a(\总周期数 ), .b(16'h7), .eq(comparator_4_eq));  // open: gt, lt
  Multiplexer #(.select(1), .width(32), .disabled("Z"), .enable("false")) multiplexer_1 (
    .in0(adder_3_out), .in1(adder_1_out), .out(multiplexer_1_out), .sel(Jal));
  Adder #(.width(32)) adder_1 (.a(imm_J), .b(EX_PC), .out(adder_1_out));  // open: cin, cout
  assign and_1_out = Jalr_Addr & 32'hfffffffe;  // AND_Gate and_1, 32 bits wide
  Hex_Digit_Display hex_digit_display_3 (.value(LedData[23:20]));  // open: dp
  Hex_Digit_Display hex_digit_display_4 (.value(LedData[19:16]));  // open: dp
  // Probe on ID_PC[19:0]
  // RiscV_Probe riscv_probe_2: pin names not known; wires that end beside it: riscv_probe_2_p1, riscv_probe_2_p2, IRA, IRB, {ID_IR[31], ID_Funct[4], ID_IR[29:26], ID_Funct[3], ID_IR[24:15], ID_Funct[2:0], ID_IR[11:0]}
  Pull_Resistor #(.pull(0)) pull_resistor_1 (.node(riscv_probe_2_p1));
  assign riscv_probe_2_p1 = or_1_out ? ~CLK : 1'bz;  // Controlled_Inverter controlled_inverter_1
  Pull_Resistor #(.pull(0)) pull_resistor_2 (.node(riscv_probe_2_p2));
  assign riscv_probe_2_p2 = comparator_3_eq ? ~CLK : 1'bz;  // Controlled_Inverter controlled_inverter_2
  Pull_Resistor #(.pull(0)) pull_resistor_3 (.node(pull_resistor_3_node));
  assign pull_resistor_3_node = comparator_4_eq ? ~CLK : 1'bz;  // Controlled_Inverter controlled_inverter_3
  Multiplexer #(.select(1), .width(32), .disabled("Z"), .enable("false")) multiplexer_2 (
    .in0(multiplexer_1_out), .in1(and_1_out), .out(multiplexer_2_out), .sel(Jalr));
  Adder #(.width(32)) adder_2 (.a(imm_B), .b(EX_PC), .out(adder_2_out));  // open: cin, cout
  Hex_Digit_Display hex_digit_display_5 (.value(LedData[11:8]));  // open: dp
  Hex_Digit_Display hex_digit_display_6 (.value(LedData[15:12]));  // open: dp
  Multiplexer #(.select(1), .width(32), .disabled("Z"), .enable("false")) multiplexer_3 (
    .in0(multiplexer_2_out), .in1(adder_2_out), .out(multiplexer_3_out), .sel(Branch));
  Hex_Digit_Display hex_digit_display_7 (.value(LedData[3:0]));  // open: dp
  Hex_Digit_Display hex_digit_display_8 (.value(LedData[7:4]));  // open: dp
  Clock #(.highDuration(1), .lowDuration(1)) clock_1 (.out(CLK));
  // Probe on EX_PC[19:0]
  // RiscV_Probe riscv_probe_3: pin names not known; wires that end beside it: EX_IR
  or or_2 (IR1_t, IR1, IRA);
  \数据冲突处理逻辑_重定向  \u_数据冲突处理逻辑_重定向_1  (
    .ID_R1_num(ID_R1_num), .EX_W_num(EX_W_num), .EX_RegWrite(EX_RegWrite_num), .EX_OP(EX_IR[6:2]),
    .ID_R2_num(ID_R2_num), .MEM_W_num(MEM_W_num), .MEM_RegWrite(MEM_RegWrite_num), .ID_OP(ID_IR[6:2]),
    .ID_Funct(ID_Funct), .\数据相关 (\数据相关 ), .R1Forward(R1Forward), .Load_Use(Load_Use), .R2Forward(R2Forward));
  Multiplexer #(.select(1), .width(32), .disabled("Z"), .enable("false")) multiplexer_4 (
    .in0(multiplexer_3_out), .in1(InterAddr), .out(multiplexer_4_out), .sel(Interrupt));
  Multiplexer #(.select(1), .width(32), .disabled("Z"), .enable("false")) multiplexer_5 (
    .in0(multiplexer_4_out), .in1(EPC), .out(multiplexer_5_out), .sel(uret));
  and and_2 (and_2_out, not_1_out, not_2_out);
  not not_1 (not_1_out, Load_Use);
  or or_3 (W1, Inter1, d_ff_1_q);
  Register #(.width(32), .trigger("rising"), .Select("low")) PC (
    .D(multiplexer_5_out), .en(and_2_out), .Q(IF_PC), .clk(CLK), .clr(RST));
  not not_2 (not_2_out, halt);
  // Probe on \总周期数 
  // Probe on M_PC[19:0]
  // RiscV_Probe riscv_probe_4: pin names not known; wires that end beside it: MEM_IR
  or or_4 (IR2_t, IR2, IRB);
  D_Flip_Flop #(.trigger("rising"), .Pre_Clr_Positions("LEGACY"), .NegatePresetClear("false"), .enable("true"), .NewFFLayout("false")) d_ff_1 (
    .clk(IR1_t), .D(1'b1), .Q(d_ff_1_q), .reset(Inter1));  // open: Qn, preset, en
  // Probe on \总周期数 
  // Probe on \无条件分支数 
  // Probe on \条件分支成功数 
  // Probe on \插入气泡数 
  // Probe on \LoadUse次数 
  // Probe on WB_PC[19:0]
  // RiscV_Probe riscv_probe_5: pin names not known; wires that end beside it: WB_IR
  or or_5 (or_5_out, d_ff_1_q, Inter1);
  and and_3 (and_3_out, or_5_out, ~Ret1);  // AND_Gate
  Adder #(.width(32)) adder_3 (.a(IF_PC), .b(32'h4), .out(adder_3_out));  // open: cin, cout
  // Probe on IF_PC[11:0]
  or or_6 (IR3_t, IR3, IRC);
  D_Flip_Flop #(.trigger("rising"), .Pre_Clr_Positions("LEGACY"), .NegatePresetClear("false"), .enable("true"), .NewFFLayout("false")) u_IR1 (
    .clk(CLK), .D(and_3_out), .Q(Inter1), .en(EXlode));  // open: Qn, preset, reset
  or or_7 (or_7_out, Branch, Jal, Jalr);
  ROM #(.addrWidth(10), .dataWidth(32), .Select("high")) rom_1 (.addr(IF_PC[11:2]), .data(IF_IR));
  not not_3 (not_3_out, Load_Use);
  // Probe on ID_PC[11:0]
  // Probe on EX_PC[11:0]
  D_Flip_Flop #(.trigger("high"), .Pre_Clr_Positions("LEGACY"), .NegatePresetClear("false"), .enable("true"), .NewFFLayout("false")) d_ff_2 (.Q(d_ff_2_q));  // open: clk, D, Qn, preset, en, reset
  or or_8 (or_8_out, uret, Interrupt, RST, or_7_out);
  and and_4 (and_4_out, not_3_out, en);
  // Probe on WB_PC[11:0]
  // Probe on M_PC[11:0]
  // Probe on 13'hc
  IF_ID if_id_1 (
    .PCin(IF_PC), .IRin(IF_IR), .PCout(ID_PC),
    .IRout({ID_IR[31], ID_Funct[4], ID_IR[29:26], ID_Funct[3], ID_IR[24:15], ID_Funct[2:0], ID_IR[11:0]}),
    .RST(or_8_out), .EN_H(and_4_out), .CLK(CLK));  // open: PredictJumpin, PredictJumpout
  Comparator #(.width(13), .mode("twosComplement")) comparator_5 (
    .a(CNT_num), .b(13'hc), .eq(comparator_5_eq), .lt(comparator_5_lt));  // open: gt
  Clock #(.highDuration(1), .lowDuration(1)) clock_2 (.out(clock_2_out));
  or or_9 (W2, Inter2, d_ff_3_q);
  nand nand_1 (nand_1_out, d_ff_2_q, comparator_5_eq);
  Counter #(.width(13), .max('h1fff), .ongoal("stay"), .trigger("rising"), .behavior("old")) counter_1 (
    .count(comparator_5_lt), .Q(CNT_num), .clk(clock_2_out));  // open: load, D, carry, clr, preset
  D_Flip_Flop #(.trigger("rising"), .Pre_Clr_Positions("LEGACY"), .NegatePresetClear("false"), .enable("true"), .NewFFLayout("false")) d_ff_3 (
    .clk(IR2_t), .D(1'b1), .Q(d_ff_3_q), .reset(Inter2));  // open: Qn, preset, en
  and and_5 (ID_ecall, \单周期硬布线控制器_1_ecall , comparator_6_eq);
  Comparator #(.width(5), .mode("twosComplement")) comparator_6 (
    .a(ID_IR[24:20]), .b({5{1'b0}}), .eq(comparator_6_eq));  // open: gt, lt
  and and_6 (and_6_out, \单周期硬布线控制器_1_uret , comparator_7_eq);
  Comparator #(.width(5), .mode("twosComplement")) comparator_7 (
    .a(ID_IR[24:20]), .b(5'b00010), .eq(comparator_7_eq));  // open: gt, lt
  \单周期硬布线控制器  \u_单周期硬布线控制器_1  (
    .Funct(ID_Funct), .OP(ID_IR[6:2]), .ALU_OP(\单周期硬布线控制器_1_alu_op ), .MemToReg(\单周期硬布线控制器_1_memtoreg ),
    .MemWrite(\单周期硬布线控制器_1_memwrite ), .ALU_SRC(\单周期硬布线控制器_1_alu_src ), .RegWrite(\单周期硬布线控制器_1_regwrite ),
    .ecall(\单周期硬布线控制器_1_ecall ), .S_type(\单周期硬布线控制器_1_s_type ), .Jalr(\单周期硬布线控制器_1_jalr ),
    .Beq(\单周期硬布线控制器_1_beq ), .JAL(\单周期硬布线控制器_1_jal ), .Bne(\单周期硬布线控制器_1_bne ), .U_type(\单周期硬布线控制器_1_u_type ),
    .BGEU(\单周期硬布线控制器_1_bgeu ), .LHU(\单周期硬布线控制器_1_lhu ), .URET(\单周期硬布线控制器_1_uret ));  // open: CSRRSI, CSRRCI
  Multiplexer #(.select(1), .width(5), .disabled("Z"), .enable("false")) multiplexer_6 (
    .in0(ID_IR[19:15]), .in1(5'b10001), .out(ID_R1_num), .sel(ID_ecall));
  Multiplexer #(.select(1), .width(5), .disabled("Z"), .enable("false")) multiplexer_7 (
    .in0(ID_IR[24:20]), .in1(5'b01010), .out(ID_R2_num), .sel(ID_ecall));
  assign bit_extender_1_out = {{20{ID_IR[31]}}, {ID_IR[31], ID_Funct[4], ID_IR[29:26], ID_Funct[3], ID_IR[24:20]}};  // Bit_Extender bit_extender_1
  assign bit_extender_2_out = {{20{ID_IR[31]}}, {ID_IR[31], ID_Funct[4], ID_IR[29:26], ID_Funct[3], ID_IR[11:7]}};  // Bit_Extender bit_extender_2
  Shifter #(.width(12), .shift("ll")) shifter_1 (
    .in({ID_IR[31], ID_IR[7], ID_Funct[4], ID_IR[29:26], ID_Funct[3], ID_IR[11:8]}), .\dist (4'b0001),
    .out(shifter_1_out));
  Shifter #(.width(20), .shift("ll")) shifter_2 (
    .in({ID_IR[31], ID_IR[19:15], ID_Funct[2:0], ID_IR[20], ID_Funct[4], ID_IR[29:26], ID_Funct[3], ID_IR[24:21]}),
    .\dist (5'b00001), .out(shifter_2_out));
  assign controlled_buffer_1_out = nand_1_out ? clock_2_out : 1'bz;  // Controlled_Buffer controlled_buffer_1
  Pull_Resistor #(.pull(1)) pull_resistor_4 (.node(controlled_buffer_1_out));
  or or_10 (or_10_out, d_ff_3_q, Inter2);
  assign bit_extender_3_out = {{20{shifter_1_out[11]}}, shifter_1_out};  // Bit_Extender bit_extender_3
  assign bit_extender_4_out = {{12{shifter_2_out[19]}}, shifter_2_out};  // Bit_Extender bit_extender_4
  and and_7 (and_7_out, or_10_out, ~Ret2);  // AND_Gate
  not not_4 (not_4_out, CLK);
  D_Flip_Flop #(.trigger("rising"), .Pre_Clr_Positions("LEGACY"), .NegatePresetClear("false"), .enable("true"), .NewFFLayout("false")) u_IR2 (
    .clk(CLK), .D(and_7_out), .Q(Inter2), .en(EXlode));  // open: Qn, preset, reset
  Regifile regifile_1 (
    .Din(RDin), .Clk(not_4_out), .R1(ID_R1), .R2(ID_R2), .WE(RegWrite), .W_num(W_num), .R1_num(ID_R1_num),
    .R2_num(ID_R2_num));
  not not_5 (not_5_out, halt);
  Counter #(.width(16), .max('hffff), .ongoal("wrap"), .trigger("rising"), .behavior("new")) counter_2 (
    .count(not_5_out), .Q(\总周期数 ), .clk(CLK), .clr(RST));  // open: load, D, carry, preset, down
  or or_11 (W3, Inter3, d_ff_4_q);
  Counter #(.width(16), .max('hffff), .ongoal("wrap"), .trigger("rising"), .behavior("new")) counter_3 (
    .count(Branch), .Q(\条件分支成功数 ), .clk(CLK), .clr(RST));  // open: load, D, carry, preset, down
  D_Flip_Flop #(.trigger("rising"), .Pre_Clr_Positions("LEGACY"), .NegatePresetClear("false"), .enable("true"), .NewFFLayout("false")) d_ff_4 (
    .clk(IR3_t), .D(1'b1), .Q(d_ff_4_q), .reset(Inter3));  // open: Qn, preset, en
  or or_12 (or_12_out, or_8_out, Load_Use);
  ID_EX id_ex_1 (
    .PCin(ID_PC), .PCout(EX_PC),
    .IRin({ID_IR[31], ID_Funct[4], ID_IR[29:26], ID_Funct[3], ID_IR[24:15], ID_Funct[2:0], ID_IR[11:0]}),
    .IRout(EX_IR), .RST(or_12_out), .EN_H(en), .CLK(CLK), .Imm_I_in(bit_extender_1_out),
    .Imm_I_out(id_ex_1_imm_i_out), .Imm_S_in(bit_extender_2_out), .Imm_S_out(id_ex_1_imm_s_out),
    .Imm_B_in(bit_extender_3_out), .Imm_B_out(imm_B), .Imm_J_in(bit_extender_4_out), .Imm_J_out(imm_J),
    .Imm_U_in({ID_IR[31], ID_Funct[4], ID_IR[29:26], ID_Funct[3], ID_IR[24:15], ID_Funct[2:0], {12{1'b0}}}),
    .Imm_U_out(id_ex_1_imm_u_out), .R1in(ID_R1), .R1out(id_ex_1_r1out), .R2in(ID_R2), .R2out(id_ex_1_r2out),
    .Lhuin(\单周期硬布线控制器_1_lhu ), .Lhuout(id_ex_1_lhuout), .Jalrin(\单周期硬布线控制器_1_jalr ), .Jalrout(Jalr),
    .Jalout(Jal), .Jalin(\单周期硬布线控制器_1_jal ), .Beqin(\单周期硬布线控制器_1_beq ), .Beqout(id_ex_1_beqout),
    .Bgeuin(\单周期硬布线控制器_1_bgeu ), .Bgeuout(id_ex_1_bgeuout), .Bnein(\单周期硬布线控制器_1_bne ),
    .Bneout(id_ex_1_bneout), .MemToRegin(\单周期硬布线控制器_1_memtoreg ), .MemToRegout(id_ex_1_memtoregout),
    .MemWritein(\单周期硬布线控制器_1_memwrite ), .MemWriteout(id_ex_1_memwriteout),
    .AluSrcBin(\单周期硬布线控制器_1_alu_src ), .AluSrcBout(id_ex_1_alusrcbout), .RegWritein(\单周期硬布线控制器_1_regwrite ),
    .RegWriteout(EX_RegWrite_num), .U_Typein(\单周期硬布线控制器_1_u_type ), .U_Tpyeout(id_ex_1_u_tpyeout),
    .AluOpin(\单周期硬布线控制器_1_alu_op ), .AluOpout(id_ex_1_aluopout), .S_Typein(\单周期硬布线控制器_1_s_type ),
    .S_Tpyeout(id_ex_1_s_tpyeout), .Ecallin(ID_ecall), .Ecallout(EX_ecall), .W_in(ID_IR[11:7]),
    .W_out(EX_W_num), .R1Forwardin(R1Forward), .R1Forwardout(id_ex_1_r1forwardout), .R2Forwardin(R2Forward),
    .R2Forwardout(id_ex_1_r2forwardout), .Uretin(and_6_out), .Uretout(id_ex_1_uretout));  // open: PredictJumpin, PredictJumpout
  or or_13 (or_13_out, d_ff_4_q, Inter3);
  and and_8 (and_8_out, or_13_out, ~Ret3);  // AND_Gate
  or or_14 (or_14_out, Jal, Jalr);
  D_Flip_Flop #(.trigger("rising"), .Pre_Clr_Positions("LEGACY"), .NegatePresetClear("false"), .enable("true"), .NewFFLayout("false")) u_IR3 (
    .clk(CLK), .D(and_8_out), .Q(Inter3), .en(EXlode));  // open: Qn, preset, reset
  Multiplexer #(.select(2), .width(32), .disabled("Z"), .enable("false")) multiplexer_8 (
    .in0(id_ex_1_r1out), .in1(RDin), .in2(RT), .out(EX_R1), .sel(id_ex_1_r1forwardout));  // open: in3
  Multiplexer #(.select(2), .width(32), .disabled("Z"), .enable("false")) multiplexer_9 (
    .in0(id_ex_1_r2out), .in1(RDin), .in2(RT), .out(EX_R2), .sel(id_ex_1_r2forwardout));  // open: in3
  Multiplexer #(.select(1), .width(32), .disabled("Z"), .enable("false")) multiplexer_10 (
    .in0(EX_R2), .in1(multiplexer_11_out), .out(multiplexer_10_out), .sel(id_ex_1_alusrcbout));
  Multiplexer #(.select(1), .width(32), .disabled("Z"), .enable("false")) multiplexer_11 (
    .in0(id_ex_1_imm_i_out), .in1(id_ex_1_imm_s_out), .out(multiplexer_11_out), .sel(id_ex_1_s_tpyeout));
  Comparator #(.width(32), .mode("twosComplement")) comparator_8 (
    .a(EX_R1), .b(32'ha), .eq(comparator_8_eq));  // open: gt, lt
  Counter #(.width(16), .max('hffff), .ongoal("wrap"), .trigger("rising"), .behavior("new")) counter_4 (
    .count(or_14_out), .Q(\无条件分支数 ), .clk(CLK), .clr(RST));  // open: load, D, carry, preset, down
  and and_9 (and_9_out, id_ex_1_beqout, equal);
  not not_6 (not_6_out, equal);
  and and_10 (and_10_out, not_6_out, id_ex_1_bneout);
  and and_11 (and_11_out, MoreAndEqu, id_ex_1_bgeuout);
  ALU alu_1 (
    .X(EX_R1), .Y(multiplexer_10_out), .AluOP(id_ex_1_aluopout), .Equal(equal), .Result(Jalr_Addr),
    .out_4(MoreAndEqu));  // open: Result_2, out_6
  and and_12 (and_12_out, EX_ecall, not_7_out);
  not not_7 (not_7_out, comparator_8_eq);
  and and_13 (and_13_out, comparator_8_eq, EX_ecall);
  or or_15 (Branch, and_9_out, and_10_out, and_11_out);
  Register #(.width(32), .trigger("rising"), .Select("low")) register_1 (
    .D(EX_R2), .en(and_12_out), .Q(LedData), .clk(CLK), .clr(RST));
  and and_14 (and_14_out, Interrupt, EXlode);
  Priority_Encoder #(.select(2), .disabled("Z")) priority_encoder_1 (
    .in0(1'b0), .in1(Inter1), .in2(Inter2), .in3(Inter3), .out(priority_encoder_1_out), .gs(Interr));  // open: en_out, en_in
  Register #(.width(32), .trigger("rising"), .Select("low")) u_EPC (
    .D(M_PC), .en(and_14_out), .Q(EPC), .clk(CLK));  // open: clr
  or or_16 (or_16_out, RST, Interrupt, uret);
  EX_MEM ex_mem_1 (
    .PCin(EX_PC), .Lhuin(id_ex_1_lhuout), .PCout(M_PC), .Lhuout(ex_mem_1_lhuout), .Jalrin(Jalr),
    .Jalrout(ex_mem_1_jalrout), .IRin(EX_IR), .IRout(MEM_IR), .Jalin(Jal), .Jalout(ex_mem_1_jalout),
    .MemToRegin(id_ex_1_memtoregout), .MemToRegout(MemToReg), .MemWritein(id_ex_1_memwriteout),
    .MemWriteout(MemWrite), .Imm_U_in(id_ex_1_imm_u_out), .Imm_U_out(ex_mem_1_imm_u_out),
    .Resultin(Jalr_Addr), .Resultout(RT), .RegWritein(EX_RegWrite_num), .RegWriteout(MEM_RegWrite_num),
    .U_Typein(id_ex_1_u_tpyeout), .U_Tpyeout(ex_mem_1_u_tpyeout), .Haltin(and_13_out),
    .Haltout(ex_mem_1_haltout), .W_in(EX_W_num), .W_out(MEM_W_num), .RST(or_16_out), .EN_H(en), .CLK(CLK),
    .WMdatain(EX_R2), .WMdataout(MDin), .Uretin(id_ex_1_uretout), .Uretout(ex_mem_1_uretout));
  Adder #(.width(16)) adder_4 (.a(\条件分支成功数 ), .b(\无条件分支数 ), .out(adder_4_out));  // open: cin, cout
  Shifter #(.width(16), .shift("ll")) shifter_3 (.in(adder_4_out), .\dist (4'b0001), .out(shifter_3_out));
  not not_8 (not_8_out, halt);
  and and_15 (and_15_out, not_8_out, Load_Use);
  Adder #(.width(16)) adder_5 (.a(shifter_3_out), .b(\LoadUse次数 ), .out(\插入气泡数 ));  // open: cin, cout
  Counter #(.width(16), .max('hffff), .ongoal("wrap"), .trigger("rising"), .behavior("new")) counter_5 (
    .count(and_15_out), .Q(\LoadUse次数 ), .clk(CLK), .clr(RST));  // open: load, D, carry, preset, down
  Multiplexer #(.select(2), .width(32), .disabled("Z"), .enable("false")) multiplexer_12 (
    .in1(32'h30ac), .in2(32'h3150), .in3(32'h31f4), .out(InterAddr), .sel(priority_encoder_1_out));  // open: in0
  or or_17 (or_17_out, Interrupt, uret);
  Register #(.width(2), .trigger("rising"), .Select("low")) \u_中断号  (
    .D(priority_encoder_1_out), .en(Interrupt), .Q(\中断号_q ), .clk(CLK));  // open: clr
  Register #(.width(1), .trigger("rising"), .Select("low")) IE (
    .D(Interrupt), .en(or_17_out), .Q(IE_q), .clk(CLK));  // open: clr
  not not_9 (not_9_out, IE_q);
  Decoder #(.select(2), .tristate("false"), .disabled("Z"), .enable("false")) decoder_1 (
    .out1(decoder_1_out1), .out2(decoder_1_out2), .out3(decoder_1_out3), .sel(\中断号_q ));  // open: out0
  and and_16 (Interrupt, not_9_out, Interr);
  RAM #(.addrWidth(10), .dataWidth(32), .bus("separate"), .Select("high")) ram_1 (
    .addr(RT[11:2]), .din(MDin), .data(ram_1_data), .str(MemWrite), .clk(CLK), .ld(MemToReg), .clr(RST));  // open: sel
  and and_17 (Ret1, uret, decoder_1_out1);
  and and_18 (Ret2, decoder_1_out2, uret);
  and and_19 (Ret3, decoder_1_out3, uret);
  or or_18 (or_18_out, RST, uret);
  MEM_WB mem_wb_1 (
    .Lhuin(ex_mem_1_lhuout), .PCin(M_PC), .Jalrin(ex_mem_1_jalrout), .Jalin(ex_mem_1_jalout), .IRin(MEM_IR),
    .MemToRegin(MemToReg), .Imm_U_in(ex_mem_1_imm_u_out), .RegWritein(MEM_RegWrite_num), .AluResultin(RT),
    .U_Typein(ex_mem_1_u_tpyeout), .RMdatain(ram_1_data), .Haltin(ex_mem_1_haltout), .W_in(MEM_W_num),
    .Lhuout(mem_wb_1_lhuout), .PCout(WB_PC), .Jalrout(mem_wb_1_jalrout), .Jalout(mem_wb_1_jalout),
    .IRout(WB_IR), .MemToRegout(mem_wb_1_memtoregout), .Imm_U_out(mem_wb_1_imm_u_out),
    .RegWriteout(RegWrite), .AluResultout(mem_wb_1_aluresultout), .U_Tpyeout(mem_wb_1_u_tpyeout),
    .RMdataout(mem_wb_1_rmdataout), .Haltout(mem_wb_1_haltout), .W_out(W_num), .RST(or_18_out), .EN_H(en),
    .CLK(CLK), .Xin(RT[1]), .Xout(mem_wb_1_xout), .Uretin(ex_mem_1_uretout), .Uretout(uret));
  not not_10 (EXlode, comparator_9_eq);
  Comparator #(.width(32), .mode("twosComplement")) comparator_9 (
    .a(EX_PC), .b({32{1'b0}}), .eq(comparator_9_eq));  // open: gt, lt
  Adder #(.width(32)) adder_6 (.a(WB_PC), .b(mem_wb_1_imm_u_out), .out(adder_6_out));  // open: cin, cout
  and and_20 (halt, mem_wb_1_haltout, ~Go);  // AND_Gate
  not not_11 (en, halt);
  Adder #(.width(32)) adder_7 (.a(32'h4), .b(WB_PC), .out(WB_PC_4));  // open: cin, cout
  or or_19 (or_19_out, mem_wb_1_jalrout, mem_wb_1_jalout, mem_wb_1_u_tpyeout);
  Multiplexer #(.select(1), .width(16), .disabled("Z"), .enable("false")) multiplexer_13 (
    .in0(mem_wb_1_rmdataout[15:0]), .in1(mem_wb_1_rmdataout[31:16]), .out(multiplexer_13_out),
    .sel(mem_wb_1_xout));
  assign bit_extender_5_out = {{16{1'b0}}, multiplexer_13_out};  // Bit_Extender bit_extender_5
  Multiplexer #(.select(1), .width(32), .disabled("Z"), .enable("false")) multiplexer_14 (
    .in0(mem_wb_1_rmdataout), .in1(bit_extender_5_out), .out(multiplexer_14_out), .sel(mem_wb_1_lhuout));
  Multiplexer #(.select(1), .width(32), .disabled("Z"), .enable("false")) multiplexer_15 (
    .in0(WB_PC_4), .in1(adder_6_out), .out(multiplexer_15_out), .sel(mem_wb_1_u_tpyeout));
  Multiplexer #(.select(1), .width(32), .disabled("Z"), .enable("false")) multiplexer_16 (
    .in0(mem_wb_1_aluresultout), .in1(multiplexer_14_out), .out(multiplexer_16_out),
    .sel(mem_wb_1_memtoregout));
  Multiplexer #(.select(1), .width(32), .disabled("Z"), .enable("false")) multiplexer_17 (
    .in0(multiplexer_16_out), .in1(multiplexer_15_out), .out(RDin), .sel(or_19_out));

  // Other names for the same wires on the sheet: ID_RD_num[4:0] = ID_IR[11:7]; ID_IR (some bits) = ID_Funct;
  //   R2_num[4:0] = ID_IR[24:20]; ID_OP[4:0] = ID_IR[6:2]; MEM_PC[31:0] = M_PC; WD[31:0] = RDin;
  //   WriteBackData[31:0] = RDin

  // Notes on the sheet:
  //   中断源
  //   时空图监测，可删除
  //   中断等待指示
  //   单级中断测试信号模拟器
  //   数码管输出
  //   指令存储器
  //   Reset 
  //   指令字
  //   contents of rom_1 (hex, n*v repeats v):
  //   7d000113 100413 1f41993 41f9d993 433 c00913 800b13 140413 f47413 800293 100313 499993 89e9b3 1300533
  //   2200893 73 406282b3 fe0294e3 140413 f00f93 1f47433 1c41413 800293 100313 49d993 89e9b3 1300533
  //   2200893 73 406282b3 fe0294e3 1c45413 406b0b33 b0463 f95ff06f 2b3 fff2c293 1029293 fff2e293 500533
  //   2200893 73 f5dff06f 1112023 410113 a12023 410113 812023 410113 1312023 410113 1412023 410113 1512023
  //   410113 1612023 410113 100b13 300a13 100a93 1600433 441413 14469b3 1300533 2200893 73 fe0416e3
  //   415a0a33 fe0a10e3 ffc10113 12b03 ffc10113 12a83 ffc10113 12a03 ffc10113 12983 ffc10113 12403
  //   ffc10113 12503 ffc10113 12883 200073 1112023 410113 a12023 410113 812023 410113 1312023 410113
  //   1412023 410113 1512023 410113 1612023 410113 200b13 300a13 100a93 1600433 441413 14469b3 1300533
  //   2200893 73 fe0416e3 415a0a33 fe0a10e3 ffc10113 12b03 ffc10113 12a83 ffc10113 12a03 ffc10113 12983
  //   ffc10113 12403 ffc10113 12503 ffc10113 12883 200073 1112023 410113 a12023 410113 812023 410113
  //   1312023 410113 1412023 410113 1512023 410113 1612023 410113 300b13 300a13 100a93 1600433 441413
  //   14469b3 1300533 2200893 73 fe0416e3 415a0a33 fe0a10e3 ffc10113 12b03 ffc10113 12a83 ffc10113 12a03
  //   ffc10113 12983 ffc10113 12403 ffc10113 12503 ffc10113 12883 200073
  //   控制位
  //   流水调试日志用
  //   暂停节拍，不能为0
  //   戳工具置1进入计数暂停模式，ctrl+k时钟自动运行到对应节拍暂停
  //   ctrl+k关闭时钟连续运行，将控制位置零，进入单步调试模式调试
  //   rs1
  //   rs2
  //   rd
  //   Beq
  //   Bgeu
  //   Bne
  //   MemToReg
  //   MemWrite
  //   AluOP
  //   AluSrcB
  //   RegWrite
  //   U_Type
  //   S_Type
  //   可计数暂停的时钟源
  //   Reset 
  //   为方便自动评测，需要输出流水线各段保存的PC值，注意是PC不是PC+4，另外ID段寄存器写入信息，Mem段内存写入信息也要输出
  //   Reset 
  //   数据存储器
endmodule

module \封装正确性测试  (
);

  wire IR1, IR2, IR3, MemW, RegW;
  wire [31:0] EX_PC, ID_PC, IF_PC, IR, LED, MDin, MDinr, MEM_PC, PC, RDin, RDinr, WB_PC;

  \单周期RISC_V  \u_单周期risc_v_1  (
    .IR1(IR1), .IR2(IR2), .IR3(IR3), .RegWrite(RegW), .MemWrite(MemW), .PC(PC), .IR(IR), .RDin(RDin),
    .MDin(MDin), .LedData(LED));
  \气泡流水线  \u_气泡流水线_1  (
    .RegWrite(RegW), .MemWrite(MemW), .IF_PC(IF_PC), .ID_PC(ID_PC), .EX_PC(EX_PC), .M_PC(MEM_PC),
    .WB_PC(WB_PC), .RDin(RDinr), .MDin(MDinr), .LedData(LED));
  \单周期_单级中断  \u_单周期_单级中断_1  (
    .IR1(IR1), .IR2(IR2), .IR3(IR3), .RegWrite(RegW), .MemWrite(MemW), .PC(PC), .IR(IR), .RDin(RDin),
    .MDin(MDin), .LedData(LED));
  \理想流水线  \u_理想流水线_1  (
    .RegWrite(RegW), .MemWrite(MemW), .IF_PC(IF_PC), .ID_PC(ID_PC), .EX_PC(EX_PC), .M_PC(MEM_PC),
    .WB_PC(WB_PC), .RDin(RDinr), .MDin(MDinr), .LedData(LED));
  \重定向流水线  \u_重定向流水线_1  (
    .RegWrite(RegW), .MemWrite(MemW), .IF_PC(IF_PC), .ID_PC(ID_PC), .EX_PC(EX_PC), .M_PC(MEM_PC),
    .WB_PC(WB_PC), .RDin(RDinr), .MDin(MDinr), .LedData(LED));
  \单周期_多级中断  \u_单周期_多级中断_1  (
    .IR1(IR1), .IR2(IR2), .IR3(IR3), .RegWrite(RegW), .MemWrite(MemW), .PC(PC), .IR(IR), .RDin(RDin),
    .MDin(MDin), .LedData(LED));

  // Notes on the sheet:
  //   单周期封装测试
  //   气泡流水封装测试
  //   单周期+单级中断封装测试
  //   请检查上面封装有无位宽不匹配，引脚标签是否和连接的标签相对应，否则无法在educoder平台上正确测试
  //   理想流水封装测试
  //   重定向流水封装测试
  //   单周期+多级中断封装测试
endmodule

// IF/ID
module IF_ID (
  input  [31:0] PCin,
  input  [31:0] IRin,
  input  PredictJumpin,
  input  RST,
  input  EN_H,
  input  CLK,
  output [31:0] PCout,
  output [31:0] IRout,
  output PredictJumpout
);

  wire multiplexer_3_out;
  wire [31:0] multiplexer_1_out, multiplexer_2_out;

  Multiplexer #(.select(1), .width(32), .disabled("Z"), .enable("false")) multiplexer_1 (
    .in0(PCin), .in1({32{1'b0}}), .out(multiplexer_1_out), .sel(RST));
  Multiplexer #(.select(1), .width(32), .disabled("Z"), .enable("false")) multiplexer_2 (
    .in0(IRin), .in1({32{1'b0}}), .out(multiplexer_2_out), .sel(RST));
  Multiplexer #(.select(1), .width(1), .disabled("Z"), .enable("false")) multiplexer_3 (
    .in0(PredictJumpin), .in1(1'b0), .out(multiplexer_3_out), .sel(RST));
  Register #(.width(32), .trigger("rising"), .Select("low")) register_1 (
    .D(multiplexer_1_out), .en(EN_H), .Q(PCout), .clk(CLK));  // open: clr
  Register #(.width(32), .trigger("rising"), .Select("low")) register_2 (
    .D(multiplexer_2_out), .en(EN_H), .Q(IRout), .clk(CLK));  // open: clr
  Register #(.width(1), .trigger("rising"), .Select("low")) register_3 (
    .D(multiplexer_3_out), .en(EN_H), .Q(PredictJumpout), .clk(CLK));  // open: clr
endmodule

// ID/EX
module ID_EX (
  input  Uretin,
  input  [31:0] PCin,
  input  Lhuin,
  input  Jalrin,
  input  [31:0] IRin,
  input  Jalin,
  input  Beqin,
  input  [31:0] Imm_I_in,
  input  Bgeuin,
  input  [31:0] Imm_S_in,
  input  Bnein,
  input  [31:0] Imm_B_in,
  input  MemToRegin,
  input  MemWritein,
  input  [31:0] Imm_J_in,
  input  [3:0] AluOpin,
  input  [31:0] Imm_U_in,
  input  AluSrcBin,
  input  [31:0] R1in,
  input  RegWritein,
  input  U_Typein,
  input  [31:0] R2in,
  input  S_Typein,
  input  PredictJumpin,
  input  Ecallin,
  input  [4:0] W_in,
  input  [1:0] R1Forwardin,
  input  [1:0] R2Forwardin,
  input  RST,
  input  EN_H,
  input  CLK,
  output Uretout,
  output [31:0] PCout,
  output Lhuout,
  output Jalrout,
  output [31:0] IRout,
  output Jalout,
  output Beqout,
  output [31:0] Imm_I_out,
  output Bgeuout,
  output [31:0] Imm_S_out,
  output Bneout,
  output [31:0] Imm_B_out,
  output MemToRegout,
  output MemWriteout,
  output [31:0] Imm_J_out,
  output [3:0] AluOpout,
  output [31:0] Imm_U_out,
  output AluSrcBout,
  output [31:0] R1out,
  output RegWriteout,
  output U_Tpyeout,
  output [31:0] R2out,
  output S_Tpyeout,
  output PredictJumpout,
  output Ecallout,
  output [4:0] W_out,
  output [1:0] R1Forwardout,
  output [1:0] R2Forwardout
);

  wire multiplexer_10_out, multiplexer_11_out, multiplexer_12_out, multiplexer_13_out, multiplexer_14_out,
       multiplexer_15_out, multiplexer_16_out, multiplexer_17_out, multiplexer_18_out, multiplexer_19_out,
       multiplexer_21_out, multiplexer_22_out, multiplexer_23_out, multiplexer_24_out, multiplexer_25_out;
  wire [1:0] multiplexer_27_out, multiplexer_28_out;
  wire [3:0] multiplexer_20_out;
  wire [4:0] multiplexer_26_out;
  wire [31:0] multiplexer_1_out, multiplexer_2_out, multiplexer_3_out, multiplexer_4_out, multiplexer_5_out,
       multiplexer_6_out, multiplexer_7_out, multiplexer_8_out, multiplexer_9_out;

  Multiplexer #(.select(1), .width(32), .disabled("Z"), .enable("false")) multiplexer_1 (
    .in0(PCin), .in1({32{1'b0}}), .out(multiplexer_1_out), .sel(RST));
  Multiplexer #(.select(1), .width(32), .disabled("Z"), .enable("false")) multiplexer_2 (
    .in0(IRin), .in1({32{1'b0}}), .out(multiplexer_2_out), .sel(RST));
  Multiplexer #(.select(1), .width(32), .disabled("Z"), .enable("false")) multiplexer_3 (
    .in0(Imm_I_in), .in1({32{1'b0}}), .out(multiplexer_3_out), .sel(RST));
  Multiplexer #(.select(1), .width(32), .disabled("Z"), .enable("false")) multiplexer_4 (
    .in0(Imm_S_in), .in1({32{1'b0}}), .out(multiplexer_4_out), .sel(RST));
  Multiplexer #(.select(1), .width(32), .disabled("Z"), .enable("false")) multiplexer_5 (
    .in0(Imm_B_in), .in1({32{1'b0}}), .out(multiplexer_5_out), .sel(RST));
  Multiplexer #(.select(1), .width(32), .disabled("Z"), .enable("false")) multiplexer_6 (
    .in0(Imm_J_in), .in1({32{1'b0}}), .out(multiplexer_6_out), .sel(RST));
  Multiplexer #(.select(1), .width(32), .disabled("Z"), .enable("false")) multiplexer_7 (
    .in0(Imm_U_in), .in1({32{1'b0}}), .out(multiplexer_7_out), .sel(RST));
  Multiplexer #(.select(1), .width(32), .disabled("Z"), .enable("false")) multiplexer_8 (
    .in0(R1in), .in1({32{1'b0}}), .out(multiplexer_8_out), .sel(RST));
  Multiplexer #(.select(1), .width(32), .disabled("Z"), .enable("false")) multiplexer_9 (
    .in0(R2in), .in1({32{1'b0}}), .out(multiplexer_9_out), .sel(RST));
  Multiplexer #(.select(1), .width(1), .disabled("Z"), .enable("false")) multiplexer_10 (
    .in0(PredictJumpin), .in1(1'b0), .out(multiplexer_10_out), .sel(RST));
  Register #(.width(32), .trigger("rising"), .Select("low")) register_1 (
    .D(multiplexer_1_out), .en(EN_H), .Q(PCout), .clk(CLK));  // open: clr
  Register #(.width(32), .trigger("rising"), .Select("low")) register_2 (
    .D(multiplexer_2_out), .en(EN_H), .Q(IRout), .clk(CLK));  // open: clr
  Register #(.width(32), .trigger("rising"), .Select("low")) register_3 (
    .D(multiplexer_3_out), .en(EN_H), .Q(Imm_I_out), .clk(CLK));  // open: clr
  Register #(.width(32), .trigger("rising"), .Select("low")) register_4 (
    .D(multiplexer_4_out), .en(EN_H), .Q(Imm_S_out), .clk(CLK));  // open: clr
  Register #(.width(32), .trigger("rising"), .Select("low")) register_5 (
    .D(multiplexer_5_out), .en(EN_H), .Q(Imm_B_out), .clk(CLK));  // open: clr
  Register #(.width(32), .trigger("rising"), .Select("low")) register_6 (
    .D(multiplexer_6_out), .en(EN_H), .Q(Imm_J_out), .clk(CLK));  // open: clr
  Register #(.width(32), .trigger("rising"), .Select("low")) register_7 (
    .D(multiplexer_7_out), .en(EN_H), .Q(Imm_U_out), .clk(CLK));  // open: clr
  Register #(.width(32), .trigger("rising"), .Select("low")) register_8 (
    .D(multiplexer_8_out), .en(EN_H), .Q(R1out), .clk(CLK));  // open: clr
  Register #(.width(32), .trigger("rising"), .Select("low")) register_9 (
    .D(multiplexer_9_out), .en(EN_H), .Q(R2out), .clk(CLK));  // open: clr
  Register #(.width(1), .trigger("rising"), .Select("low")) register_10 (
    .D(multiplexer_10_out), .en(EN_H), .Q(PredictJumpout), .clk(CLK));  // open: clr
  Multiplexer #(.select(1), .width(1), .disabled("Z"), .enable("false")) multiplexer_11 (
    .in0(Uretin), .in1(1'b0), .out(multiplexer_11_out), .sel(RST));
  Multiplexer #(.select(1), .width(1), .disabled("Z"), .enable("false")) multiplexer_12 (
    .in0(Lhuin), .in1(1'b0), .out(multiplexer_12_out), .sel(RST));
  Multiplexer #(.select(1), .width(1), .disabled("Z"), .enable("false")) multiplexer_13 (
    .in0(Jalrin), .in1(1'b0), .out(multiplexer_13_out), .sel(RST));
  Multiplexer #(.select(1), .width(1), .disabled("Z"), .enable("false")) multiplexer_14 (
    .in0(Jalin), .in1(1'b0), .out(multiplexer_14_out), .sel(RST));
  Multiplexer #(.select(1), .width(1), .disabled("Z"), .enable("false")) multiplexer_15 (
    .in0(Beqin), .in1(1'b0), .out(multiplexer_15_out), .sel(RST));
  Multiplexer #(.select(1), .width(1), .disabled("Z"), .enable("false")) multiplexer_16 (
    .in0(Bgeuin), .in1(1'b0), .out(multiplexer_16_out), .sel(RST));
  Multiplexer #(.select(1), .width(1), .disabled("Z"), .enable("false")) multiplexer_17 (
    .in0(Bnein), .in1(1'b0), .out(multiplexer_17_out), .sel(RST));
  Multiplexer #(.select(1), .width(1), .disabled("Z"), .enable("false")) multiplexer_18 (
    .in0(MemToRegin), .in1(1'b0), .out(multiplexer_18_out), .sel(RST));
  Multiplexer #(.select(1), .width(1), .disabled("Z"), .enable("false")) multiplexer_19 (
    .in0(MemWritein), .in1(1'b0), .out(multiplexer_19_out), .sel(RST));
  Multiplexer #(.select(1), .width(4), .disabled("Z"), .enable("false")) multiplexer_20 (
    .in0(AluOpin), .in1(4'b0000), .out(multiplexer_20_out), .sel(RST));
  Multiplexer #(.select(1), .width(1), .disabled("Z"), .enable("false")) multiplexer_21 (
    .in0(AluSrcBin), .in1(1'b0), .out(multiplexer_21_out), .sel(RST));
  Multiplexer #(.select(1), .width(1), .disabled("Z"), .enable("false")) multiplexer_22 (
    .in0(RegWritein), .in1(1'b0), .out(multiplexer_22_out), .sel(RST));
  Multiplexer #(.select(1), .width(1), .disabled("Z"), .enable("false")) multiplexer_23 (
    .in0(U_Typein), .in1(1'b0), .out(multiplexer_23_out), .sel(RST));
  Multiplexer #(.select(1), .width(1), .disabled("Z"), .enable("false")) multiplexer_24 (
    .in0(S_Typein), .in1(1'b0), .out(multiplexer_24_out), .sel(RST));
  Multiplexer #(.select(1), .width(1), .disabled("Z"), .enable("false")) multiplexer_25 (
    .in0(Ecallin), .in1(1'b0), .out(multiplexer_25_out), .sel(RST));
  Multiplexer #(.select(1), .width(5), .disabled("Z"), .enable("false")) multiplexer_26 (
    .in0(W_in), .in1({5{1'b0}}), .out(multiplexer_26_out), .sel(RST));
  Multiplexer #(.select(1), .width(2), .disabled("Z"), .enable("false")) multiplexer_27 (
    .in0(R1Forwardin), .in1(2'b00), .out(multiplexer_27_out), .sel(RST));
  Multiplexer #(.select(1), .width(2), .disabled("Z"), .enable("false")) multiplexer_28 (
    .in0(R2Forwardin), .in1(2'b00), .out(multiplexer_28_out), .sel(RST));
  Register #(.width(1), .trigger("rising"), .Select("low")) register_11 (
    .D(multiplexer_11_out), .en(EN_H), .Q(Uretout), .clk(CLK));  // open: clr
  Register #(.width(1), .trigger("rising"), .Select("low")) register_12 (
    .D(multiplexer_12_out), .en(EN_H), .Q(Lhuout), .clk(CLK));  // open: clr
  Register #(.width(1), .trigger("rising"), .Select("low")) register_13 (
    .D(multiplexer_13_out), .en(EN_H), .Q(Jalrout), .clk(CLK));  // open: clr
  Register #(.width(1), .trigger("rising"), .Select("low")) register_14 (
    .D(multiplexer_14_out), .en(EN_H), .Q(Jalout), .clk(CLK));  // open: clr
  Register #(.width(1), .trigger("rising"), .Select("low")) register_15 (
    .D(multiplexer_15_out), .en(EN_H), .Q(Beqout), .clk(CLK));  // open: clr
  Register #(.width(1), .trigger("rising"), .Select("low")) register_16 (
    .D(multiplexer_16_out), .en(EN_H), .Q(Bgeuout), .clk(CLK));  // open: clr
  Register #(.width(1), .trigger("rising"), .Select("low")) register_17 (
    .D(multiplexer_17_out), .en(EN_H), .Q(Bneout), .clk(CLK));  // open: clr
  Register #(.width(1), .trigger("rising"), .Select("low")) register_18 (
    .D(multiplexer_18_out), .en(EN_H), .Q(MemToRegout), .clk(CLK));  // open: clr
  Register #(.width(1), .trigger("rising"), .Select("low")) register_19 (
    .D(multiplexer_19_out), .en(EN_H), .Q(MemWriteout), .clk(CLK));  // open: clr
  Register #(.width(4), .trigger("rising"), .Select("low")) register_20 (
    .D(multiplexer_20_out), .en(EN_H), .Q(AluOpout), .clk(CLK));  // open: clr
  Register #(.width(1), .trigger("rising"), .Select("low")) register_21 (
    .D(multiplexer_21_out), .en(EN_H), .Q(AluSrcBout), .clk(CLK));  // open: clr
  Register #(.width(1), .trigger("rising"), .Select("low")) register_22 (
    .D(multiplexer_22_out), .en(EN_H), .Q(RegWriteout), .clk(CLK));  // open: clr
  Register #(.width(1), .trigger("rising"), .Select("low")) register_23 (
    .D(multiplexer_23_out), .en(EN_H), .Q(U_Tpyeout), .clk(CLK));  // open: clr
  Register #(.width(1), .trigger("rising"), .Select("low")) register_24 (
    .D(multiplexer_24_out), .en(EN_H), .Q(S_Tpyeout), .clk(CLK));  // open: clr
  Register #(.width(1), .trigger("rising"), .Select("low")) register_25 (
    .D(multiplexer_25_out), .en(EN_H), .Q(Ecallout), .clk(CLK));  // open: clr
  Register #(.width(5), .trigger("rising"), .Select("low")) register_26 (
    .D(multiplexer_26_out), .en(EN_H), .Q(W_out), .clk(CLK));  // open: clr
  Register #(.width(2), .trigger("rising"), .Select("low")) register_27 (
    .D(multiplexer_27_out), .en(EN_H), .Q(R1Forwardout), .clk(CLK));  // open: clr
  Register #(.width(2), .trigger("rising"), .Select("low")) register_28 (
    .D(multiplexer_28_out), .en(EN_H), .Q(R2Forwardout), .clk(CLK));  // open: clr
endmodule

// EX/MEM
module EX_MEM (
  input  Uretin,
  input  Lhuin,
  input  [31:0] PCin,
  input  Jalrin,
  input  Jalin,
  input  [31:0] IRin,
  input  MemToRegin,
  input  [31:0] Imm_U_in,
  input  MemWritein,
  input  [31:0] Resultin,
  input  RegWritein,
  input  U_Typein,
  input  [31:0] WMdatain,
  input  Haltin,
  input  [4:0] W_in,
  input  RST,
  input  EN_H,
  input  CLK,
  output Uretout,
  output Lhuout,
  output [31:0] PCout,
  output Jalrout,
  output Jalout,
  output [31:0] IRout,
  output MemToRegout,
  output [31:0] Imm_U_out,
  output MemWriteout,
  output [31:0] Resultout,
  output RegWriteout,
  output U_Tpyeout,
  output [31:0] WMdataout,
  output Haltout,
  output [4:0] W_out
);

  wire multiplexer_6_out, multiplexer_7_out, multiplexer_8_out, multiplexer_9_out, multiplexer_10_out,
       multiplexer_11_out, multiplexer_12_out, multiplexer_13_out, multiplexer_14_out;
  wire [4:0] multiplexer_15_out;
  wire [31:0] multiplexer_1_out, multiplexer_2_out, multiplexer_3_out, multiplexer_4_out, multiplexer_5_out;

  Multiplexer #(.select(1), .width(32), .disabled("Z"), .enable("false")) multiplexer_1 (
    .in0(PCin), .in1({32{1'b0}}), .out(multiplexer_1_out), .sel(RST));
  Multiplexer #(.select(1), .width(32), .disabled("Z"), .enable("false")) multiplexer_2 (
    .in0(IRin), .in1({32{1'b0}}), .out(multiplexer_2_out), .sel(RST));
  Multiplexer #(.select(1), .width(32), .disabled("Z"), .enable("false")) multiplexer_3 (
    .in0(Imm_U_in), .in1({32{1'b0}}), .out(multiplexer_3_out), .sel(RST));
  Multiplexer #(.select(1), .width(32), .disabled("Z"), .enable("false")) multiplexer_4 (
    .in0(Resultin), .in1({32{1'b0}}), .out(multiplexer_4_out), .sel(RST));
  Multiplexer #(.select(1), .width(32), .disabled("Z"), .enable("false")) multiplexer_5 (
    .in0(WMdatain), .in1({32{1'b0}}), .out(multiplexer_5_out), .sel(RST));
  Register #(.width(32), .trigger("rising"), .Select("low")) register_1 (
    .D(multiplexer_1_out), .en(EN_H), .Q(PCout), .clk(CLK));  // open: clr
  Register #(.width(32), .trigger("rising"), .Select("low")) register_2 (
    .D(multiplexer_2_out), .en(EN_H), .Q(IRout), .clk(CLK));  // open: clr
  Register #(.width(32), .trigger("rising"), .Select("low")) register_3 (
    .D(multiplexer_3_out), .en(EN_H), .Q(Imm_U_out), .clk(CLK));  // open: clr
  Register #(.width(32), .trigger("rising"), .Select("low")) register_4 (
    .D(multiplexer_4_out), .en(EN_H), .Q(Resultout), .clk(CLK));  // open: clr
  Register #(.width(32), .trigger("rising"), .Select("low")) register_5 (
    .D(multiplexer_5_out), .en(EN_H), .Q(WMdataout), .clk(CLK));  // open: clr
  Multiplexer #(.select(1), .width(1), .disabled("Z"), .enable("false")) multiplexer_6 (
    .in0(Uretin), .in1(1'b0), .out(multiplexer_6_out), .sel(RST));
  Multiplexer #(.select(1), .width(1), .disabled("Z"), .enable("false")) multiplexer_7 (
    .in0(Lhuin), .in1(1'b0), .out(multiplexer_7_out), .sel(RST));
  Multiplexer #(.select(1), .width(1), .disabled("Z"), .enable("false")) multiplexer_8 (
    .in0(Jalrin), .in1(1'b0), .out(multiplexer_8_out), .sel(RST));
  Multiplexer #(.select(1), .width(1), .disabled("Z"), .enable("false")) multiplexer_9 (
    .in0(Jalin), .in1(1'b0), .out(multiplexer_9_out), .sel(RST));
  Multiplexer #(.select(1), .width(1), .disabled("Z"), .enable("false")) multiplexer_10 (
    .in0(MemToRegin), .in1(1'b0), .out(multiplexer_10_out), .sel(RST));
  Multiplexer #(.select(1), .width(1), .disabled("Z"), .enable("false")) multiplexer_11 (
    .in0(MemWritein), .in1(1'b0), .out(multiplexer_11_out), .sel(RST));
  Multiplexer #(.select(1), .width(1), .disabled("Z"), .enable("false")) multiplexer_12 (
    .in0(RegWritein), .in1(1'b0), .out(multiplexer_12_out), .sel(RST));
  Multiplexer #(.select(1), .width(1), .disabled("Z"), .enable("false")) multiplexer_13 (
    .in0(U_Typein), .in1(1'b0), .out(multiplexer_13_out), .sel(RST));
  Multiplexer #(.select(1), .width(1), .disabled("Z"), .enable("false")) multiplexer_14 (
    .in0(Haltin), .in1(1'b0), .out(multiplexer_14_out), .sel(RST));
  Multiplexer #(.select(1), .width(5), .disabled("Z"), .enable("false")) multiplexer_15 (
    .in0(W_in), .in1({5{1'b0}}), .out(multiplexer_15_out), .sel(RST));
  Register #(.width(1), .trigger("rising"), .Select("low")) register_6 (
    .D(multiplexer_6_out), .en(EN_H), .Q(Uretout), .clk(CLK));  // open: clr
  Register #(.width(1), .trigger("rising"), .Select("low")) register_7 (
    .D(multiplexer_7_out), .en(EN_H), .Q(Lhuout), .clk(CLK));  // open: clr
  Register #(.width(1), .trigger("rising"), .Select("low")) register_8 (
    .D(multiplexer_8_out), .en(EN_H), .Q(Jalrout), .clk(CLK));  // open: clr
  Register #(.width(1), .trigger("rising"), .Select("low")) register_9 (
    .D(multiplexer_9_out), .en(EN_H), .Q(Jalout), .clk(CLK));  // open: clr
  Register #(.width(1), .trigger("rising"), .Select("low")) register_10 (
    .D(multiplexer_10_out), .en(EN_H), .Q(MemToRegout), .clk(CLK));  // open: clr
  Register #(.width(1), .trigger("rising"), .Select("low")) register_11 (
    .D(multiplexer_11_out), .en(EN_H), .Q(MemWriteout), .clk(CLK));  // open: clr
  Register #(.width(1), .trigger("rising"), .Select("low")) register_12 (
    .D(multiplexer_12_out), .en(EN_H), .Q(RegWriteout), .clk(CLK));  // open: clr
  Register #(.width(1), .trigger("rising"), .Select("low")) register_13 (
    .D(multiplexer_13_out), .en(EN_H), .Q(U_Tpyeout), .clk(CLK));  // open: clr
  Register #(.width(1), .trigger("rising"), .Select("low")) register_14 (
    .D(multiplexer_14_out), .en(EN_H), .Q(Haltout), .clk(CLK));  // open: clr
  Register #(.width(5), .trigger("rising"), .Select("low")) register_15 (
    .D(multiplexer_15_out), .en(EN_H), .Q(W_out), .clk(CLK));  // open: clr
endmodule

// MEM/WB
module MEM_WB (
  input  Uretin,
  input  Lhuin,
  input  [31:0] PCin,
  input  Jalrin,
  input  Jalin,
  input  [31:0] IRin,
  input  MemToRegin,
  input  [31:0] Imm_U_in,
  input  RegWritein,
  input  [31:0] AluResultin,
  input  U_Typein,
  input  Xin,
  input  [31:0] RMdatain,
  input  Haltin,
  input  [4:0] W_in,
  input  RST,
  input  EN_H,
  input  CLK,
  output Uretout,
  output Lhuout,
  output [31:0] PCout,
  output Jalrout,
  output Jalout,
  output [31:0] IRout,
  output MemToRegout,
  output [31:0] Imm_U_out,
  output RegWriteout,
  output [31:0] AluResultout,
  output U_Tpyeout,
  output Xout,
  output [31:0] RMdataout,
  output Haltout,
  output [4:0] W_out
);

  wire multiplexer_6_out, multiplexer_7_out, multiplexer_8_out, multiplexer_9_out, multiplexer_10_out,
       multiplexer_11_out, multiplexer_12_out, multiplexer_13_out, multiplexer_14_out;
  wire [4:0] multiplexer_15_out;
  wire [31:0] multiplexer_1_out, multiplexer_2_out, multiplexer_3_out, multiplexer_4_out, multiplexer_5_out;

  Multiplexer #(.select(1), .width(32), .disabled("Z"), .enable("false")) multiplexer_1 (
    .in0(PCin), .in1({32{1'b0}}), .out(multiplexer_1_out), .sel(RST));
  Multiplexer #(.select(1), .width(32), .disabled("Z"), .enable("false")) multiplexer_2 (
    .in0(IRin), .in1({32{1'b0}}), .out(multiplexer_2_out), .sel(RST));
  Multiplexer #(.select(1), .width(32), .disabled("Z"), .enable("false")) multiplexer_3 (
    .in0(Imm_U_in), .in1({32{1'b0}}), .out(multiplexer_3_out), .sel(RST));
  Multiplexer #(.select(1), .width(32), .disabled("Z"), .enable("false")) multiplexer_4 (
    .in0(AluResultin), .in1({32{1'b0}}), .out(multiplexer_4_out), .sel(RST));
  Multiplexer #(.select(1), .width(32), .disabled("Z"), .enable("false")) multiplexer_5 (
    .in0(RMdatain), .in1({32{1'b0}}), .out(multiplexer_5_out), .sel(RST));
  Register #(.width(32), .trigger("rising"), .Select("low")) register_1 (
    .D(multiplexer_1_out), .en(EN_H), .Q(PCout), .clk(CLK));  // open: clr
  Register #(.width(32), .trigger("rising"), .Select("low")) register_2 (
    .D(multiplexer_2_out), .en(EN_H), .Q(IRout), .clk(CLK));  // open: clr
  Register #(.width(32), .trigger("rising"), .Select("low")) register_3 (
    .D(multiplexer_3_out), .en(EN_H), .Q(Imm_U_out), .clk(CLK));  // open: clr
  Register #(.width(32), .trigger("rising"), .Select("low")) register_4 (
    .D(multiplexer_4_out), .en(EN_H), .Q(AluResultout), .clk(CLK));  // open: clr
  Register #(.width(32), .trigger("rising"), .Select("low")) register_5 (
    .D(multiplexer_5_out), .en(EN_H), .Q(RMdataout), .clk(CLK));  // open: clr
  Multiplexer #(.select(1), .width(1), .disabled("Z"), .enable("false")) multiplexer_6 (
    .in0(Uretin), .in1(1'b0), .out(multiplexer_6_out), .sel(RST));
  Multiplexer #(.select(1), .width(1), .disabled("Z"), .enable("false")) multiplexer_7 (
    .in0(Lhuin), .in1(1'b0), .out(multiplexer_7_out), .sel(RST));
  Multiplexer #(.select(1), .width(1), .disabled("Z"), .enable("false")) multiplexer_8 (
    .in0(Jalrin), .in1(1'b0), .out(multiplexer_8_out), .sel(RST));
  Multiplexer #(.select(1), .width(1), .disabled("Z"), .enable("false")) multiplexer_9 (
    .in0(Jalin), .in1(1'b0), .out(multiplexer_9_out), .sel(RST));
  Multiplexer #(.select(1), .width(1), .disabled("Z"), .enable("false")) multiplexer_10 (
    .in0(MemToRegin), .in1(1'b0), .out(multiplexer_10_out), .sel(RST));
  Multiplexer #(.select(1), .width(1), .disabled("Z"), .enable("false")) multiplexer_11 (
    .in0(RegWritein), .in1(1'b0), .out(multiplexer_11_out), .sel(RST));
  Multiplexer #(.select(1), .width(1), .disabled("Z"), .enable("false")) multiplexer_12 (
    .in0(U_Typein), .in1(1'b0), .out(multiplexer_12_out), .sel(RST));
  Multiplexer #(.select(1), .width(1), .disabled("Z"), .enable("false")) multiplexer_13 (
    .in0(Xin), .in1(1'b0), .out(multiplexer_13_out), .sel(RST));
  Multiplexer #(.select(1), .width(1), .disabled("Z"), .enable("false")) multiplexer_14 (
    .in0(Haltin), .in1(1'b0), .out(multiplexer_14_out), .sel(RST));
  Multiplexer #(.select(1), .width(5), .disabled("Z"), .enable("false")) multiplexer_15 (
    .in0(W_in), .in1({5{1'b0}}), .out(multiplexer_15_out), .sel(RST));
  Register #(.width(1), .trigger("rising"), .Select("low")) register_6 (
    .D(multiplexer_6_out), .en(EN_H), .Q(Uretout), .clk(CLK));  // open: clr
  Register #(.width(1), .trigger("rising"), .Select("low")) register_7 (
    .D(multiplexer_7_out), .en(EN_H), .Q(Lhuout), .clk(CLK));  // open: clr
  Register #(.width(1), .trigger("rising"), .Select("low")) register_8 (
    .D(multiplexer_8_out), .en(EN_H), .Q(Jalrout), .clk(CLK));  // open: clr
  Register #(.width(1), .trigger("rising"), .Select("low")) register_9 (
    .D(multiplexer_9_out), .en(EN_H), .Q(Jalout), .clk(CLK));  // open: clr
  Register #(.width(1), .trigger("rising"), .Select("low")) register_10 (
    .D(multiplexer_10_out), .en(EN_H), .Q(MemToRegout), .clk(CLK));  // open: clr
  Register #(.width(1), .trigger("rising"), .Select("low")) register_11 (
    .D(multiplexer_11_out), .en(EN_H), .Q(RegWriteout), .clk(CLK));  // open: clr
  Register #(.width(1), .trigger("rising"), .Select("low")) register_12 (
    .D(multiplexer_12_out), .en(EN_H), .Q(U_Tpyeout), .clk(CLK));  // open: clr
  Register #(.width(1), .trigger("rising"), .Select("low")) register_13 (
    .D(multiplexer_13_out), .en(EN_H), .Q(Xout), .clk(CLK));  // open: clr
  Register #(.width(1), .trigger("rising"), .Select("low")) register_14 (
    .D(multiplexer_14_out), .en(EN_H), .Q(Haltout), .clk(CLK));  // open: clr
  Register #(.width(5), .trigger("rising"), .Select("low")) register_15 (
    .D(multiplexer_15_out), .en(EN_H), .Q(W_out), .clk(CLK));  // open: clr
endmodule

module BHT (
  input  Clk,
  input  EX_Branch,
  input  [31:0] PC,
  input  [31:0] EX_PC,
  input  [31:0] EX_BranchAddr,
  input  EX_Branched,
  output [31:0] JumpAddr,
  output PredictJump
);

  wire A0, A1, A2, A3, A4, A5, A6, A7, and_1_out, comparator_1_eq, comparator_2_eq, comparator_3_eq,
       comparator_4_eq, comparator_5_eq, comparator_6_eq, comparator_7_eq, comparator_8_eq, comparator_9_eq,
       comparator_10_eq, comparator_11_eq, comparator_12_eq, comparator_13_eq, comparator_14_eq,
       comparator_15_eq, comparator_16_eq, decoder_1_out0, decoder_1_out1, decoder_1_out2, decoder_1_out3,
       decoder_1_out4, decoder_1_out5, decoder_1_out6, decoder_1_out7, decoder_2_out0, decoder_2_out1,
       decoder_2_out2, decoder_2_out3, decoder_2_out4, decoder_2_out5, decoder_2_out6, decoder_2_out7,
       EX_Hit, EX_Miss, IF_Hit, IF_Miss, L0, L1, L2, L3, L4, L5, L6, L7, M0, M1, M2, M3, M4, M5, M6, M7,
       not_1_out, not_2_out, not_3_out, not_4_out, not_5_out, not_6_out, not_7_out, not_8_out, or_1_out,
       or_2_out, or_3_out, or_4_out, or_5_out, or_6_out, or_7_out, or_8_out, or_9_out, or_10_out, or_11_out,
       or_12_out, or_13_out, or_14_out, or_17_out, or_18_out, priority_encoder_1_gs, V0, V1, V2, V3, V4, V5,
       V6, V7, WriteL0, WriteL1, WriteL2, WriteL3, WriteL4, WriteL5, WriteL6, WriteL7;
  wire [0:0] controlled_buffer_1_out, controlled_buffer_2_out, controlled_buffer_3_out,
       controlled_buffer_4_out, controlled_buffer_5_out, controlled_buffer_6_out, controlled_buffer_7_out,
       controlled_buffer_8_out;
  wire [1:0] adder_1_out, adder_2_out, adder_3_out, adder_4_out, adder_5_out, adder_6_out, adder_7_out,
       adder_8_out, multiplexer_1_out, multiplexer_2_out, multiplexer_3_out, multiplexer_4_out,
       multiplexer_5_out, multiplexer_6_out, multiplexer_7_out, multiplexer_8_out, multiplexer_9_out,
       multiplexer_10_out, multiplexer_11_out, multiplexer_12_out, multiplexer_13_out, multiplexer_14_out,
       multiplexer_15_out, multiplexer_16_out, multiplexer_17_out, multiplexer_18_out, multiplexer_19_out,
       multiplexer_20_out, multiplexer_21_out, multiplexer_22_out, multiplexer_23_out, multiplexer_24_out,
       multiplexer_25_out, multiplexer_26_out, multiplexer_27_out, multiplexer_28_out, multiplexer_29_out,
       multiplexer_30_out, multiplexer_31_out, multiplexer_32_out, multiplexer_33_out, multiplexer_34_out,
       multiplexer_35_out, multiplexer_36_out, multiplexer_37_out, multiplexer_38_out, multiplexer_39_out,
       multiplexer_40_out, Predict0, Predict1, Predict2, Predict3, Predict4, Predict5, Predict6, Predict7;
  wire [2:0] max2_1_max_num, max2_2_max_num, max2_3_max_num, max2_4_max_num, max2_5_max_num, max2_6_max_num,
       max2_7_max_num, priority_encoder_1_out;
  wire [15:0] C0, C1, C2, C3, C4, C5, C6, C7, max2_1_max, max2_2_max, max2_3_max, max2_4_max, max2_5_max,
       max2_6_max;
  wire [31:0] Tag0, Tag1, Tag2, Tag3, Tag4, Tag5, Tag6, Tag7, \分支目标地址_2_q , \分支目标地址_3_q , \分支目标地址_4_q ,
       \分支目标地址_5_q , \分支目标地址_6_q , \分支目标地址_7_q , \分支目标地址_8_q , \分支目标地址_q ;

  Register #(.width(1), .trigger("rising"), .Select("low")) VALID (
    .D(1'b1), .en(WriteL0), .Q(V0), .clk(Clk));  // open: clr
  Register #(.width(1), .trigger("rising"), .Select("low")) VALID_2 (
    .D(1'b1), .en(WriteL1), .Q(V1), .clk(Clk));  // open: clr
  Register #(.width(1), .trigger("rising"), .Select("low")) VALID_3 (
    .D(1'b1), .en(WriteL2), .Q(V2), .clk(Clk));  // open: clr
  Register #(.width(1), .trigger("rising"), .Select("low")) VALID_4 (
    .D(1'b1), .en(WriteL3), .Q(V3), .clk(Clk));  // open: clr
  Register #(.width(1), .trigger("rising"), .Select("low")) VALID_5 (
    .D(1'b1), .en(WriteL4), .Q(V4), .clk(Clk));  // open: clr
  Register #(.width(1), .trigger("rising"), .Select("low")) VALID_6 (
    .D(1'b1), .en(WriteL5), .Q(V5), .clk(Clk));  // open: clr
  Register #(.width(1), .trigger("rising"), .Select("low")) VALID_7 (
    .D(1'b1), .en(WriteL6), .Q(V6), .clk(Clk));  // open: clr
  Register #(.width(1), .trigger("rising"), .Select("low")) VALID_8 (
    .D(1'b1), .en(WriteL7), .Q(V7), .clk(Clk));  // open: clr
  not not_1 (not_1_out, V0);
  not not_2 (not_2_out, V1);
  not not_3 (not_3_out, V2);
  not not_4 (not_4_out, V3);
  not not_5 (not_5_out, V4);
  not not_6 (not_6_out, V5);
  not not_7 (not_7_out, V6);
  not not_8 (not_8_out, V7);
  MAX2 max2_1 (.Y(C1), .X(C0), .Y_num(3'b001), .X_num(3'b000), .MAX(max2_1_max), .MAX_num(max2_1_max_num));
  MAX2 max2_2 (.Y(C3), .X(C2), .Y_num(3'b011), .X_num(3'b010), .MAX(max2_2_max), .MAX_num(max2_2_max_num));
  MAX2 max2_3 (.Y(C5), .X(C4), .Y_num(3'b101), .X_num(3'b100), .MAX(max2_3_max), .MAX_num(max2_3_max_num));
  MAX2 max2_4 (.Y(C7), .X(C6), .Y_num(3'b111), .X_num(3'b110), .MAX(max2_4_max), .MAX_num(max2_4_max_num));
  Pull_Resistor #(.pull(0)) pull_resistor_1 (.node(PredictJump));
  assign {PredictJump, controlled_buffer_1_out[0]} = L0 ? Predict0 : 2'bz;  // Controlled_Buffer controlled_buffer_1
  assign {PredictJump, controlled_buffer_2_out[0]} = L1 ? Predict1 : 2'bz;  // Controlled_Buffer controlled_buffer_2
  assign {PredictJump, controlled_buffer_3_out[0]} = L2 ? Predict2 : 2'bz;  // Controlled_Buffer controlled_buffer_3
  assign {PredictJump, controlled_buffer_4_out[0]} = L3 ? Predict3 : 2'bz;  // Controlled_Buffer controlled_buffer_4
  assign {PredictJump, controlled_buffer_5_out[0]} = L4 ? Predict4 : 2'bz;  // Controlled_Buffer controlled_buffer_5
  assign {PredictJump, controlled_buffer_6_out[0]} = L5 ? Predict5 : 2'bz;  // Controlled_Buffer controlled_buffer_6
  assign {PredictJump, controlled_buffer_7_out[0]} = L6 ? Predict6 : 2'bz;  // Controlled_Buffer controlled_buffer_7
  assign {PredictJump, controlled_buffer_8_out[0]} = L7 ? Predict7 : 2'bz;  // Controlled_Buffer controlled_buffer_8
  Priority_Encoder #(.select(3), .disabled("Z")) priority_encoder_1 (
    .in0(not_1_out), .in1(not_2_out), .in2(not_3_out), .in3(not_4_out), .in4(not_5_out), .in5(not_6_out),
    .in6(not_7_out), .in7(not_8_out), .out(priority_encoder_1_out), .gs(priority_encoder_1_gs));  // open: en_out, en_in
  MAX2 max2_5 (
    .Y(max2_2_max), .X(max2_1_max), .Y_num(max2_2_max_num), .X_num(max2_1_max_num), .MAX(max2_5_max),
    .MAX_num(max2_5_max_num));
  MAX2 max2_6 (
    .Y(max2_4_max), .X(max2_3_max), .Y_num(max2_4_max_num), .X_num(max2_3_max_num), .MAX(max2_6_max),
    .MAX_num(max2_6_max_num));
  and and_1 (and_1_out, V0, V1, V2, V3, V4, V5, V6, V7);
  or or_1 (or_1_out, L1, L2, L3, L4, L5, L6, L7, WriteL1, WriteL2, WriteL3, WriteL4, WriteL5, WriteL6, WriteL7);
  or or_2 (or_2_out, L0, L1, L2, L3, L5, L6, L7, WriteL0, WriteL1, WriteL2, WriteL3, WriteL5, WriteL6, WriteL7);
  Register #(.width(32), .trigger("rising"), .Select("low")) \u_分支指令地址  (
    .D(EX_PC), .en(WriteL0), .Q(Tag0), .clk(Clk));  // open: clr
  Register #(.width(32), .trigger("rising"), .Select("low")) \u_分支指令地址_2  (
    .D(EX_PC), .en(WriteL1), .Q(Tag1), .clk(Clk));  // open: clr
  Register #(.width(32), .trigger("rising"), .Select("low")) \u_分支指令地址_3  (
    .D(EX_PC), .en(WriteL2), .Q(Tag2), .clk(Clk));  // open: clr
  Register #(.width(32), .trigger("rising"), .Select("low")) \u_分支指令地址_4  (
    .D(EX_PC), .en(WriteL3), .Q(Tag3), .clk(Clk));  // open: clr
  Register #(.width(32), .trigger("rising"), .Select("low")) \u_分支指令地址_5  (
    .D(EX_PC), .en(WriteL4), .Q(Tag4), .clk(Clk));  // open: clr
  Register #(.width(32), .trigger("rising"), .Select("low")) \u_分支指令地址_6  (
    .D(EX_PC), .en(WriteL5), .Q(Tag5), .clk(Clk));  // open: clr
  Register #(.width(32), .trigger("rising"), .Select("low")) \u_分支指令地址_7  (
    .D(EX_PC), .en(WriteL6), .Q(Tag6), .clk(Clk));  // open: clr
  Register #(.width(32), .trigger("rising"), .Select("low")) \u_分支指令地址_8  (
    .D(EX_PC), .en(WriteL7), .Q(Tag7), .clk(Clk));  // open: clr
  Decoder #(.select(3), .tristate("false"), .disabled(0), .enable("true")) decoder_1 (
    .out0(decoder_1_out0), .out1(decoder_1_out1), .out2(decoder_1_out2), .out3(decoder_1_out3),
    .out4(decoder_1_out4), .out5(decoder_1_out5), .out6(decoder_1_out6), .out7(decoder_1_out7),
    .sel(priority_encoder_1_out), .en(priority_encoder_1_gs));
  Decoder #(.select(3), .tristate("false"), .disabled(0), .enable("true")) decoder_2 (
    .out0(decoder_2_out0), .out1(decoder_2_out1), .out2(decoder_2_out2), .out3(decoder_2_out3),
    .out4(decoder_2_out4), .out5(decoder_2_out5), .out6(decoder_2_out6), .out7(decoder_2_out7),
    .sel(max2_7_max_num), .en(and_1_out));
  MAX2 max2_7 (
    .Y(max2_6_max), .X(max2_5_max), .Y_num(max2_6_max_num), .X_num(max2_5_max_num), .MAX_num(max2_7_max_num));  // open: MAX
  Multiplexer #(.select(1), .width(2), .disabled("Z"), .enable("false")) multiplexer_1 (
    .in0(2'b00), .in1(2'b01), .out(multiplexer_1_out), .sel(EX_Branched));
  Multiplexer #(.select(1), .width(2), .disabled("Z"), .enable("false")) multiplexer_2 (
    .in0(2'b11), .in1(2'b01), .out(multiplexer_2_out), .sel(EX_Branched));
  Multiplexer #(.select(1), .width(2), .disabled("Z"), .enable("false")) multiplexer_3 (
    .in0(2'b01), .in1(2'b00), .out(multiplexer_3_out), .sel(EX_Branched));
  Multiplexer #(.select(1), .width(2), .disabled("Z"), .enable("false")) multiplexer_4 (
    .in0(2'b01), .in1(2'b11), .out(multiplexer_4_out), .sel(EX_Branched));
  Multiplexer #(.select(1), .width(2), .disabled("Z"), .enable("false")) multiplexer_5 (
    .in0(2'b00), .in1(2'b01), .out(multiplexer_5_out), .sel(EX_Branched));
  Multiplexer #(.select(1), .width(2), .disabled("Z"), .enable("false")) multiplexer_6 (
    .in0(2'b11), .in1(2'b01), .out(multiplexer_6_out), .sel(EX_Branched));
  Multiplexer #(.select(1), .width(2), .disabled("Z"), .enable("false")) multiplexer_7 (
    .in0(2'b01), .in1(2'b00), .out(multiplexer_7_out), .sel(EX_Branched));
  Multiplexer #(.select(1), .width(2), .disabled("Z"), .enable("false")) multiplexer_8 (
    .in0(2'b01), .in1(2'b11), .out(multiplexer_8_out), .sel(EX_Branched));
  Counter #(.width(16), .max('hffff), .ongoal("wrap"), .trigger("rising"), .behavior("old")) \u_置换标记  (
    .count(A0), .Q(C0), .clk(Clk), .clr(L0));  // open: load, D, carry, preset
  Counter #(.width(16), .max('hffff), .ongoal("wrap"), .trigger("rising"), .behavior("old")) \u_置换标记_2  (
    .count(A1), .Q(C1), .clk(Clk), .clr(L1));  // open: load, D, carry, preset
  Counter #(.width(16), .max('hffff), .ongoal("wrap"), .trigger("rising"), .behavior("old")) \u_置换标记_3  (
    .count(A2), .Q(C2), .clk(Clk), .clr(L2));  // open: load, D, carry, preset
  Counter #(.width(16), .max('hffff), .ongoal("wrap"), .trigger("rising"), .behavior("old")) \u_置换标记_4  (
    .count(A3), .Q(C3), .clk(Clk), .clr(L3));  // open: load, D, carry, preset
  Counter #(.width(16), .max('hffff), .ongoal("wrap"), .trigger("rising"), .behavior("old")) \u_置换标记_5  (
    .count(A4), .Q(C4), .clk(Clk), .clr(L4));  // open: load, D, carry, preset
  Counter #(.width(16), .max('hffff), .ongoal("wrap"), .trigger("rising"), .behavior("old")) \u_置换标记_6  (
    .count(A5), .Q(C5), .clk(Clk), .clr(L5));  // open: load, D, carry, preset
  Counter #(.width(16), .max('hffff), .ongoal("wrap"), .trigger("rising"), .behavior("old")) \u_置换标记_7  (
    .count(A6), .Q(C6), .clk(Clk), .clr(L6));  // open: load, D, carry, preset
  Counter #(.width(16), .max('hffff), .ongoal("wrap"), .trigger("rising"), .behavior("old")) \u_置换标记_8  (
    .count(A7), .Q(C7), .clk(Clk), .clr(L7));  // open: load, D, carry, preset
  and and_2 (A0, or_1_out, V0);
  and and_3 (A4, or_2_out, V4);
  Multiplexer #(.select(2), .width(2), .disabled("Z"), .enable("false")) multiplexer_9 (
    .in0(multiplexer_1_out), .in1(multiplexer_2_out), .in2(multiplexer_3_out), .in3(multiplexer_4_out),
    .out(multiplexer_9_out), .sel(Predict0));
  Adder #(.width(2)) adder_1 (.a(Predict0), .b(multiplexer_9_out), .out(adder_1_out));  // open: cin, cout
  Adder #(.width(2)) adder_2 (.a(Predict4), .b(multiplexer_10_out), .out(adder_2_out));  // open: cin, cout
  Multiplexer #(.select(2), .width(2), .disabled("Z"), .enable("false")) multiplexer_10 (
    .in0(multiplexer_5_out), .in1(multiplexer_6_out), .in2(multiplexer_7_out), .in3(multiplexer_8_out),
    .out(multiplexer_10_out), .sel(Predict4));
  or or_3 (or_3_out, decoder_1_out0, decoder_2_out0);
  or or_4 (or_4_out, decoder_1_out1, decoder_2_out1);
  or or_5 (or_5_out, decoder_1_out2, decoder_2_out2);
  or or_6 (or_6_out, decoder_1_out3, decoder_2_out3);
  or or_7 (or_7_out, decoder_1_out4, decoder_2_out4);
  or or_8 (or_8_out, decoder_1_out5, decoder_2_out5);
  or or_9 (or_9_out, decoder_1_out6, decoder_2_out6);
  or or_10 (or_10_out, decoder_1_out7, decoder_2_out7);
  Register #(.width(2), .trigger("rising"), .Select("low")) \u_分支预测历史位  (
    .D(adder_1_out), .en(M0), .Q(Predict0), .clk(Clk));  // open: clr
  Register #(.width(2), .trigger("rising"), .Select("low")) \u_分支预测历史位_2  (
    .D(adder_2_out), .en(M4), .Q(Predict4), .clk(Clk));  // open: clr
  Register #(.width(32), .trigger("rising"), .Select("low")) \u_分支目标地址  (
    .D(EX_BranchAddr), .en(WriteL0), .Q(\分支目标地址_q ), .clk(Clk));  // open: clr
  assign JumpAddr = L0 ? \分支目标地址_q  : 32'bz;  // Controlled_Buffer controlled_buffer_9
  Register #(.width(32), .trigger("rising"), .Select("low")) \u_分支目标地址_2  (
    .D(EX_BranchAddr), .en(WriteL1), .Q(\分支目标地址_2_q ), .clk(Clk));  // open: clr
  assign JumpAddr = L1 ? \分支目标地址_2_q  : 32'bz;  // Controlled_Buffer controlled_buffer_10
  Register #(.width(32), .trigger("rising"), .Select("low")) \u_分支目标地址_3  (
    .D(EX_BranchAddr), .en(WriteL2), .Q(\分支目标地址_3_q ), .clk(Clk));  // open: clr
  assign JumpAddr = L2 ? \分支目标地址_3_q  : 32'bz;  // Controlled_Buffer controlled_buffer_11
  assign JumpAddr = L3 ? \分支目标地址_4_q  : 32'bz;  // Controlled_Buffer controlled_buffer_12
  Register #(.width(32), .trigger("rising"), .Select("low")) \u_分支目标地址_4  (
    .D(EX_BranchAddr), .en(WriteL3), .Q(\分支目标地址_4_q ), .clk(Clk));  // open: clr
  Register #(.width(32), .trigger("rising"), .Select("low")) \u_分支目标地址_5  (
    .D(EX_BranchAddr), .en(WriteL4), .Q(\分支目标地址_5_q ), .clk(Clk));  // open: clr
  assign JumpAddr = L4 ? \分支目标地址_5_q  : 32'bz;  // Controlled_Buffer controlled_buffer_13
  assign JumpAddr = L5 ? \分支目标地址_6_q  : 32'bz;  // Controlled_Buffer controlled_buffer_14
  Register #(.width(32), .trigger("rising"), .Select("low")) \u_分支目标地址_6  (
    .D(EX_BranchAddr), .en(WriteL5), .Q(\分支目标地址_6_q ), .clk(Clk));  // open: clr
  assign JumpAddr = L6 ? \分支目标地址_7_q  : 32'bz;  // Controlled_Buffer controlled_buffer_15
  Register #(.width(32), .trigger("rising"), .Select("low")) \u_分支目标地址_7  (
    .D(EX_BranchAddr), .en(WriteL6), .Q(\分支目标地址_7_q ), .clk(Clk));  // open: clr
  Register #(.width(32), .trigger("rising"), .Select("low")) \u_分支目标地址_8  (
    .D(EX_BranchAddr), .en(WriteL7), .Q(\分支目标地址_8_q ), .clk(Clk));  // open: clr
  assign JumpAddr = L7 ? \分支目标地址_8_q  : 32'bz;  // Controlled_Buffer controlled_buffer_16
  and and_4 (WriteL0, or_3_out, EX_Miss, EX_Branch);
  and and_5 (WriteL1, or_4_out, EX_Miss, EX_Branch);
  and and_6 (WriteL2, or_5_out, EX_Miss, EX_Branch);
  and and_7 (WriteL3, or_6_out, EX_Miss, EX_Branch);
  and and_8 (WriteL4, or_7_out, EX_Miss, EX_Branch);
  and and_9 (WriteL5, or_8_out, EX_Miss, EX_Branch);
  and and_10 (WriteL6, or_9_out, EX_Miss, EX_Branch);
  and and_11 (WriteL7, or_10_out, EX_Miss, EX_Branch);
  or or_11 (or_11_out, L0, L2, L3, L4, L5, L6, L7, WriteL0, WriteL2, WriteL3, WriteL4, WriteL5, WriteL6, WriteL7);
  or or_12 (or_12_out, L0, L1, L2, L3, L4, L6, L7, WriteL0, WriteL1, WriteL2, WriteL3, WriteL4, WriteL6, WriteL7);
  and and_12 (A1, or_11_out, V1);
  and and_13 (A5, or_12_out, V5);
  Multiplexer #(.select(1), .width(2), .disabled("Z"), .enable("false")) multiplexer_11 (
    .in0(2'b00), .in1(2'b01), .out(multiplexer_11_out), .sel(EX_Branched));
  Multiplexer #(.select(1), .width(2), .disabled("Z"), .enable("false")) multiplexer_12 (
    .in0(2'b11), .in1(2'b01), .out(multiplexer_12_out), .sel(EX_Branched));
  Multiplexer #(.select(1), .width(2), .disabled("Z"), .enable("false")) multiplexer_13 (
    .in0(2'b01), .in1(2'b00), .out(multiplexer_13_out), .sel(EX_Branched));
  Multiplexer #(.select(1), .width(2), .disabled("Z"), .enable("false")) multiplexer_14 (
    .in0(2'b01), .in1(2'b11), .out(multiplexer_14_out), .sel(EX_Branched));
  Multiplexer #(.select(1), .width(2), .disabled("Z"), .enable("false")) multiplexer_15 (
    .in0(2'b00), .in1(2'b01), .out(multiplexer_15_out), .sel(EX_Branched));
  Multiplexer #(.select(1), .width(2), .disabled("Z"), .enable("false")) multiplexer_16 (
    .in0(2'b11), .in1(2'b01), .out(multiplexer_16_out), .sel(EX_Branched));
  Multiplexer #(.select(1), .width(2), .disabled("Z"), .enable("false")) multiplexer_17 (
    .in0(2'b01), .in1(2'b00), .out(multiplexer_17_out), .sel(EX_Branched));
  Multiplexer #(.select(1), .width(2), .disabled("Z"), .enable("false")) multiplexer_18 (
    .in0(2'b01), .in1(2'b11), .out(multiplexer_18_out), .sel(EX_Branched));
  Multiplexer #(.select(2), .width(2), .disabled("Z"), .enable("false")) multiplexer_19 (
    .in0(multiplexer_11_out), .in1(multiplexer_12_out), .in2(multiplexer_13_out), .in3(multiplexer_14_out),
    .out(multiplexer_19_out), .sel(Predict1));
  Multiplexer #(.select(2), .width(2), .disabled("Z"), .enable("false")) multiplexer_20 (
    .in0(multiplexer_15_out), .in1(multiplexer_16_out), .in2(multiplexer_17_out), .in3(multiplexer_18_out),
    .out(multiplexer_20_out), .sel(Predict5));
  Comparator #(.width(32), .mode("twosComplement")) comparator_1 (
    .a(PC), .b(Tag0), .eq(comparator_1_eq));  // open: gt, lt
  Comparator #(.width(32), .mode("twosComplement")) comparator_2 (
    .a(PC), .b(Tag1), .eq(comparator_2_eq));  // open: gt, lt
  Comparator #(.width(32), .mode("twosComplement")) comparator_3 (
    .a(PC), .b(Tag2), .eq(comparator_3_eq));  // open: gt, lt
  Comparator #(.width(32), .mode("twosComplement")) comparator_4 (
    .a(PC), .b(Tag3), .eq(comparator_4_eq));  // open: gt, lt
  Comparator #(.width(32), .mode("twosComplement")) comparator_5 (
    .a(PC), .b(Tag4), .eq(comparator_5_eq));  // open: gt, lt
  Comparator #(.width(32), .mode("twosComplement")) comparator_6 (
    .a(PC), .b(Tag5), .eq(comparator_6_eq));  // open: gt, lt
  Comparator #(.width(32), .mode("twosComplement")) comparator_7 (
    .a(PC), .b(Tag6), .eq(comparator_7_eq));  // open: gt, lt
  Comparator #(.width(32), .mode("twosComplement")) comparator_8 (
    .a(PC), .b(Tag7), .eq(comparator_8_eq));  // open: gt, lt
  Comparator #(.width(32), .mode("twosComplement")) comparator_9 (
    .a(EX_PC), .b(Tag0), .eq(comparator_9_eq));  // open: gt, lt
  Comparator #(.width(32), .mode("twosComplement")) comparator_10 (
    .a(EX_PC), .b(Tag1), .eq(comparator_10_eq));  // open: gt, lt
  Comparator #(.width(32), .mode("twosComplement")) comparator_11 (
    .a(EX_PC), .b(Tag2), .eq(comparator_11_eq));  // open: gt, lt
  Comparator #(.width(32), .mode("twosComplement")) comparator_12 (
    .a(EX_PC), .b(Tag3), .eq(comparator_12_eq));  // open: gt, lt
  Comparator #(.width(32), .mode("twosComplement")) comparator_13 (
    .a(EX_PC), .b(Tag4), .eq(comparator_13_eq));  // open: gt, lt
  Comparator #(.width(32), .mode("twosComplement")) comparator_14 (
    .a(EX_PC), .b(Tag5), .eq(comparator_14_eq));  // open: gt, lt
  Comparator #(.width(32), .mode("twosComplement")) comparator_15 (
    .a(EX_PC), .b(Tag6), .eq(comparator_15_eq));  // open: gt, lt
  Comparator #(.width(32), .mode("twosComplement")) comparator_16 (
    .a(EX_PC), .b(Tag7), .eq(comparator_16_eq));  // open: gt, lt
  Adder #(.width(2)) adder_3 (.a(Predict1), .b(multiplexer_19_out), .out(adder_3_out));  // open: cin, cout
  Register #(.width(2), .trigger("rising"), .Select("low")) \u_分支预测历史位_3  (
    .D(adder_3_out), .en(M1), .Q(Predict1), .clk(Clk));  // open: clr
  Adder #(.width(2)) adder_4 (.a(Predict5), .b(multiplexer_20_out), .out(adder_4_out));  // open: cin, cout
  or or_13 (or_13_out, L0, L1, L3, L4, L5, L6, L7, WriteL0, WriteL1, WriteL3, WriteL4, WriteL5, WriteL6, WriteL7);
  or or_14 (or_14_out, L0, L1, L2, L3, L4, L5, L7, WriteL0, WriteL1, WriteL2, WriteL3, WriteL4, WriteL5, WriteL7);
  Register #(.width(2), .trigger("rising"), .Select("low")) \u_分支预测历史位_4  (
    .D(adder_4_out), .en(M5), .Q(Predict5), .clk(Clk));  // open: clr
  and and_14 (L0, comparator_1_eq, V0);
  and and_15 (L1, comparator_2_eq, V1);
  and and_16 (L2, comparator_3_eq, V2);
  and and_17 (L3, comparator_4_eq, V3);
  and and_18 (L4, comparator_5_eq, V4);
  and and_19 (L5, comparator_6_eq, V5);
  and and_20 (L6, comparator_7_eq, V6);
  and and_21 (L7, comparator_8_eq, V7);
  and and_22 (M0, comparator_9_eq, V0);
  and and_23 (M1, comparator_10_eq, V1);
  and and_24 (M2, comparator_11_eq, V2);
  and and_25 (M3, comparator_12_eq, V3);
  and and_26 (M4, comparator_13_eq, V4);
  and and_27 (M5, comparator_14_eq, V5);
  and and_28 (M6, comparator_15_eq, V6);
  and and_29 (M7, comparator_16_eq, V7);
  and and_30 (A2, or_13_out, V2);
  and and_31 (A6, or_14_out, V6);
  or or_15 (IF_Hit, L0, L1, L2, L3, L4, L5, L6, L7);
  or or_16 (EX_Hit, M0, M1, M2, M3, M4, M5, M6, M7);
  Multiplexer #(.select(1), .width(2), .disabled("Z"), .enable("false")) multiplexer_21 (
    .in0(2'b00), .in1(2'b01), .out(multiplexer_21_out), .sel(EX_Branched));
  Multiplexer #(.select(1), .width(2), .disabled("Z"), .enable("false")) multiplexer_22 (
    .in0(2'b11), .in1(2'b01), .out(multiplexer_22_out), .sel(EX_Branched));
  Multiplexer #(.select(1), .width(2), .disabled("Z"), .enable("false")) multiplexer_23 (
    .in0(2'b01), .in1(2'b00), .out(multiplexer_23_out), .sel(EX_Branched));
  Multiplexer #(.select(1), .width(2), .disabled("Z"), .enable("false")) multiplexer_24 (
    .in0(2'b01), .in1(2'b11), .out(multiplexer_24_out), .sel(EX_Branched));
  Multiplexer #(.select(1), .width(2), .disabled("Z"), .enable("false")) multiplexer_25 (
    .in0(2'b00), .in1(2'b01), .out(multiplexer_25_out), .sel(EX_Branched));
  Multiplexer #(.select(1), .width(2), .disabled("Z"), .enable("false")) multiplexer_26 (
    .in0(2'b11), .in1(2'b01), .out(multiplexer_26_out), .sel(EX_Branched));
  Multiplexer #(.select(1), .width(2), .disabled("Z"), .enable("false")) multiplexer_27 (
    .in0(2'b01), .in1(2'b00), .out(multiplexer_27_out), .sel(EX_Branched));
  Multiplexer #(.select(1), .width(2), .disabled("Z"), .enable("false")) multiplexer_28 (
    .in0(2'b01), .in1(2'b11), .out(multiplexer_28_out), .sel(EX_Branched));
  not not_9 (IF_Miss, IF_Hit);
  not not_10 (EX_Miss, EX_Hit);
  Adder #(.width(2)) adder_5 (.a(Predict2), .b(multiplexer_29_out), .out(adder_5_out));  // open: cin, cout
  Multiplexer #(.select(2), .width(2), .disabled("Z"), .enable("false")) multiplexer_29 (
    .in0(multiplexer_21_out), .in1(multiplexer_22_out), .in2(multiplexer_23_out), .in3(multiplexer_24_out),
    .out(multiplexer_29_out), .sel(Predict2));
  Multiplexer #(.select(2), .width(2), .disabled("Z"), .enable("false")) multiplexer_30 (
    .in0(multiplexer_25_out), .in1(multiplexer_26_out), .in2(multiplexer_27_out), .in3(multiplexer_28_out),
    .out(multiplexer_30_out), .sel(Predict6));
  or or_17 (or_17_out, L0, L1, L2, L4, L5, L6, L7, WriteL0, WriteL1, WriteL2, WriteL4, WriteL5, WriteL6, WriteL7);
  or or_18 (or_18_out, L0, L1, L2, L3, L4, L5, L6, WriteL0, WriteL1, WriteL2, WriteL3, WriteL4, WriteL5, WriteL6);
  Register #(.width(2), .trigger("rising"), .Select("low")) \u_分支预测历史位_5  (
    .D(adder_5_out), .en(M2), .Q(Predict2), .clk(Clk));  // open: clr
  Adder #(.width(2)) adder_6 (.a(Predict6), .b(multiplexer_30_out), .out(adder_6_out));  // open: cin, cout
  Register #(.width(2), .trigger("rising"), .Select("low")) \u_分支预测历史位_6  (
    .D(adder_6_out), .en(M6), .Q(Predict6), .clk(Clk));  // open: clr
  and and_32 (A3, or_17_out, V3);
  and and_33 (A7, or_18_out, V7);
  Multiplexer #(.select(1), .width(2), .disabled("Z"), .enable("false")) multiplexer_31 (
    .in0(2'b00), .in1(2'b01), .out(multiplexer_31_out), .sel(EX_Branched));
  Multiplexer #(.select(1), .width(2), .disabled("Z"), .enable("false")) multiplexer_32 (
    .in0(2'b11), .in1(2'b01), .out(multiplexer_32_out), .sel(EX_Branched));
  Multiplexer #(.select(1), .width(2), .disabled("Z"), .enable("false")) multiplexer_33 (
    .in0(2'b01), .in1(2'b00), .out(multiplexer_33_out), .sel(EX_Branched));
  Multiplexer #(.select(1), .width(2), .disabled("Z"), .enable("false")) multiplexer_34 (
    .in0(2'b01), .in1(2'b11), .out(multiplexer_34_out), .sel(EX_Branched));
  Multiplexer #(.select(1), .width(2), .disabled("Z"), .enable("false")) multiplexer_35 (
    .in0(2'b00), .in1(2'b01), .out(multiplexer_35_out), .sel(EX_Branched));
  Multiplexer #(.select(1), .width(2), .disabled("Z"), .enable("false")) multiplexer_36 (
    .in0(2'b11), .in1(2'b01), .out(multiplexer_36_out), .sel(EX_Branched));
  Multiplexer #(.select(1), .width(2), .disabled("Z"), .enable("false")) multiplexer_37 (
    .in0(2'b01), .in1(2'b00), .out(multiplexer_37_out), .sel(EX_Branched));
  Multiplexer #(.select(1), .width(2), .disabled("Z"), .enable("false")) multiplexer_38 (
    .in0(2'b01), .in1(2'b11), .out(multiplexer_38_out), .sel(EX_Branched));
  Multiplexer #(.select(2), .width(2), .disabled("Z"), .enable("false")) multiplexer_39 (
    .in0(multiplexer_31_out), .in1(multiplexer_32_out), .in2(multiplexer_33_out), .in3(multiplexer_34_out),
    .out(multiplexer_39_out), .sel(Predict3));
  Multiplexer #(.select(2), .width(2), .disabled("Z"), .enable("false")) multiplexer_40 (
    .in0(multiplexer_35_out), .in1(multiplexer_36_out), .in2(multiplexer_37_out), .in3(multiplexer_38_out),
    .out(multiplexer_40_out), .sel(Predict7));
  Adder #(.width(2)) adder_7 (.a(Predict3), .b(multiplexer_39_out), .out(adder_7_out));  // open: cin, cout
  Adder #(.width(2)) adder_8 (.a(Predict7), .b(multiplexer_40_out), .out(adder_8_out));  // open: cin, cout
  Register #(.width(2), .trigger("rising"), .Select("low")) \u_分支预测历史位_7  (
    .D(adder_7_out), .en(M3), .Q(Predict3), .clk(Clk));  // open: clr
  Register #(.width(2), .trigger("rising"), .Select("low")) \u_分支预测历史位_8  (
    .D(adder_8_out), .en(M7), .Q(Predict7), .clk(Clk));  // open: clr

  // Other names for the same wires on the sheet: Tag[31:0] = EX_PC

  // Notes on the sheet:
  //   Cache槽
  //   读缺失逻辑/块载入逻辑
  //   查找逻辑
endmodule
